// Logisim project cpu24-version-1.8.circ as structural Verilog: 24 circuits, main circuit ◇单周期MIPS
module \单周期MIPS  (
  input  IR1,
  input  IR2,
  input  IR3,
  output RegWrite,
  output MemWrite,
  output [31:0] PC,
  output [31:0] IR,
  output [31:0] RDin,
  output [31:0] MDin,
  output [31:0] LedData
);

  wire and_1_out, and_2_out, BEQ, BGEZ, BGEZ_YES, BNE, CLK, clock_2_out, comparator_1_eq, comparator_2_eq,
       comparator_2_lt, d_ff_1_q, equal, Go, halt, IR1_t, IR2_t, IR3_t, IRA, IRB, IRC, JAL, JMP, JMP_IF, JR,
       LED, nand_1_out, not_1_out, not_2_out, not_3_out, not_4_out, or_1_out, RegDst, RST, SB, SignedExt,
       syscall, W1, W2, W3, \单周期硬布线控制器_1_memtoreg ;
  wire [1:1] \单周期硬布线控制器_1_alu_src ;
  wire [3:0] \单周期硬布线控制器_1_alu_op ;
  wire [4:0] multiplexer_3_out, multiplexer_4_out, multiplexer_5_out, multiplexer_6_out;
  wire [12:0] CNT_num;
  wire [15:0] \总周期数 ;
  wire [31:0] A0, bit_extender_1_out, bit_extender_2_out, mips_alu_1_result, MOUT, multiplexer_1_out,
       multiplexer_2_out, multiplexer_8_out, multiplexer_10_out, multiplexer_11_out, PC_4, PC_imm, PC_JR,
       shifter_1_out, shifter_2_out;

  Clock #(.highDuration(1), .lowDuration(1)) clock_1 ();  // open: out
  Button _1 (.out(IRA));
  Button _2 (.out(IRB));
  Button _3 (.out(IRC));
  Button \u_继续运行  (.out(Go));
  LED #(.active("true")) led_1 (.in(W1));
  LED #(.active("true")) led_2 (.in(W2));
  LED #(.active("true")) led_3 (.in(W3));
  Hex_Digit_Display hex_digit_display_1 (.value(LedData[31:28]));  // open: dp
  Adder #(.width(32)) adder_1 (.a(PC), .b(32'h4), .out(PC_4));  // open: cin, cout
  Register #(.width(32), .trigger("rising"), .Select("low")) register_1 (
    .D(A0), .en(LED), .Q(LedData), .clk(CLK), .clr(RST));
  Hex_Digit_Display hex_digit_display_2 (.value(LedData[27:24]));  // open: dp
  Hex_Digit_Display hex_digit_display_3 (.value(LedData[23:20]));  // open: dp
  Hex_Digit_Display hex_digit_display_4 (.value(LedData[15:12]));  // open: dp
  Hex_Digit_Display hex_digit_display_5 (.value(LedData[19:16]));  // open: dp
  Multiplexer #(.select(3), .width(32), .disabled("Z"), .enable("false")) multiplexer_1 (
    .in0(PC_4), .in1(PC_imm), .in2({PC_4[31:28], IR[25:0], 2'b00}), .in6(PC_JR), .out(multiplexer_1_out),
    .sel({JR, JMP, JMP_IF}));  // open: in3, in4, in5, in7
  Hex_Digit_Display hex_digit_display_6 (.value(LedData[7:4]));  // open: dp
  Hex_Digit_Display hex_digit_display_7 (.value(LedData[11:8]));  // open: dp
  // Probe on \总周期数 
  not not_1 (not_1_out, equal);
  Comparator #(.width(32), .mode("twosComplement")) comparator_1 (
    .a(PC_JR), .b(32'h22), .eq(comparator_1_eq));  // open: gt, lt
  Multiplexer #(.select(2), .width(32), .disabled("Z"), .enable("false")) multiplexer_2 (
    .in0(multiplexer_1_out), .in1(multiplexer_1_out), .in2(PC_4), .in3(PC_imm), .out(multiplexer_2_out),
    .sel({BGEZ, BGEZ_YES}));
  Hex_Digit_Display hex_digit_display_8 (.value(LedData[3:0]));  // open: dp
  and and_1 (and_1_out, BEQ, equal);
  and and_2 (and_2_out, BNE, not_1_out);
  not not_2 (not_2_out, comparator_1_eq);
  Register #(.width(32), .trigger("rising"), .Select("low")) u_PC (
    .D(multiplexer_2_out), .en(or_1_out), .Q(PC), .clk(CLK), .clr(RST));
  or or_1 (or_1_out, not_3_out, Go);
  not not_3 (not_3_out, halt);
  or or_2 (JMP_IF, and_1_out, and_2_out);
  and and_3 (LED, syscall, comparator_1_eq);
  and and_4 (halt, syscall, not_2_out);
  or or_3 (IR1_t, IR1, IRA);
  or or_4 (IR2_t, IR2, IRB);
  Button u_RST (.out(RST));
  not not_4 (not_4_out, halt);
  Counter #(.width(16), .max('hffff), .ongoal("wrap"), .trigger("rising"), .behavior("new")) counter_1 (
    .count(not_4_out), .Q(\总周期数 ), .clk(CLK), .clr(RST));  // open: load, D, carry, preset, down
  // Mips_Probe mips_probe_1: pin names not known; wires that end beside it: IR
  ROM #(.addrWidth(10), .dataWidth(32), .Select("high")) rom_1 (.addr(PC[11:2]), .data(IR));
  or or_5 (IR3_t, IR3, IRC);
  Multiplexer #(.select(1), .width(5), .disabled("Z"), .enable("false")) multiplexer_3 (
    .in0(IR[20:16]), .in1(IR[15:11]), .out(multiplexer_3_out), .sel(RegDst));
  \单周期硬布线控制器  \u_单周期硬布线控制器_1  (
    .Func(IR[5:0]), .OP(IR[31:26]), .ALU_OP(\单周期硬布线控制器_1_alu_op ), .MemToReg(\单周期硬布线控制器_1_memtoreg ),
    .MemWrite(MemWrite), .ALU_SRC(\单周期硬布线控制器_1_alu_src [1]), .RegWrite(RegWrite), .SysCALL(syscall),
    .SignedExt(SignedExt), .RegDst(RegDst), .JR(JR), .JMP(JMP), .Beq(BEQ), .JAL(JAL), .Bne(BNE), .BGEZ(BGEZ),
    .SB(SB));  // open: ERET
  Multiplexer #(.select(1), .width(5), .disabled("Z"), .enable("false")) multiplexer_4 (
    .in0(IR[25:21]), .in1(5'b00010), .out(multiplexer_4_out), .sel(syscall));
  Multiplexer #(.select(1), .width(5), .disabled("Z"), .enable("false")) multiplexer_5 (
    .in0(IR[20:16]), .in1(5'b00100), .out(multiplexer_5_out), .sel(syscall));
  Multiplexer #(.select(1), .width(5), .disabled("Z"), .enable("false")) multiplexer_6 (
    .in0(multiplexer_3_out), .in1({5{1'b1}}), .out(multiplexer_6_out), .sel(JAL));
  Shifter #(.width(32), .shift("ll")) shifter_1 (.in(MOUT), .\dist (5'b01000), .out(shifter_1_out));
  Multiplexer #(.select(1), .width(32), .disabled("Z"), .enable("false")) multiplexer_7 (
    .in0(multiplexer_11_out), .in1(PC_4), .out(RDin), .sel(JAL));
  MIPS_Regifile mips_regifile_1 (
    .Din(RDin), .Clk(CLK), .R1(PC_JR), .R2(A0), .WE(RegWrite), .W_num(multiplexer_6_out),
    .R1_num(multiplexer_4_out), .R2_num(multiplexer_5_out));
  assign bit_extender_1_out = {{16{1'b0}}, IR[15:0]};  // Bit_Extender bit_extender_1
  assign bit_extender_2_out = {{16{IR[15]}}, IR[15:0]};  // Bit_Extender bit_extender_2
  Shifter #(.width(32), .shift("ll")) shifter_2 (.in(bit_extender_2_out), .\dist (5'b00010), .out(shifter_2_out));
  Multiplexer #(.select(2), .width(32), .disabled("Z"), .enable("false")) multiplexer_8 (
    .in0(A0), .in1(A0), .in2(bit_extender_1_out), .in3(bit_extender_2_out), .out(multiplexer_8_out),
    .sel({\单周期硬布线控制器_1_alu_src [1], SignedExt}));
  Adder #(.width(32)) adder_2 (.a(shifter_2_out), .b(PC_4), .out(PC_imm));  // open: cin, cout
  Multiplexer #(.select(1), .width(32), .disabled("Z"), .enable("false")) multiplexer_9 (
    .in0(A0), .in1({shifter_1_out[31:8], A0[7:0]}), .out(MDin), .sel(SB));
  D_Flip_Flop #(.trigger("high"), .Pre_Clr_Positions("LEGACY"), .NegatePresetClear("false"), .enable("true"), .NewFFLayout("false")) d_ff_1 (.Q(d_ff_1_q));  // open: clk, D, Qn, preset, en, reset
  // Probe on 13'hc
  Multiplexer #(.select(1), .width(32), .disabled("Z"), .enable("false")) multiplexer_10 (
    .in0(multiplexer_8_out), .in1({32{1'b0}}), .out(multiplexer_10_out), .sel(BGEZ));
  Clock #(.highDuration(1), .lowDuration(1)) clock_2 (.out(clock_2_out));
  MIPS_ALU mips_alu_1 (
    .X(PC_JR), .Y(multiplexer_10_out), .AluOP(\单周期硬布线控制器_1_alu_op ), .Equal(equal),
    .Result(mips_alu_1_result), .shamt(IR[10:6]));  // open: Result_2
  Comparator #(.width(13), .mode("twosComplement")) comparator_2 (
    .a(CNT_num), .b(13'hc), .eq(comparator_2_eq), .lt(comparator_2_lt));  // open: gt
  not not_5 (BGEZ_YES, mips_alu_1_result[0]);
  nand nand_1 (nand_1_out, d_ff_1_q, comparator_2_eq);
  Counter #(.width(13), .max('h1fff), .ongoal("stay"), .trigger("rising"), .behavior("old")) counter_2 (
    .count(comparator_2_lt), .Q(CNT_num), .clk(clock_2_out));  // open: load, D, carry, clr, preset
  assign CLK = nand_1_out ? clock_2_out : 1'bz;  // Controlled_Buffer controlled_buffer_1
  Pull_Resistor #(.pull(1)) pull_resistor_1 (.node(CLK));
  RAM #(.addrWidth(10), .dataWidth(32), .bus("separate"), .Select("high")) ram_1 (
    .addr(mips_alu_1_result[11:2]), .din(MDin), .data(MOUT), .str(MemWrite), .clk(CLK), .clr(RST));  // open: sel, ld
  Multiplexer #(.select(1), .width(32), .disabled("Z"), .enable("false")) multiplexer_11 (
    .in0(mips_alu_1_result), .in1(MOUT), .out(multiplexer_11_out), .sel(\单周期硬布线控制器_1_memtoreg ));

  // Other names for the same wires on the sheet: addr[25:0] = IR[25:0]; imm[15:0] = IR[15:0];
  //   PC_J[31:2] = {PC_4[31:28], IR[25:0]}; shamt[4:0] = IR[10:6]; rd[4:0] = IR[15:11]; V0[31:0] = PC_JR

  // Notes on the sheet:
  //   中断源
  //   中断等待指示
  //   总复位信号应将除ROM以外所有存储组件全部清零
  //   数码管输出
  //   数码管输出应该用寄存器锁存，否则显示数据只能一闪而过
  //   指令存储器
  //   指令字
  //   contents of rom_1 (hex, n*v repeats v):
  //   201d07d0 20100001 109fc0 139fc3 8021 2012000c 24160008 26100001 3210000f 20080008 20090001 139900
  //   2709825 132020 20020022 c 1094022 1500fff9 22100001 2018000f 2188024 108700 20080008 20090001 139902
  //   2709825 132021 20020022 c 1094022 1500fff9 108702 2c9b022 12c00001 8000c07 4020 1084027 84400
  //   3508ffff 82021 20020022 c 8000c01 afa20000 23bd0004 afa40000 23bd0004 afb00000 23bd0004 afb30000
  //   23bd0004 afb40000 23bd0004 afb50000 23bd0004 afb60000 23bd0004 20160001 20140003 20150001 168020
  //   108100 2149825 132020 20020022 c 1600fffa 295a022 1680fff7 23bdfffc 8fb60000 23bdfffc 8fb50000
  //   23bdfffc 8fb40000 23bdfffc 8fb30000 23bdfffc 8fb00000 23bdfffc 8fa40000 23bdfffc 8fa20000 42000018
  //   afa20000 23bd0004 afa40000 23bd0004 afb00000 23bd0004 afb30000 23bd0004 afb40000 23bd0004 afb50000
  //   23bd0004 afb60000 23bd0004 20160002 20140003 20150001 168020 108100 2149825 132020 20020022 c
  //   1600fffa 295a022 1680fff7 23bdfffc 8fb60000 23bdfffc 8fb50000 23bdfffc 8fb40000 23bdfffc 8fb30000
  //   23bdfffc 8fb00000 23bdfffc 8fa40000 23bdfffc 8fa20000 42000018 afa20000 23bd0004 afa40000 23bd0004
  //   afb00000 23bd0004 afb30000 23bd0004 afb40000 23bd0004 afb50000 23bd0004 afb60000 23bd0004 20160003
  //   20140003 20150001 168020 108100 2149825 132020 20020022 c 1600fffa 295a022 1680fff7 23bdfffc
  //   8fb60000 23bdfffc 8fb50000 23bdfffc 8fb40000 23bdfffc 8fb30000 23bdfffc 8fb00000 23bdfffc 8fa40000
  //   23bdfffc 8fa20000 42000018
  //   OP
  //   Func
  //   rs
  //   rt
  //   rd
  //   JMP
  //   JR
  //   OP
  //   Func
  //   Beq
  //   Bne
  //   MemToReg
  //   MemWrite
  //   AluOP
  //   AluSrcB
  //   RegWrite
  //   JAL
  //   RegDst
  //   Syscall
  //   为方便自动评测，需要输出PC，IR，寄存器堆写如数据RDin
  //   RAM写使能MemWrite、RAM写入数据MDin等信号
  //   控制位
  //   暂停节拍，不能为0
  //   戳工具置1进入计数暂停模式，ctrl+k时钟自动运行到对应节拍暂停
  //   ctrl+k关闭时钟连续运行，将控制位置零，进入单步调试模式调试
  //   用这个时钟源需要去掉电路中的其他时钟源
  //   可计数暂停的时钟源
endmodule

// 单周期硬布线控制器
module \单周期硬布线控制器  (
  input  [5:0] OP,
  input  [5:0] Func,
  output [3:0] ALU_OP,
  output MemToReg,
  output MemWrite,
  output BGEZ,
  output SB,
  output ALU_SRC,
  output RegWrite,
  output SysCALL,
  output SignedExt,
  output RegDst,
  output Beq,
  output Bne,
  output JR,
  output JMP,
  output JAL,
  output ERET
);

  \运算控制器自动生成  \u_运算控制器自动生成_1  (
    .OP0(OP[0]), .OP1(OP[1]), .OP2(OP[2]), .OP3(OP[3]), .OP4(OP[4]), .OP5(OP[5]), .F0(Func[0]), .F1(Func[1]),
    .F2(Func[2]), .F3(Func[3]), .F4(Func[4]), .F5(Func[5]), .S0(ALU_OP[0]), .S1(ALU_OP[1]), .S2(ALU_OP[2]),
    .S3(ALU_OP[3]));
  \控制信号自动生成  \u_控制信号自动生成_1  (
    .OP0(OP[0]), .MemToReg(MemToReg), .OP1(OP[1]), .OP2(OP[2]), .OP3(OP[3]), .OP4(OP[4]),
    .MemWrite(MemWrite), .OP5(OP[5]), .F0(Func[0]), .F1(Func[1]), .BGEZ(BGEZ), .F2(Func[2]), .F3(Func[3]),
    .F4(Func[4]), .SB(SB), .F5(Func[5]), .ALU_SRC(ALU_SRC), .RegWrite(RegWrite), .SysCALL(SysCALL),
    .SignedExt(SignedExt), .RegDst(RegDst), .BEQ(Beq), .BNE(Bne), .JR(JR), .JUMP(JMP), .JAL(JAL), .ERET(ERET));

  // Other names for the same wires on the sheet: OP_CODE[5:0] = OP

  // Notes on the sheet:
  //   运算器控制器，根据指令生成运算器功能选择信号
  //   控制信号生成，产生数据通路需要的其他控制信号
endmodule

// 运算器控制器
module \运算控制器自动生成  (
  input  OP0,
  input  OP1,
  input  OP2,
  input  OP3,
  input  OP4,
  input  OP5,
  input  F0,
  input  F1,
  input  F2,
  input  F3,
  input  F4,
  input  F5,
  output S0,
  output S1,
  output S2,
  output S3
);

  wire and_1_out, and_2_out, and_3_out, and_4_out, and_5_out, and_6_out, and_7_out, and_8_out, and_9_out,
       and_10_out, and_11_out, and_12_out, and_13_out, and_14_out, and_15_out, and_16_out, and_17_out,
       and_18_out, and_19_out, and_20_out, and_21_out, and_22_out, and_23_out, and_24_out, and_25_out,
       and_26_out, and_27_out, and_28_out, and_29_out, and_30_out, and_31_out, and_32_out, and_33_out,
       and_34_out, and_35_out, and_36_out, and_37_out, and_38_out, and_39_out, and_40_out, and_41_out,
       and_42_out, and_43_out, not_1_out, not_2_out, not_3_out, not_4_out, not_5_out, not_6_out, not_7_out,
       not_8_out, not_9_out, not_10_out, not_11_out, not_12_out, not_13_out, not_14_out, not_15_out,
       not_16_out, not_17_out, not_18_out, not_19_out, not_20_out, not_21_out, not_22_out, not_23_out,
       not_24_out, not_25_out, not_26_out, not_27_out, not_28_out, not_29_out, not_30_out, not_31_out,
       not_32_out, not_33_out, not_34_out, not_35_out, not_36_out, not_37_out, not_38_out, not_39_out,
       not_40_out, not_41_out, not_42_out, not_43_out, not_44_out, not_45_out, not_46_out, not_47_out,
       not_48_out, not_49_out, not_50_out, not_51_out, not_52_out, not_53_out, not_54_out, not_55_out,
       not_56_out, not_57_out, not_58_out, not_59_out, not_60_out, not_61_out, not_62_out, not_63_out,
       not_64_out, not_65_out, not_66_out, not_67_out, not_68_out, not_69_out, not_70_out, not_71_out,
       not_72_out, not_73_out, not_74_out, not_75_out, not_76_out, not_77_out, not_78_out, not_79_out,
       not_80_out, not_81_out, not_82_out, not_83_out, not_84_out, not_85_out, not_86_out, not_87_out,
       not_88_out, not_89_out, not_90_out, not_91_out, not_92_out, not_93_out, not_94_out, not_95_out,
       not_96_out, not_97_out, not_98_out, not_99_out, not_100_out, not_101_out, not_102_out, not_103_out,
       not_104_out, not_105_out, not_106_out, not_107_out, not_108_out, not_109_out, not_110_out,
       not_111_out, not_112_out, not_113_out, not_114_out, not_115_out, not_116_out, not_117_out,
       not_118_out, not_119_out, not_120_out, not_121_out, not_122_out, not_123_out, not_124_out,
       not_125_out, not_126_out, not_127_out, not_128_out, not_129_out, not_130_out, not_131_out,
       not_132_out, not_133_out, not_134_out, not_135_out, not_136_out, not_137_out, not_138_out,
       not_139_out, not_140_out, not_141_out, not_142_out, not_143_out, not_144_out, not_145_out,
       not_146_out, not_147_out, not_148_out, not_149_out, not_150_out, not_151_out, not_152_out,
       not_153_out, not_154_out, not_155_out, not_156_out, not_157_out, not_158_out, not_159_out,
       not_160_out, not_161_out, not_162_out, not_163_out, not_164_out, not_165_out, not_166_out,
       not_167_out, not_168_out, not_169_out, not_170_out, not_171_out, not_172_out, not_173_out,
       not_174_out, not_175_out, not_176_out, not_177_out, not_178_out, not_179_out, not_180_out,
       not_181_out, not_182_out, not_183_out, not_184_out, not_185_out, not_186_out, not_187_out,
       not_188_out, not_189_out, not_190_out, not_191_out, not_192_out, not_193_out, not_194_out,
       not_195_out, not_196_out, not_197_out, not_198_out, not_199_out, not_200_out, not_201_out,
       not_202_out, not_203_out, not_204_out, not_205_out, not_206_out, not_207_out, not_208_out,
       not_209_out, not_210_out, not_211_out, not_212_out, not_213_out, not_214_out, not_215_out,
       not_216_out, not_217_out, not_218_out, not_219_out, not_220_out, not_221_out, not_222_out,
       not_223_out, not_224_out, not_225_out, not_226_out, not_227_out, not_228_out, not_229_out,
       not_230_out, not_231_out, not_232_out, not_233_out, not_234_out, not_235_out, not_236_out,
       not_237_out, not_238_out, not_239_out, not_240_out, not_241_out, not_242_out, not_243_out,
       not_244_out, not_245_out, not_246_out, not_247_out, not_248_out, not_249_out, not_250_out,
       not_251_out, not_252_out, not_253_out, not_254_out, not_255_out, not_256_out, not_257_out,
       not_258_out, not_259_out, not_260_out, not_261_out, not_262_out, not_263_out, not_264_out,
       not_265_out, not_266_out, not_267_out, not_268_out, not_269_out, not_270_out, not_271_out,
       not_272_out, not_273_out, not_274_out, not_275_out, not_276_out, not_277_out, not_278_out,
       not_279_out, not_280_out, not_281_out, not_282_out, not_283_out, not_284_out, not_285_out,
       not_286_out, not_287_out, not_288_out, not_289_out, not_290_out, not_291_out, not_292_out,
       not_293_out, not_294_out, not_295_out;

  not not_1 (not_1_out, OP5);
  not not_2 (not_2_out, OP4);
  not not_3 (not_3_out, OP3);
  not not_4 (not_4_out, OP2);
  not not_5 (not_5_out, OP1);
  not not_6 (not_6_out, OP0);
  not not_7 (not_7_out, F5);
  not not_8 (not_8_out, F4);
  not not_9 (not_9_out, F3);
  not not_10 (not_10_out, F2);
  not not_11 (not_11_out, OP5);
  not not_12 (not_12_out, OP4);
  not not_13 (not_13_out, OP3);
  not not_14 (not_14_out, OP2);
  not not_15 (not_15_out, OP1);
  not not_16 (not_16_out, OP0);
  not not_17 (not_17_out, F4);
  not not_18 (not_18_out, F3);
  not not_19 (not_19_out, F2);
  not not_20 (not_20_out, F1);
  not not_21 (not_21_out, F0);
  not not_22 (not_22_out, OP5);
  not not_23 (not_23_out, OP4);
  not not_24 (not_24_out, OP3);
  not not_25 (not_25_out, OP2);
  not not_26 (not_26_out, OP1);
  not not_27 (not_27_out, OP0);
  not not_28 (not_28_out, F4);
  not not_29 (not_29_out, F3);
  not not_30 (not_30_out, F2);
  not not_31 (not_31_out, F1);
  not not_32 (not_32_out, OP5);
  not not_33 (not_33_out, OP4);
  not not_34 (not_34_out, OP3);
  not not_35 (not_35_out, OP2);
  not not_36 (not_36_out, OP1);
  not not_37 (not_37_out, OP0);
  not not_38 (not_38_out, F4);
  not not_39 (not_39_out, F3);
  not not_40 (not_40_out, F1);
  not not_41 (not_41_out, F0);
  not not_42 (not_42_out, OP5);
  not not_43 (not_43_out, OP4);
  not not_44 (not_44_out, OP3);
  not not_45 (not_45_out, OP2);
  not not_46 (not_46_out, OP1);
  not not_47 (not_47_out, OP0);
  not not_48 (not_48_out, F4);
  not not_49 (not_49_out, F2);
  not not_50 (not_50_out, F0);
  not not_51 (not_51_out, OP5);
  not not_52 (not_52_out, OP4);
  not not_53 (not_53_out, OP2);
  not not_54 (not_54_out, OP1);
  not not_55 (not_55_out, OP0);
  not not_56 (not_56_out, OP5);
  not not_57 (not_57_out, OP4);
  not not_58 (not_58_out, OP1);
  not not_59 (not_59_out, OP0);
  not not_60 (not_60_out, OP5);
  not not_61 (not_61_out, OP4);
  not not_62 (not_62_out, OP2);
  not not_63 (not_63_out, OP1);
  not not_64 (not_64_out, OP5);
  not not_65 (not_65_out, OP4);
  not not_66 (not_66_out, OP2);
  not not_67 (not_67_out, OP0);
  not not_68 (not_68_out, OP4);
  not not_69 (not_69_out, OP3);
  not not_70 (not_70_out, OP2);
  not not_71 (not_71_out, OP4);
  not not_72 (not_72_out, OP2);
  not not_73 (not_73_out, OP5);
  not not_74 (not_74_out, OP4);
  not not_75 (not_75_out, OP3);
  not not_76 (not_76_out, OP2);
  not not_77 (not_77_out, OP1);
  not not_78 (not_78_out, OP0);
  not not_79 (not_79_out, F4);
  not not_80 (not_80_out, F3);
  not not_81 (not_81_out, F0);
  not not_82 (not_82_out, OP4);
  not not_83 (not_83_out, OP2);
  not not_84 (not_84_out, OP1);
  not not_85 (not_85_out, OP0);
  not not_86 (not_86_out, OP5);
  not not_87 (not_87_out, OP4);
  not not_88 (not_88_out, OP3);
  not not_89 (not_89_out, OP2);
  not not_90 (not_90_out, OP1);
  not not_91 (not_91_out, OP5);
  not not_92 (not_92_out, OP4);
  not not_93 (not_93_out, OP3);
  not not_94 (not_94_out, OP2);
  not not_95 (not_95_out, OP1);
  not not_96 (not_96_out, OP0);
  not not_97 (not_97_out, F5);
  not not_98 (not_98_out, F4);
  not not_99 (not_99_out, F3);
  not not_100 (not_100_out, F2);
  not not_101 (not_101_out, F0);
  not not_102 (not_102_out, OP5);
  not not_103 (not_103_out, OP4);
  not not_104 (not_104_out, OP3);
  not not_105 (not_105_out, OP2);
  not not_106 (not_106_out, OP1);
  not not_107 (not_107_out, OP0);
  not not_108 (not_108_out, F4);
  not not_109 (not_109_out, F3);
  not not_110 (not_110_out, F2);
  not not_111 (not_111_out, F0);
  not not_112 (not_112_out, OP5);
  not not_113 (not_113_out, OP4);
  not not_114 (not_114_out, OP3);
  not not_115 (not_115_out, OP2);
  not not_116 (not_116_out, OP1);
  not not_117 (not_117_out, OP0);
  not not_118 (not_118_out, F4);
  not not_119 (not_119_out, F3);
  not not_120 (not_120_out, F1);
  not not_121 (not_121_out, F0);
  not not_122 (not_122_out, OP5);
  not not_123 (not_123_out, OP4);
  not not_124 (not_124_out, OP3);
  not not_125 (not_125_out, OP2);
  not not_126 (not_126_out, OP1);
  not not_127 (not_127_out, OP0);
  not not_128 (not_128_out, F4);
  not not_129 (not_129_out, F3);
  not not_130 (not_130_out, OP5);
  not not_131 (not_131_out, OP4);
  not not_132 (not_132_out, OP3);
  not not_133 (not_133_out, OP2);
  not not_134 (not_134_out, OP1);
  not not_135 (not_135_out, OP0);
  not not_136 (not_136_out, F4);
  not not_137 (not_137_out, F2);
  not not_138 (not_138_out, F0);
  not not_139 (not_139_out, OP5);
  not not_140 (not_140_out, OP4);
  not not_141 (not_141_out, OP1);
  not not_142 (not_142_out, OP0);
  not not_143 (not_143_out, OP5);
  not not_144 (not_144_out, OP4);
  not not_145 (not_145_out, OP2);
  not not_146 (not_146_out, OP0);
  not not_147 (not_147_out, OP5);
  not not_148 (not_148_out, OP4);
  not not_149 (not_149_out, OP3);
  not not_150 (not_150_out, OP2);
  not not_151 (not_151_out, OP1);
  not not_152 (not_152_out, OP0);
  not not_153 (not_153_out, F4);
  not not_154 (not_154_out, F3);
  not not_155 (not_155_out, F2);
  not not_156 (not_156_out, OP5);
  not not_157 (not_157_out, OP4);
  not not_158 (not_158_out, OP3);
  not not_159 (not_159_out, OP2);
  not not_160 (not_160_out, OP1);
  not not_161 (not_161_out, OP5);
  not not_162 (not_162_out, OP4);
  not not_163 (not_163_out, OP3);
  not not_164 (not_164_out, OP2);
  not not_165 (not_165_out, OP1);
  not not_166 (not_166_out, OP0);
  not not_167 (not_167_out, F4);
  not not_168 (not_168_out, F3);
  not not_169 (not_169_out, F2);
  not not_170 (not_170_out, F1);
  not not_171 (not_171_out, F0);
  not not_172 (not_172_out, OP5);
  not not_173 (not_173_out, OP4);
  not not_174 (not_174_out, OP3);
  not not_175 (not_175_out, OP2);
  not not_176 (not_176_out, OP1);
  not not_177 (not_177_out, OP0);
  not not_178 (not_178_out, F4);
  not not_179 (not_179_out, F3);
  not not_180 (not_180_out, F2);
  not not_181 (not_181_out, F1);
  not not_182 (not_182_out, OP5);
  not not_183 (not_183_out, OP4);
  not not_184 (not_184_out, OP3);
  not not_185 (not_185_out, OP2);
  not not_186 (not_186_out, OP1);
  not not_187 (not_187_out, OP0);
  not not_188 (not_188_out, F4);
  not not_189 (not_189_out, F3);
  not not_190 (not_190_out, F2);
  not not_191 (not_191_out, F0);
  not not_192 (not_192_out, OP5);
  not not_193 (not_193_out, OP4);
  not not_194 (not_194_out, OP3);
  not not_195 (not_195_out, OP2);
  not not_196 (not_196_out, OP1);
  not not_197 (not_197_out, OP0);
  not not_198 (not_198_out, F4);
  not not_199 (not_199_out, F3);
  not not_200 (not_200_out, F1);
  not not_201 (not_201_out, F0);
  not not_202 (not_202_out, OP5);
  not not_203 (not_203_out, OP4);
  not not_204 (not_204_out, OP3);
  not not_205 (not_205_out, OP2);
  not not_206 (not_206_out, OP1);
  not not_207 (not_207_out, OP0);
  not not_208 (not_208_out, F4);
  not not_209 (not_209_out, F2);
  not not_210 (not_210_out, OP5);
  not not_211 (not_211_out, OP4);
  not not_212 (not_212_out, OP2);
  not not_213 (not_213_out, OP1);
  not not_214 (not_214_out, OP0);
  not not_215 (not_215_out, OP5);
  not not_216 (not_216_out, OP4);
  not not_217 (not_217_out, OP1);
  not not_218 (not_218_out, OP0);
  not not_219 (not_219_out, OP5);
  not not_220 (not_220_out, OP4);
  not not_221 (not_221_out, OP2);
  not not_222 (not_222_out, OP1);
  not not_223 (not_223_out, OP4);
  not not_224 (not_224_out, OP3);
  not not_225 (not_225_out, OP2);
  not not_226 (not_226_out, OP4);
  not not_227 (not_227_out, OP2);
  not not_228 (not_228_out, OP5);
  not not_229 (not_229_out, OP4);
  not not_230 (not_230_out, OP3);
  not not_231 (not_231_out, OP2);
  not not_232 (not_232_out, OP1);
  not not_233 (not_233_out, OP0);
  not not_234 (not_234_out, F4);
  not not_235 (not_235_out, F3);
  not not_236 (not_236_out, F2);
  not not_237 (not_237_out, OP4);
  not not_238 (not_238_out, OP2);
  not not_239 (not_239_out, OP1);
  not not_240 (not_240_out, OP0);
  not not_241 (not_241_out, OP5);
  not not_242 (not_242_out, OP4);
  not not_243 (not_243_out, OP3);
  not not_244 (not_244_out, OP2);
  not not_245 (not_245_out, OP1);
  not not_246 (not_246_out, OP0);
  not not_247 (not_247_out, F4);
  not not_248 (not_248_out, F3);
  not not_249 (not_249_out, F1);
  not not_250 (not_250_out, OP5);
  not not_251 (not_251_out, OP4);
  not not_252 (not_252_out, OP3);
  not not_253 (not_253_out, OP2);
  not not_254 (not_254_out, OP1);
  not not_255 (not_255_out, OP0);
  not not_256 (not_256_out, F4);
  not not_257 (not_257_out, F3);
  not not_258 (not_258_out, OP5);
  not not_259 (not_259_out, OP4);
  not not_260 (not_260_out, OP3);
  not not_261 (not_261_out, OP2);
  not not_262 (not_262_out, OP1);
  not not_263 (not_263_out, OP0);
  not not_264 (not_264_out, F4);
  not not_265 (not_265_out, F2);
  not not_266 (not_266_out, F0);
  not not_267 (not_267_out, OP5);
  not not_268 (not_268_out, OP4);
  not not_269 (not_269_out, OP3);
  not not_270 (not_270_out, OP2);
  not not_271 (not_271_out, OP1);
  not not_272 (not_272_out, OP0);
  not not_273 (not_273_out, F4);
  not not_274 (not_274_out, F2);
  not not_275 (not_275_out, OP5);
  not not_276 (not_276_out, OP4);
  not not_277 (not_277_out, OP2);
  not not_278 (not_278_out, OP0);
  not not_279 (not_279_out, OP5);
  not not_280 (not_280_out, OP4);
  not not_281 (not_281_out, OP1);
  not not_282 (not_282_out, OP5);
  not not_283 (not_283_out, OP4);
  not not_284 (not_284_out, OP3);
  not not_285 (not_285_out, OP2);
  not not_286 (not_286_out, OP1);
  not not_287 (not_287_out, OP0);
  not not_288 (not_288_out, F4);
  not not_289 (not_289_out, F3);
  not not_290 (not_290_out, F0);
  not not_291 (not_291_out, OP5);
  not not_292 (not_292_out, OP4);
  not not_293 (not_293_out, OP3);
  not not_294 (not_294_out, OP2);
  not not_295 (not_295_out, OP1);
  and and_1 (and_1_out, not_1_out, not_2_out, not_3_out, not_4_out, not_5_out, not_6_out, not_7_out, not_8_out, not_9_out, not_10_out, F1, F0);
  and and_2 (and_2_out, not_11_out, not_12_out, not_13_out, not_14_out, not_15_out, not_16_out, F5, not_17_out, not_18_out, not_19_out, not_20_out, not_21_out);
  and and_3 (and_3_out, not_22_out, not_23_out, not_24_out, not_25_out, not_26_out, not_27_out, F5, not_28_out, not_29_out, not_30_out, not_31_out, F0);
  and and_4 (and_4_out, not_32_out, not_33_out, not_34_out, not_35_out, not_36_out, not_37_out, F5, not_38_out, not_39_out, F2, not_40_out, not_41_out);
  and and_5 (and_5_out, not_42_out, not_43_out, not_44_out, not_45_out, not_46_out, not_47_out, F5, not_48_out, F3, not_49_out, F1, not_50_out);
  and and_6 (and_6_out, not_51_out, not_52_out, OP3, not_53_out, not_54_out, not_55_out);
  and and_7 (and_7_out, not_56_out, not_57_out, OP3, OP2, not_58_out, not_59_out);
  and and_8 (and_8_out, not_60_out, not_61_out, OP3, not_62_out, not_63_out, OP0);
  and and_9 (and_9_out, not_64_out, not_65_out, OP3, not_66_out, OP1, not_67_out);
  and and_10 (and_10_out, OP5, not_68_out, not_69_out, not_70_out, OP1, OP0);
  and and_11 (and_11_out, OP5, not_71_out, OP3, not_72_out, OP1, OP0);
  and and_12 (and_12_out, not_73_out, not_74_out, not_75_out, not_76_out, not_77_out, not_78_out, F5, not_79_out, not_80_out, F2, F1, not_81_out);
  and and_13 (and_13_out, OP5, not_82_out, OP3, not_83_out, not_84_out, not_85_out);
  and and_14 (and_14_out, not_86_out, not_87_out, not_88_out, not_89_out, not_90_out, OP0);
  and and_15 (and_15_out, not_91_out, not_92_out, not_93_out, not_94_out, not_95_out, not_96_out, not_97_out, not_98_out, not_99_out, not_100_out, F1, not_101_out);
  and and_16 (and_16_out, not_102_out, not_103_out, not_104_out, not_105_out, not_106_out, not_107_out, F5, not_108_out, not_109_out, not_110_out, F1, not_111_out);
  and and_17 (and_17_out, not_112_out, not_113_out, not_114_out, not_115_out, not_116_out, not_117_out, F5, not_118_out, not_119_out, F2, not_120_out, not_121_out);
  and and_18 (and_18_out, not_122_out, not_123_out, not_124_out, not_125_out, not_126_out, not_127_out, F5, not_128_out, not_129_out, F2, F1, F0);
  and and_19 (and_19_out, not_130_out, not_131_out, not_132_out, not_133_out, not_134_out, not_135_out, F5, not_136_out, F3, not_137_out, F1, not_138_out);
  and and_20 (and_20_out, not_139_out, not_140_out, OP3, OP2, not_141_out, not_142_out);
  and and_21 (and_21_out, not_143_out, not_144_out, OP3, not_145_out, OP1, not_146_out);
  and and_22 (and_22_out, not_147_out, not_148_out, not_149_out, not_150_out, not_151_out, not_152_out, F5, not_153_out, not_154_out, not_155_out, F1, F0);
  and and_23 (and_23_out, not_156_out, not_157_out, not_158_out, not_159_out, not_160_out, OP0);
  and and_24 (and_24_out, not_161_out, not_162_out, not_163_out, not_164_out, not_165_out, not_166_out, F5, not_167_out, not_168_out, not_169_out, not_170_out, not_171_out);
  and and_25 (and_25_out, not_172_out, not_173_out, not_174_out, not_175_out, not_176_out, not_177_out, F5, not_178_out, not_179_out, not_180_out, not_181_out, F0);
  and and_26 (and_26_out, not_182_out, not_183_out, not_184_out, not_185_out, not_186_out, not_187_out, F5, not_188_out, not_189_out, not_190_out, F1, not_191_out);
  and and_27 (and_27_out, not_192_out, not_193_out, not_194_out, not_195_out, not_196_out, not_197_out, F5, not_198_out, not_199_out, F2, not_200_out, not_201_out);
  and and_28 (and_28_out, not_202_out, not_203_out, not_204_out, not_205_out, not_206_out, not_207_out, F5, not_208_out, F3, not_209_out, F1, F0);
  and and_29 (and_29_out, not_210_out, not_211_out, OP3, not_212_out, not_213_out, not_214_out);
  and and_30 (and_30_out, not_215_out, not_216_out, OP3, OP2, not_217_out, not_218_out);
  and and_31 (and_31_out, not_219_out, not_220_out, OP3, not_221_out, not_222_out, OP0);
  and and_32 (and_32_out, OP5, not_223_out, not_224_out, not_225_out, OP1, OP0);
  and and_33 (and_33_out, OP5, not_226_out, OP3, not_227_out, OP1, OP0);
  and and_34 (and_34_out, not_228_out, not_229_out, not_230_out, not_231_out, not_232_out, not_233_out, F5, not_234_out, not_235_out, not_236_out, F1, F0);
  and and_35 (and_35_out, OP5, not_237_out, OP3, not_238_out, not_239_out, not_240_out);
  and and_36 (and_36_out, not_241_out, not_242_out, not_243_out, not_244_out, not_245_out, not_246_out, F5, not_247_out, not_248_out, F2, not_249_out, F0);
  and and_37 (and_37_out, not_250_out, not_251_out, not_252_out, not_253_out, not_254_out, not_255_out, F5, not_256_out, not_257_out, F2, F1, F0);
  and and_38 (and_38_out, not_258_out, not_259_out, not_260_out, not_261_out, not_262_out, not_263_out, F5, not_264_out, F3, not_265_out, F1, not_266_out);
  and and_39 (and_39_out, not_267_out, not_268_out, not_269_out, not_270_out, not_271_out, not_272_out, F5, not_273_out, F3, not_274_out, F1, F0);
  and and_40 (and_40_out, not_275_out, not_276_out, OP3, not_277_out, OP1, not_278_out);
  and and_41 (and_41_out, not_279_out, not_280_out, OP3, OP2, not_281_out, OP0);
  and and_42 (and_42_out, not_282_out, not_283_out, not_284_out, not_285_out, not_286_out, not_287_out, F5, not_288_out, not_289_out, F2, F1, not_290_out);
  and and_43 (and_43_out, not_291_out, not_292_out, not_293_out, not_294_out, not_295_out, OP0);
  or or_1 (S1, and_15_out, and_16_out, and_17_out, and_18_out, and_19_out, and_20_out, and_21_out, and_22_out, and_23_out);
  or or_2 (S3, and_36_out, and_37_out, and_38_out, and_39_out, and_40_out, and_41_out, and_42_out, and_43_out);
  or or_3 (S0, and_1_out, and_2_out, and_3_out, and_4_out, and_5_out, and_6_out, and_7_out, and_8_out, and_9_out, and_10_out, and_11_out, and_12_out, and_13_out, and_14_out);
  or or_4 (S2, and_24_out, and_25_out, and_26_out, and_27_out, and_28_out, and_29_out, and_30_out, and_31_out, and_32_out, and_33_out, and_34_out, and_35_out);
endmodule

// 控制信号生成
module \控制信号自动生成  (
  input  OP0,
  input  OP1,
  input  OP2,
  input  OP3,
  input  OP4,
  input  OP5,
  input  F0,
  input  F1,
  input  F2,
  input  F3,
  input  F4,
  input  F5,
  output MemToReg,
  output MemWrite,
  output BGEZ,
  output SB,
  output ALU_SRC,
  output RegWrite,
  output SysCALL,
  output SignedExt,
  output RegDst,
  output BEQ,
  output BNE,
  output JR,
  output JUMP,
  output JAL,
  output ERET
);

  wire and_2_out, and_3_out, and_6_out, and_7_out, and_8_out, and_9_out, and_10_out, and_11_out, and_12_out,
       and_13_out, and_14_out, and_15_out, and_16_out, and_18_out, and_19_out, and_20_out, and_21_out,
       and_22_out, and_23_out, and_24_out, and_25_out, and_26_out, and_27_out, and_30_out, and_31_out,
       not_1_out, not_2_out, not_3_out, not_4_out, not_5_out, not_6_out, not_7_out, not_8_out, not_9_out,
       not_10_out, not_11_out, not_12_out, not_13_out, not_14_out, not_15_out, not_16_out, not_17_out,
       not_18_out, not_19_out, not_20_out, not_21_out, not_22_out, not_23_out, not_24_out, not_25_out,
       not_26_out, not_27_out, not_28_out, not_29_out, not_30_out, not_31_out, not_32_out, not_33_out,
       not_34_out, not_35_out, not_36_out, not_37_out, not_38_out, not_39_out, not_40_out, not_41_out,
       not_42_out, not_43_out, not_44_out, not_45_out, not_46_out, not_47_out, not_48_out, not_49_out,
       not_50_out, not_51_out, not_52_out, not_53_out, not_54_out, not_55_out, not_56_out, not_57_out,
       not_58_out, not_59_out, not_60_out, not_61_out, not_62_out, not_63_out, not_64_out, not_65_out,
       not_66_out, not_67_out, not_68_out, not_69_out, not_70_out, not_71_out, not_72_out, not_73_out,
       not_74_out, not_75_out, not_76_out, not_77_out, not_78_out, not_79_out, not_80_out, not_81_out,
       not_82_out, not_83_out, not_84_out, not_85_out, not_86_out, not_87_out, not_88_out, not_89_out,
       not_90_out, not_91_out, not_92_out, not_93_out, not_94_out, not_95_out, not_96_out, not_97_out,
       not_98_out, not_99_out, not_100_out, not_101_out, not_102_out, not_103_out, not_104_out, not_105_out,
       not_106_out, not_107_out, not_108_out, not_109_out, not_110_out, not_111_out, not_112_out,
       not_113_out, not_114_out, not_115_out, not_116_out, not_117_out, not_118_out, not_119_out,
       not_120_out, not_121_out, not_122_out, not_123_out, not_124_out, not_125_out, not_126_out,
       not_127_out, not_128_out, not_129_out, not_130_out, not_131_out, not_132_out, not_133_out,
       not_134_out, not_135_out, not_136_out, not_137_out, not_138_out, not_139_out, not_140_out,
       not_141_out, not_142_out, not_143_out, not_144_out, not_145_out, not_146_out, not_147_out,
       not_148_out, not_149_out, not_150_out, not_151_out, not_152_out, not_153_out, not_154_out,
       not_155_out, not_156_out, not_157_out, not_158_out, not_159_out, not_160_out, not_161_out,
       not_162_out, not_163_out, not_164_out, not_165_out, not_166_out, not_167_out, not_168_out,
       not_169_out, not_170_out, not_171_out, not_172_out, not_173_out, not_174_out, not_175_out,
       not_176_out, not_177_out, not_178_out, not_179_out, not_180_out, not_181_out, not_182_out,
       not_183_out, not_184_out;

  not not_1 (not_1_out, OP2);
  not not_2 (not_2_out, OP3);
  not not_3 (not_3_out, OP4);
  not not_4 (not_4_out, OP0);
  not not_5 (not_5_out, OP1);
  not not_6 (not_6_out, OP2);
  not not_7 (not_7_out, OP4);
  not not_8 (not_8_out, OP2);
  not not_9 (not_9_out, OP4);
  not not_10 (not_10_out, OP1);
  not not_11 (not_11_out, OP2);
  not not_12 (not_12_out, OP3);
  not not_13 (not_13_out, OP4);
  not not_14 (not_14_out, OP5);
  not not_15 (not_15_out, OP0);
  not not_16 (not_16_out, OP1);
  not not_17 (not_17_out, OP2);
  not not_18 (not_18_out, OP4);
  not not_19 (not_19_out, OP0);
  not not_20 (not_20_out, OP1);
  not not_21 (not_21_out, OP2);
  not not_22 (not_22_out, OP4);
  not not_23 (not_23_out, OP0);
  not not_24 (not_24_out, OP2);
  not not_25 (not_25_out, OP4);
  not not_26 (not_26_out, OP5);
  not not_27 (not_27_out, OP1);
  not not_28 (not_28_out, OP4);
  not not_29 (not_29_out, OP5);
  not not_30 (not_30_out, OP2);
  not not_31 (not_31_out, OP4);
  not not_32 (not_32_out, OP0);
  not not_33 (not_33_out, OP1);
  not not_34 (not_34_out, OP2);
  not not_35 (not_35_out, OP4);
  not not_36 (not_36_out, OP5);
  not not_37 (not_37_out, F0);
  not not_38 (not_38_out, F2);
  not not_39 (not_39_out, F3);
  not not_40 (not_40_out, F4);
  not not_41 (not_41_out, OP0);
  not not_42 (not_42_out, OP1);
  not not_43 (not_43_out, OP2);
  not not_44 (not_44_out, OP4);
  not not_45 (not_45_out, OP5);
  not not_46 (not_46_out, F3);
  not not_47 (not_47_out, F4);
  not not_48 (not_48_out, OP0);
  not not_49 (not_49_out, OP1);
  not not_50 (not_50_out, OP2);
  not not_51 (not_51_out, OP4);
  not not_52 (not_52_out, OP5);
  not not_53 (not_53_out, F2);
  not not_54 (not_54_out, F3);
  not not_55 (not_55_out, F4);
  not not_56 (not_56_out, OP0);
  not not_57 (not_57_out, OP1);
  not not_58 (not_58_out, OP2);
  not not_59 (not_59_out, OP4);
  not not_60 (not_60_out, OP5);
  not not_61 (not_61_out, F2);
  not not_62 (not_62_out, F4);
  not not_63 (not_63_out, OP0);
  not not_64 (not_64_out, OP2);
  not not_65 (not_65_out, OP4);
  not not_66 (not_66_out, OP5);
  not not_67 (not_67_out, OP1);
  not not_68 (not_68_out, OP4);
  not not_69 (not_69_out, OP5);
  not not_70 (not_70_out, OP2);
  not not_71 (not_71_out, OP3);
  not not_72 (not_72_out, OP4);
  not not_73 (not_73_out, OP0);
  not not_74 (not_74_out, OP1);
  not not_75 (not_75_out, OP2);
  not not_76 (not_76_out, OP3);
  not not_77 (not_77_out, OP4);
  not not_78 (not_78_out, OP5);
  not not_79 (not_79_out, F0);
  not not_80 (not_80_out, F1);
  not not_81 (not_81_out, F4);
  not not_82 (not_82_out, F5);
  not not_83 (not_83_out, OP0);
  not not_84 (not_84_out, OP1);
  not not_85 (not_85_out, OP2);
  not not_86 (not_86_out, OP4);
  not not_87 (not_87_out, OP0);
  not not_88 (not_88_out, OP2);
  not not_89 (not_89_out, OP4);
  not not_90 (not_90_out, OP5);
  not not_91 (not_91_out, OP1);
  not not_92 (not_92_out, OP2);
  not not_93 (not_93_out, OP4);
  not not_94 (not_94_out, OP5);
  not not_95 (not_95_out, OP2);
  not not_96 (not_96_out, OP4);
  not not_97 (not_97_out, OP0);
  not not_98 (not_98_out, OP1);
  not not_99 (not_99_out, OP2);
  not not_100 (not_100_out, OP3);
  not not_101 (not_101_out, OP4);
  not not_102 (not_102_out, OP5);
  not not_103 (not_103_out, F0);
  not not_104 (not_104_out, F1);
  not not_105 (not_105_out, F2);
  not not_106 (not_106_out, F4);
  not not_107 (not_107_out, F5);
  not not_108 (not_108_out, OP0);
  not not_109 (not_109_out, OP1);
  not not_110 (not_110_out, OP2);
  not not_111 (not_111_out, OP3);
  not not_112 (not_112_out, OP4);
  not not_113 (not_113_out, OP5);
  not not_114 (not_114_out, F3);
  not not_115 (not_115_out, F4);
  not not_116 (not_116_out, OP0);
  not not_117 (not_117_out, OP1);
  not not_118 (not_118_out, OP2);
  not not_119 (not_119_out, OP3);
  not not_120 (not_120_out, OP4);
  not not_121 (not_121_out, OP5);
  not not_122 (not_122_out, F2);
  not not_123 (not_123_out, F3);
  not not_124 (not_124_out, F4);
  not not_125 (not_125_out, OP0);
  not not_126 (not_126_out, OP1);
  not not_127 (not_127_out, OP2);
  not not_128 (not_128_out, OP3);
  not not_129 (not_129_out, OP4);
  not not_130 (not_130_out, OP5);
  not not_131 (not_131_out, F2);
  not not_132 (not_132_out, F4);
  not not_133 (not_133_out, OP0);
  not not_134 (not_134_out, OP1);
  not not_135 (not_135_out, OP3);
  not not_136 (not_136_out, OP4);
  not not_137 (not_137_out, OP5);
  not not_138 (not_138_out, OP1);
  not not_139 (not_139_out, OP2);
  not not_140 (not_140_out, OP3);
  not not_141 (not_141_out, OP4);
  not not_142 (not_142_out, OP5);
  not not_143 (not_143_out, OP1);
  not not_144 (not_144_out, OP3);
  not not_145 (not_145_out, OP4);
  not not_146 (not_146_out, OP5);
  not not_147 (not_147_out, OP0);
  not not_148 (not_148_out, OP1);
  not not_149 (not_149_out, OP2);
  not not_150 (not_150_out, OP3);
  not not_151 (not_151_out, OP4);
  not not_152 (not_152_out, OP5);
  not not_153 (not_153_out, F0);
  not not_154 (not_154_out, F1);
  not not_155 (not_155_out, F2);
  not not_156 (not_156_out, F4);
  not not_157 (not_157_out, F5);
  not not_158 (not_158_out, OP0);
  not not_159 (not_159_out, OP2);
  not not_160 (not_160_out, OP3);
  not not_161 (not_161_out, OP4);
  not not_162 (not_162_out, OP5);
  not not_163 (not_163_out, F0);
  not not_164 (not_164_out, F1);
  not not_165 (not_165_out, F2);
  not not_166 (not_166_out, F4);
  not not_167 (not_167_out, F5);
  not not_168 (not_168_out, OP2);
  not not_169 (not_169_out, OP3);
  not not_170 (not_170_out, OP4);
  not not_171 (not_171_out, OP5);
  not not_172 (not_172_out, OP2);
  not not_173 (not_173_out, OP3);
  not not_174 (not_174_out, OP4);
  not not_175 (not_175_out, OP5);
  not not_176 (not_176_out, OP5);
  not not_177 (not_177_out, OP3);
  not not_178 (not_178_out, OP2);
  not not_179 (not_179_out, OP1);
  not not_180 (not_180_out, OP0);
  not not_181 (not_181_out, F5);
  not not_182 (not_182_out, F2);
  not not_183 (not_183_out, F1);
  not not_184 (not_184_out, F0);
  and and_1 (MemToReg, OP0, OP1, not_1_out, not_2_out, not_3_out, OP5);
  and and_2 (and_2_out, not_4_out, not_5_out, not_6_out, OP3, not_7_out, OP5);
  and and_3 (and_3_out, OP0, OP1, not_8_out, OP3, not_9_out, OP5);
  and and_4 (BGEZ, OP0, not_10_out, not_11_out, not_12_out, not_13_out, not_14_out);
  and and_5 (SB, not_15_out, not_16_out, not_17_out, OP3, not_18_out, OP5);
  and and_6 (and_6_out, not_19_out, not_20_out, not_21_out, OP3, not_22_out);
  and and_7 (and_7_out, not_23_out, not_24_out, OP3, not_25_out, not_26_out);
  and and_8 (and_8_out, not_27_out, OP3, not_28_out, not_29_out);
  and and_9 (and_9_out, OP0, OP1, not_30_out, not_31_out, OP5);
  and and_10 (and_10_out, not_32_out, not_33_out, not_34_out, not_35_out, not_36_out, not_37_out, not_38_out, not_39_out, not_40_out);
  and and_11 (and_11_out, not_41_out, not_42_out, not_43_out, not_44_out, not_45_out, not_46_out, not_47_out, F5);
  and and_12 (and_12_out, not_48_out, not_49_out, not_50_out, not_51_out, not_52_out, F1, not_53_out, not_54_out, not_55_out);
  and and_13 (and_13_out, not_56_out, not_57_out, not_58_out, not_59_out, not_60_out, F1, not_61_out, not_62_out, F5);
  and and_14 (and_14_out, not_63_out, not_64_out, OP3, not_65_out, not_66_out);
  and and_15 (and_15_out, not_67_out, OP3, not_68_out, not_69_out);
  and and_16 (and_16_out, OP0, OP1, not_70_out, not_71_out, not_72_out);
  and and_17 (SysCALL, not_73_out, not_74_out, not_75_out, not_76_out, not_77_out, not_78_out, not_79_out, not_80_out, F2, F3, not_81_out, not_82_out);
  and and_18 (and_18_out, not_83_out, not_84_out, not_85_out, OP3, not_86_out);
  and and_19 (and_19_out, not_87_out, not_88_out, OP3, not_89_out, not_90_out);
  and and_20 (and_20_out, not_91_out, not_92_out, OP3, not_93_out, not_94_out);
  and and_21 (and_21_out, OP0, OP1, not_95_out, not_96_out, OP5);
  and and_22 (and_22_out, not_97_out, not_98_out, not_99_out, not_100_out, not_101_out, not_102_out, not_103_out, not_104_out, not_105_out, not_106_out, not_107_out);
  and and_23 (and_23_out, not_108_out, not_109_out, not_110_out, not_111_out, not_112_out, not_113_out, not_114_out, not_115_out, F5);
  and and_24 (and_24_out, not_116_out, not_117_out, not_118_out, not_119_out, not_120_out, not_121_out, F1, not_122_out, not_123_out, not_124_out);
  and and_25 (and_25_out, not_125_out, not_126_out, not_127_out, not_128_out, not_129_out, not_130_out, F1, not_131_out, not_132_out, F5);
  and and_26 (and_26_out, not_133_out, not_134_out, OP2, not_135_out, not_136_out, not_137_out);
  and and_27 (and_27_out, OP0, not_138_out, not_139_out, not_140_out, not_141_out, not_142_out);
  and and_28 (BNE, OP0, not_143_out, OP2, not_144_out, not_145_out, not_146_out);
  and and_29 (JR, not_147_out, not_148_out, not_149_out, not_150_out, not_151_out, not_152_out, not_153_out, not_154_out, not_155_out, F3, not_156_out, not_157_out);
  and and_30 (and_30_out, not_158_out, not_159_out, not_160_out, not_161_out, not_162_out, not_163_out, not_164_out, not_165_out, F3, not_166_out, not_167_out);
  and and_31 (and_31_out, OP1, not_168_out, not_169_out, not_170_out, not_171_out);
  and and_32 (JAL, OP0, OP1, not_172_out, not_173_out, not_174_out, not_175_out);
  and and_33 (ERET, not_176_out, OP4, not_177_out, not_178_out, not_179_out, not_180_out, not_181_out, F4, F3, not_182_out, not_183_out, not_184_out);
  or or_1 (MemWrite, and_2_out, and_3_out);
  or or_2 (ALU_SRC, and_6_out, and_7_out, and_8_out, and_9_out);
  or or_3 (RegWrite, and_10_out, and_11_out, and_12_out, and_13_out, and_14_out, and_15_out, and_16_out);
  or or_4 (SignedExt, and_18_out, and_19_out, and_20_out, and_21_out);
  or or_5 (RegDst, and_22_out, and_23_out, and_24_out, and_25_out);
  or or_6 (BEQ, and_26_out, and_27_out);
  or or_7 (JUMP, and_30_out, and_31_out);
endmodule

// 相关检测逻辑
module Correlation_detection_logic (
  input  [5:0] ID_OP,
  input  [5:0] ID_FUNC,
  input  [4:0] ID_R1_num,
  input  [4:0] ID_R2_num,
  input  EX_RegWrite,
  input  MEM_RegWrite,
  input  [4:0] EX_W_num,
  input  [4:0] MEM_W_num,
  output NEED_BUBBLE
);

  wire and_1_out, and_2_out, and_3_out, and_4_out, and_5_out, and_6_out, comparator_1_eq, comparator_2_eq,
       comparator_3_eq, comparator_4_eq, comparator_5_eq, comparator_6_eq, not_1_out, not_2_out, or_1_out,
       or_2_out, r_used_1_r1used, r_used_1_r2used;

  R_USED r_used_1 (
    .OP0(ID_OP[0]), .OP1(ID_OP[1]), .OP2(ID_OP[2]), .OP3(ID_OP[3]), .OP4(ID_OP[4]), .OP5(ID_OP[5]),
    .F0(ID_FUNC[0]), .F1(ID_FUNC[1]), .F2(ID_FUNC[2]), .F3(ID_FUNC[3]), .F4(ID_FUNC[4]), .F5(ID_FUNC[5]),
    .R1USED(r_used_1_r1used), .R2USED(r_used_1_r2used));
  Comparator #(.width(5), .mode("twosComplement")) comparator_1 (
    .a(ID_R1_num), .b(EX_W_num), .eq(comparator_1_eq));  // open: gt, lt
  Comparator #(.width(5), .mode("twosComplement")) comparator_2 (
    .a(ID_R2_num), .b(EX_W_num), .eq(comparator_2_eq));  // open: gt, lt
  Comparator #(.width(5), .mode("twosComplement")) comparator_3 (
    .a(ID_R1_num), .b(MEM_W_num), .eq(comparator_3_eq));  // open: gt, lt
  Comparator #(.width(5), .mode("twosComplement")) comparator_4 (
    .a(ID_R2_num), .b(MEM_W_num), .eq(comparator_4_eq));  // open: gt, lt
  and and_1 (and_1_out, comparator_1_eq, r_used_1_r1used);
  and and_2 (and_2_out, r_used_1_r2used, comparator_2_eq);
  and and_3 (and_3_out, comparator_3_eq, r_used_1_r1used);
  and and_4 (and_4_out, r_used_1_r2used, comparator_4_eq);
  or or_1 (or_1_out, and_1_out, and_2_out);
  or or_2 (or_2_out, and_3_out, and_4_out);
  Comparator #(.width(5), .mode("twosComplement")) comparator_5 (
    .a({5{1'b0}}), .b(EX_W_num), .eq(comparator_5_eq));  // open: gt, lt
  Comparator #(.width(5), .mode("twosComplement")) comparator_6 (
    .a({5{1'b0}}), .b(MEM_W_num), .eq(comparator_6_eq));  // open: gt, lt
  not not_1 (not_1_out, comparator_5_eq);
  not not_2 (not_2_out, comparator_6_eq);
  and and_5 (and_5_out, or_1_out, EX_RegWrite, not_1_out);
  or or_3 (NEED_BUBBLE, and_5_out, and_6_out);
  and and_6 (and_6_out, not_2_out, MEM_RegWrite, or_2_out);

  // Notes on the sheet:
  //   不考虑0号寄存器
endmodule

// 重定向信号逻辑
module Redirect_signal_logic (
  input  [5:0] ID_OP,
  input  [5:0] ID_FUNC,
  input  [4:0] ID_R1_num,
  input  [4:0] ID_R2_num,
  input  [4:0] EX_W_num,
  input  [4:0] MEM_W_num,
  input  [4:0] WB_W_num,
  input  EX_RegWrite,
  input  MEM_RegWrite,
  input  WB_RegWrite,
  input  [5:0] EX_OP,
  input  [5:0] EX_FUNC,
  input  [4:0] EX_R1_num,
  input  [4:0] EX_R2_num,
  output Load_Use,
  output [1:0] R2_Forward,
  output [1:0] R1_Forward
);

  wire and_1_out, and_2_out, and_3_out, and_4_out, and_5_out, comparator_1_eq, comparator_2_eq,
       comparator_3_eq, comparator_4_eq, comparator_5_eq, comparator_6_eq, comparator_7_eq, comparator_8_eq,
       comparator_9_eq, comparator_10_eq, not_1_out, not_2_out, not_3_out, or_1_out, r_used_1_r1used,
       r_used_1_r2used, r_used_2_r1used, r_used_2_r2used;
  wire [1:0] and_7_out, and_9_out;

  R_USED r_used_1 (
    .OP0(ID_OP[0]), .OP1(ID_OP[1]), .OP2(ID_OP[2]), .OP3(ID_OP[3]), .OP4(ID_OP[4]), .OP5(ID_OP[5]),
    .F0(ID_FUNC[0]), .F1(ID_FUNC[1]), .F2(ID_FUNC[2]), .F3(ID_FUNC[3]), .F4(ID_FUNC[4]), .F5(ID_FUNC[5]),
    .R1USED(r_used_1_r1used), .R2USED(r_used_1_r2used));
  R_USED r_used_2 (
    .OP0(EX_OP[0]), .OP1(EX_OP[1]), .OP2(EX_OP[2]), .OP3(EX_OP[3]), .OP4(EX_OP[4]), .OP5(EX_OP[5]),
    .F0(EX_FUNC[0]), .F1(EX_FUNC[1]), .F2(EX_FUNC[2]), .F3(EX_FUNC[3]), .F4(EX_FUNC[4]), .F5(EX_FUNC[5]),
    .R1USED(r_used_2_r1used), .R2USED(r_used_2_r2used));
  Comparator #(.width(5), .mode("twosComplement")) comparator_1 (
    .a(ID_R1_num), .b(EX_W_num), .eq(comparator_1_eq));  // open: gt, lt
  Comparator #(.width(5), .mode("twosComplement")) comparator_2 (
    .a(ID_R2_num), .b(EX_W_num), .eq(comparator_2_eq));  // open: gt, lt
  Comparator #(.width(5), .mode("twosComplement")) comparator_3 (
    .a(EX_R1_num), .b({5{1'b0}}), .eq(comparator_3_eq));  // open: gt, lt
  Comparator #(.width(5), .mode("twosComplement")) comparator_4 (
    .a(EX_R2_num), .b({5{1'b0}}), .eq(comparator_4_eq));  // open: gt, lt
  and and_1 (and_1_out, comparator_1_eq, r_used_1_r1used);
  and and_2 (and_2_out, r_used_1_r2used, comparator_2_eq);
  not not_1 (not_1_out, comparator_3_eq);
  and and_3 (and_3_out, not_1_out, r_used_2_r1used);
  and and_4 (and_4_out, r_used_2_r2used, not_2_out);
  not not_2 (not_2_out, comparator_4_eq);
  or or_1 (or_1_out, and_1_out, and_2_out);
  Comparator #(.width(5), .mode("twosComplement")) comparator_5 (
    .a({5{1'b0}}), .b(EX_W_num), .eq(comparator_5_eq));  // open: gt, lt
  Comparator #(.width(5), .mode("twosComplement")) comparator_6 (
    .a(EX_R1_num), .b(MEM_W_num), .eq(comparator_6_eq));  // open: gt, lt
  Comparator #(.width(5), .mode("twosComplement")) comparator_7 (
    .a(EX_R1_num), .b(WB_W_num), .eq(comparator_7_eq));  // open: gt, lt
  Comparator #(.width(5), .mode("twosComplement")) comparator_8 (
    .a(EX_R2_num), .b(MEM_W_num), .eq(comparator_8_eq));  // open: gt, lt
  Comparator #(.width(5), .mode("twosComplement")) comparator_9 (
    .a(EX_R2_num), .b(WB_W_num), .eq(comparator_9_eq));  // open: gt, lt
  not not_3 (not_3_out, comparator_5_eq);
  and and_5 (and_5_out, or_1_out, EX_RegWrite, not_3_out);
  Comparator #(.width(6), .mode("twosComplement")) comparator_10 (
    .a(EX_OP), .b(6'b100011), .eq(comparator_10_eq));  // open: gt, lt
  and and_6 (and_7_out[1], MEM_RegWrite, comparator_6_eq, and_3_out);
  and and_7 (and_7_out[0], and_3_out, comparator_7_eq, WB_RegWrite);
  and and_8 (and_9_out[1], MEM_RegWrite, comparator_8_eq, and_4_out);
  and and_9 (and_9_out[0], and_4_out, comparator_9_eq, WB_RegWrite);
  and and_10 (Load_Use, comparator_10_eq, and_5_out);
  Multiplexer #(.select(2), .width(2), .disabled("Z"), .enable("false")) multiplexer_1 (
    .in0(2'b00), .in1(2'b10), .in2(2'b01), .in3(2'b01), .out(R1_Forward), .sel(and_7_out));
  Multiplexer #(.select(2), .width(2), .disabled("Z"), .enable("false")) multiplexer_2 (
    .in0(2'b00), .in1(2'b10), .in2(2'b01), .in3(2'b01), .out(R2_Forward), .sel(and_9_out));

  // Notes on the sheet:
  //   不考虑0号寄存器
  //   不考虑0号寄存器
endmodule

// 寄存器使用
module R_USED (
  input  OP0,
  input  OP1,
  input  OP2,
  input  OP3,
  input  OP4,
  input  OP5,
  input  F0,
  input  F1,
  input  F2,
  input  F3,
  input  F4,
  input  F5,
  output R1USED,
  output R2USED
);

  wire and_1_out, and_2_out, and_3_out, and_4_out, and_5_out, and_6_out, and_7_out, and_8_out, and_9_out,
       and_10_out, and_11_out, and_12_out, and_13_out, and_14_out, and_15_out, and_16_out, and_17_out,
       and_18_out, and_19_out, and_20_out, and_21_out, and_22_out, and_23_out, and_24_out, and_25_out,
       and_26_out, and_27_out, and_28_out, and_29_out, and_30_out, and_31_out, and_32_out, and_33_out,
       and_34_out, and_35_out, and_36_out, and_37_out, and_38_out, and_39_out, and_40_out, and_41_out,
       not_1_out, not_2_out, not_3_out, not_4_out, not_5_out, not_6_out, not_7_out, not_8_out, not_9_out,
       not_10_out, not_11_out, not_12_out, not_13_out, not_14_out, not_15_out, not_16_out, not_17_out,
       not_18_out, not_19_out, not_20_out, not_21_out, not_22_out, not_23_out, not_24_out, not_25_out,
       not_26_out, not_27_out, not_28_out, not_29_out, not_30_out, not_31_out, not_32_out, not_33_out,
       not_34_out, not_35_out, not_36_out, not_37_out, not_38_out, not_39_out, not_40_out, not_41_out,
       not_42_out, not_43_out, not_44_out, not_45_out, not_46_out, not_47_out, not_48_out, not_49_out,
       not_50_out, not_51_out, not_52_out, not_53_out, not_54_out, not_55_out, not_56_out, not_57_out,
       not_58_out, not_59_out, not_60_out, not_61_out, not_62_out, not_63_out, not_64_out, not_65_out,
       not_66_out, not_67_out, not_68_out, not_69_out, not_70_out, not_71_out, not_72_out, not_73_out,
       not_74_out, not_75_out, not_76_out, not_77_out, not_78_out, not_79_out, not_80_out, not_81_out,
       not_82_out, not_83_out, not_84_out, not_85_out, not_86_out, not_87_out, not_88_out, not_89_out,
       not_90_out, not_91_out, not_92_out, not_93_out, not_94_out, not_95_out, not_96_out, not_97_out,
       not_98_out, not_99_out, not_100_out, not_101_out, not_102_out, not_103_out, not_104_out, not_105_out,
       not_106_out, not_107_out, not_108_out, not_109_out, not_110_out, not_111_out, not_112_out,
       not_113_out, not_114_out, not_115_out, not_116_out, not_117_out, not_118_out, not_119_out,
       not_120_out, not_121_out, not_122_out, not_123_out, not_124_out, not_125_out, not_126_out,
       not_127_out, not_128_out, not_129_out, not_130_out, not_131_out, not_132_out, not_133_out,
       not_134_out, not_135_out, not_136_out, not_137_out, not_138_out, not_139_out, not_140_out,
       not_141_out, not_142_out, not_143_out, not_144_out, not_145_out, not_146_out, not_147_out,
       not_148_out, not_149_out, not_150_out, not_151_out, not_152_out, not_153_out, not_154_out,
       not_155_out, not_156_out, not_157_out, not_158_out, not_159_out, not_160_out, not_161_out,
       not_162_out, not_163_out, not_164_out, not_165_out, not_166_out, not_167_out, not_168_out,
       not_169_out, not_170_out, not_171_out, not_172_out, not_173_out, not_174_out, not_175_out,
       not_176_out, not_177_out, not_178_out, not_179_out, not_180_out, not_181_out, not_182_out,
       not_183_out, not_184_out, not_185_out, not_186_out, not_187_out, not_188_out, not_189_out,
       not_190_out, not_191_out, not_192_out, not_193_out, not_194_out, not_195_out, not_196_out,
       not_197_out, not_198_out, not_199_out, not_200_out, not_201_out, not_202_out, not_203_out,
       not_204_out, not_205_out, not_206_out, not_207_out, not_208_out, not_209_out, not_210_out,
       not_211_out, not_212_out, not_213_out, not_214_out, not_215_out, not_216_out, not_217_out,
       not_218_out, not_219_out, not_220_out, not_221_out, not_222_out, not_223_out, not_224_out,
       not_225_out, not_226_out, not_227_out, not_228_out, not_229_out, not_230_out, not_231_out,
       not_232_out, not_233_out, not_234_out, not_235_out, not_236_out, not_237_out, not_238_out,
       not_239_out, not_240_out, not_241_out, not_242_out, not_243_out, not_244_out, not_245_out,
       not_246_out, not_247_out, not_248_out, not_249_out, not_250_out, not_251_out, not_252_out,
       not_253_out, not_254_out, not_255_out, not_256_out, not_257_out, not_258_out, not_259_out,
       not_260_out, not_261_out, not_262_out, not_263_out, not_264_out, not_265_out, not_266_out,
       not_267_out, not_268_out, not_269_out, not_270_out, not_271_out, not_272_out, not_273_out,
       not_274_out, not_275_out, not_276_out, not_277_out, not_278_out, not_279_out, not_280_out,
       not_281_out, not_282_out, not_283_out, not_284_out, not_285_out, not_286_out, not_287_out,
       not_288_out, not_289_out, not_290_out, not_291_out, not_292_out, not_293_out, not_294_out,
       not_295_out, not_296_out, not_297_out, not_298_out, not_299_out, not_300_out, not_301_out,
       not_302_out, not_303_out, not_304_out, not_305_out, not_306_out, not_307_out, not_308_out;

  not not_1 (not_1_out, OP5);
  not not_2 (not_2_out, OP4);
  not not_3 (not_3_out, OP3);
  not not_4 (not_4_out, OP2);
  not not_5 (not_5_out, OP1);
  not not_6 (not_6_out, OP0);
  not not_7 (not_7_out, F4);
  not not_8 (not_8_out, F3);
  not not_9 (not_9_out, F2);
  not not_10 (not_10_out, F1);
  not not_11 (not_11_out, F0);
  not not_12 (not_12_out, OP5);
  not not_13 (not_13_out, OP4);
  not not_14 (not_14_out, OP3);
  not not_15 (not_15_out, OP2);
  not not_16 (not_16_out, OP1);
  not not_17 (not_17_out, OP0);
  not not_18 (not_18_out, F4);
  not not_19 (not_19_out, F3);
  not not_20 (not_20_out, F2);
  not not_21 (not_21_out, F1);
  not not_22 (not_22_out, OP5);
  not not_23 (not_23_out, OP4);
  not not_24 (not_24_out, OP3);
  not not_25 (not_25_out, OP2);
  not not_26 (not_26_out, OP1);
  not not_27 (not_27_out, OP0);
  not not_28 (not_28_out, F4);
  not not_29 (not_29_out, F3);
  not not_30 (not_30_out, F2);
  not not_31 (not_31_out, F0);
  not not_32 (not_32_out, OP5);
  not not_33 (not_33_out, OP4);
  not not_34 (not_34_out, OP3);
  not not_35 (not_35_out, OP2);
  not not_36 (not_36_out, OP1);
  not not_37 (not_37_out, OP0);
  not not_38 (not_38_out, F4);
  not not_39 (not_39_out, F3);
  not not_40 (not_40_out, F1);
  not not_41 (not_41_out, F0);
  not not_42 (not_42_out, OP5);
  not not_43 (not_43_out, OP4);
  not not_44 (not_44_out, OP3);
  not not_45 (not_45_out, OP2);
  not not_46 (not_46_out, OP1);
  not not_47 (not_47_out, OP0);
  not not_48 (not_48_out, F4);
  not not_49 (not_49_out, F3);
  not not_50 (not_50_out, F1);
  not not_51 (not_51_out, OP5);
  not not_52 (not_52_out, OP4);
  not not_53 (not_53_out, OP3);
  not not_54 (not_54_out, OP2);
  not not_55 (not_55_out, OP1);
  not not_56 (not_56_out, OP0);
  not not_57 (not_57_out, F4);
  not not_58 (not_58_out, F3);
  not not_59 (not_59_out, OP5);
  not not_60 (not_60_out, OP4);
  not not_61 (not_61_out, OP3);
  not not_62 (not_62_out, OP2);
  not not_63 (not_63_out, OP1);
  not not_64 (not_64_out, OP0);
  not not_65 (not_65_out, F4);
  not not_66 (not_66_out, F2);
  not not_67 (not_67_out, F0);
  not not_68 (not_68_out, OP5);
  not not_69 (not_69_out, OP4);
  not not_70 (not_70_out, OP3);
  not not_71 (not_71_out, OP2);
  not not_72 (not_72_out, OP1);
  not not_73 (not_73_out, OP0);
  not not_74 (not_74_out, F4);
  not not_75 (not_75_out, F2);
  not not_76 (not_76_out, OP5);
  not not_77 (not_77_out, OP4);
  not not_78 (not_78_out, OP3);
  not not_79 (not_79_out, OP2);
  not not_80 (not_80_out, OP1);
  not not_81 (not_81_out, OP0);
  not not_82 (not_82_out, F5);
  not not_83 (not_83_out, F4);
  not not_84 (not_84_out, F2);
  not not_85 (not_85_out, F1);
  not not_86 (not_86_out, F0);
  not not_87 (not_87_out, OP5);
  not not_88 (not_88_out, OP4);
  not not_89 (not_89_out, OP3);
  not not_90 (not_90_out, OP2);
  not not_91 (not_91_out, OP1);
  not not_92 (not_92_out, OP0);
  not not_93 (not_93_out, F5);
  not not_94 (not_94_out, F4);
  not not_95 (not_95_out, F1);
  not not_96 (not_96_out, F0);
  not not_97 (not_97_out, OP5);
  not not_98 (not_98_out, OP4);
  not not_99 (not_99_out, OP3);
  not not_100 (not_100_out, OP1);
  not not_101 (not_101_out, OP0);
  not not_102 (not_102_out, OP5);
  not not_103 (not_103_out, OP4);
  not not_104 (not_104_out, OP3);
  not not_105 (not_105_out, OP1);
  not not_106 (not_106_out, OP5);
  not not_107 (not_107_out, OP4);
  not not_108 (not_108_out, OP2);
  not not_109 (not_109_out, OP1);
  not not_110 (not_110_out, OP0);
  not not_111 (not_111_out, OP5);
  not not_112 (not_112_out, OP4);
  not not_113 (not_113_out, OP1);
  not not_114 (not_114_out, OP0);
  not not_115 (not_115_out, OP5);
  not not_116 (not_116_out, OP4);
  not not_117 (not_117_out, OP2);
  not not_118 (not_118_out, OP1);
  not not_119 (not_119_out, OP5);
  not not_120 (not_120_out, OP4);
  not not_121 (not_121_out, OP2);
  not not_122 (not_122_out, OP0);
  not not_123 (not_123_out, OP5);
  not not_124 (not_124_out, OP4);
  not not_125 (not_125_out, OP1);
  not not_126 (not_126_out, OP4);
  not not_127 (not_127_out, OP3);
  not not_128 (not_128_out, OP2);
  not not_129 (not_129_out, OP4);
  not not_130 (not_130_out, OP2);
  not not_131 (not_131_out, OP5);
  not not_132 (not_132_out, OP4);
  not not_133 (not_133_out, OP3);
  not not_134 (not_134_out, OP2);
  not not_135 (not_135_out, OP1);
  not not_136 (not_136_out, OP0);
  not not_137 (not_137_out, F4);
  not not_138 (not_138_out, F3);
  not not_139 (not_139_out, F2);
  not not_140 (not_140_out, OP5);
  not not_141 (not_141_out, OP4);
  not not_142 (not_142_out, OP3);
  not not_143 (not_143_out, OP2);
  not not_144 (not_144_out, OP1);
  not not_145 (not_145_out, OP0);
  not not_146 (not_146_out, F4);
  not not_147 (not_147_out, F3);
  not not_148 (not_148_out, F0);
  not not_149 (not_149_out, OP4);
  not not_150 (not_150_out, OP2);
  not not_151 (not_151_out, OP1);
  not not_152 (not_152_out, OP0);
  not not_153 (not_153_out, OP5);
  not not_154 (not_154_out, OP4);
  not not_155 (not_155_out, OP3);
  not not_156 (not_156_out, OP2);
  not not_157 (not_157_out, OP1);
  not not_158 (not_158_out, OP5);
  not not_159 (not_159_out, OP4);
  not not_160 (not_160_out, OP3);
  not not_161 (not_161_out, OP2);
  not not_162 (not_162_out, OP1);
  not not_163 (not_163_out, OP0);
  not not_164 (not_164_out, F5);
  not not_165 (not_165_out, F4);
  not not_166 (not_166_out, F3);
  not not_167 (not_167_out, F2);
  not not_168 (not_168_out, F1);
  not not_169 (not_169_out, F0);
  not not_170 (not_170_out, OP5);
  not not_171 (not_171_out, OP4);
  not not_172 (not_172_out, OP3);
  not not_173 (not_173_out, OP2);
  not not_174 (not_174_out, OP1);
  not not_175 (not_175_out, OP0);
  not not_176 (not_176_out, F5);
  not not_177 (not_177_out, F4);
  not not_178 (not_178_out, F3);
  not not_179 (not_179_out, F2);
  not not_180 (not_180_out, OP5);
  not not_181 (not_181_out, OP4);
  not not_182 (not_182_out, OP3);
  not not_183 (not_183_out, OP2);
  not not_184 (not_184_out, OP1);
  not not_185 (not_185_out, OP0);
  not not_186 (not_186_out, F5);
  not not_187 (not_187_out, F4);
  not not_188 (not_188_out, F3);
  not not_189 (not_189_out, F2);
  not not_190 (not_190_out, F0);
  not not_191 (not_191_out, OP5);
  not not_192 (not_192_out, OP4);
  not not_193 (not_193_out, OP3);
  not not_194 (not_194_out, OP2);
  not not_195 (not_195_out, OP1);
  not not_196 (not_196_out, OP0);
  not not_197 (not_197_out, F4);
  not not_198 (not_198_out, F3);
  not not_199 (not_199_out, F2);
  not not_200 (not_200_out, F1);
  not not_201 (not_201_out, F0);
  not not_202 (not_202_out, OP5);
  not not_203 (not_203_out, OP4);
  not not_204 (not_204_out, OP3);
  not not_205 (not_205_out, OP2);
  not not_206 (not_206_out, OP1);
  not not_207 (not_207_out, OP0);
  not not_208 (not_208_out, F4);
  not not_209 (not_209_out, F3);
  not not_210 (not_210_out, F2);
  not not_211 (not_211_out, F1);
  not not_212 (not_212_out, OP5);
  not not_213 (not_213_out, OP4);
  not not_214 (not_214_out, OP3);
  not not_215 (not_215_out, OP2);
  not not_216 (not_216_out, OP1);
  not not_217 (not_217_out, OP0);
  not not_218 (not_218_out, F4);
  not not_219 (not_219_out, F3);
  not not_220 (not_220_out, F2);
  not not_221 (not_221_out, F0);
  not not_222 (not_222_out, OP5);
  not not_223 (not_223_out, OP4);
  not not_224 (not_224_out, OP3);
  not not_225 (not_225_out, OP2);
  not not_226 (not_226_out, OP1);
  not not_227 (not_227_out, OP0);
  not not_228 (not_228_out, F4);
  not not_229 (not_229_out, F3);
  not not_230 (not_230_out, F1);
  not not_231 (not_231_out, F0);
  not not_232 (not_232_out, OP5);
  not not_233 (not_233_out, OP4);
  not not_234 (not_234_out, OP3);
  not not_235 (not_235_out, OP2);
  not not_236 (not_236_out, OP1);
  not not_237 (not_237_out, OP0);
  not not_238 (not_238_out, F4);
  not not_239 (not_239_out, F3);
  not not_240 (not_240_out, F1);
  not not_241 (not_241_out, OP5);
  not not_242 (not_242_out, OP4);
  not not_243 (not_243_out, OP3);
  not not_244 (not_244_out, OP2);
  not not_245 (not_245_out, OP1);
  not not_246 (not_246_out, OP0);
  not not_247 (not_247_out, F4);
  not not_248 (not_248_out, F3);
  not not_249 (not_249_out, OP5);
  not not_250 (not_250_out, OP4);
  not not_251 (not_251_out, OP3);
  not not_252 (not_252_out, OP2);
  not not_253 (not_253_out, OP1);
  not not_254 (not_254_out, OP0);
  not not_255 (not_255_out, F4);
  not not_256 (not_256_out, F2);
  not not_257 (not_257_out, F0);
  not not_258 (not_258_out, OP5);
  not not_259 (not_259_out, OP4);
  not not_260 (not_260_out, OP3);
  not not_261 (not_261_out, OP2);
  not not_262 (not_262_out, OP1);
  not not_263 (not_263_out, OP0);
  not not_264 (not_264_out, F4);
  not not_265 (not_265_out, F2);
  not not_266 (not_266_out, OP5);
  not not_267 (not_267_out, OP4);
  not not_268 (not_268_out, OP3);
  not not_269 (not_269_out, OP2);
  not not_270 (not_270_out, OP1);
  not not_271 (not_271_out, OP0);
  not not_272 (not_272_out, F5);
  not not_273 (not_273_out, F4);
  not not_274 (not_274_out, F1);
  not not_275 (not_275_out, F0);
  not not_276 (not_276_out, OP5);
  not not_277 (not_277_out, OP4);
  not not_278 (not_278_out, OP3);
  not not_279 (not_279_out, OP1);
  not not_280 (not_280_out, OP0);
  not not_281 (not_281_out, OP5);
  not not_282 (not_282_out, OP4);
  not not_283 (not_283_out, OP3);
  not not_284 (not_284_out, OP1);
  not not_285 (not_285_out, OP4);
  not not_286 (not_286_out, OP2);
  not not_287 (not_287_out, OP5);
  not not_288 (not_288_out, OP4);
  not not_289 (not_289_out, OP3);
  not not_290 (not_290_out, OP2);
  not not_291 (not_291_out, OP1);
  not not_292 (not_292_out, OP0);
  not not_293 (not_293_out, F4);
  not not_294 (not_294_out, F3);
  not not_295 (not_295_out, F2);
  not not_296 (not_296_out, OP5);
  not not_297 (not_297_out, OP4);
  not not_298 (not_298_out, OP3);
  not not_299 (not_299_out, OP2);
  not not_300 (not_300_out, OP1);
  not not_301 (not_301_out, OP0);
  not not_302 (not_302_out, F4);
  not not_303 (not_303_out, F3);
  not not_304 (not_304_out, F0);
  not not_305 (not_305_out, OP4);
  not not_306 (not_306_out, OP2);
  not not_307 (not_307_out, OP1);
  not not_308 (not_308_out, OP0);
  and and_1 (and_1_out, not_1_out, not_2_out, not_3_out, not_4_out, not_5_out, not_6_out, F5, not_7_out, not_8_out, not_9_out, not_10_out, not_11_out);
  and and_2 (and_2_out, not_12_out, not_13_out, not_14_out, not_15_out, not_16_out, not_17_out, F5, not_18_out, not_19_out, not_20_out, not_21_out, F0);
  and and_3 (and_3_out, not_22_out, not_23_out, not_24_out, not_25_out, not_26_out, not_27_out, F5, not_28_out, not_29_out, not_30_out, F1, not_31_out);
  and and_4 (and_4_out, not_32_out, not_33_out, not_34_out, not_35_out, not_36_out, not_37_out, F5, not_38_out, not_39_out, F2, not_40_out, not_41_out);
  and and_5 (and_5_out, not_42_out, not_43_out, not_44_out, not_45_out, not_46_out, not_47_out, F5, not_48_out, not_49_out, F2, not_50_out, F0);
  and and_6 (and_6_out, not_51_out, not_52_out, not_53_out, not_54_out, not_55_out, not_56_out, F5, not_57_out, not_58_out, F2, F1, F0);
  and and_7 (and_7_out, not_59_out, not_60_out, not_61_out, not_62_out, not_63_out, not_64_out, F5, not_65_out, F3, not_66_out, F1, not_67_out);
  and and_8 (and_8_out, not_68_out, not_69_out, not_70_out, not_71_out, not_72_out, not_73_out, F5, not_74_out, F3, not_75_out, F1, F0);
  and and_9 (and_9_out, not_76_out, not_77_out, not_78_out, not_79_out, not_80_out, not_81_out, not_82_out, not_83_out, F3, not_84_out, not_85_out, not_86_out);
  and and_10 (and_10_out, not_87_out, not_88_out, not_89_out, not_90_out, not_91_out, not_92_out, not_93_out, not_94_out, F3, F2, not_95_out, not_96_out);
  and and_11 (and_11_out, not_97_out, not_98_out, not_99_out, OP2, not_100_out, not_101_out);
  and and_12 (and_12_out, not_102_out, not_103_out, not_104_out, OP2, not_105_out, OP0);
  and and_13 (and_13_out, not_106_out, not_107_out, OP3, not_108_out, not_109_out, not_110_out);
  and and_14 (and_14_out, not_111_out, not_112_out, OP3, OP2, not_113_out, not_114_out);
  and and_15 (and_15_out, not_115_out, not_116_out, OP3, not_117_out, not_118_out, OP0);
  and and_16 (and_16_out, not_119_out, not_120_out, OP3, not_121_out, OP1, not_122_out);
  and and_17 (and_17_out, not_123_out, not_124_out, OP3, OP2, not_125_out, OP0);
  and and_18 (and_18_out, OP5, not_126_out, not_127_out, not_128_out, OP1, OP0);
  and and_19 (and_19_out, OP5, not_129_out, OP3, not_130_out, OP1, OP0);
  and and_20 (and_20_out, not_131_out, not_132_out, not_133_out, not_134_out, not_135_out, not_136_out, F5, not_137_out, not_138_out, not_139_out, F1, F0);
  and and_21 (and_21_out, not_140_out, not_141_out, not_142_out, not_143_out, not_144_out, not_145_out, F5, not_146_out, not_147_out, F2, F1, not_148_out);
  and and_22 (and_22_out, OP5, not_149_out, OP3, not_150_out, not_151_out, not_152_out);
  and and_23 (and_23_out, not_153_out, not_154_out, not_155_out, not_156_out, not_157_out, OP0);
  and and_24 (and_24_out, not_158_out, not_159_out, not_160_out, not_161_out, not_162_out, not_163_out, not_164_out, not_165_out, not_166_out, not_167_out, not_168_out, not_169_out);
  and and_25 (and_25_out, not_170_out, not_171_out, not_172_out, not_173_out, not_174_out, not_175_out, not_176_out, not_177_out, not_178_out, not_179_out, F1, F0);
  and and_26 (and_26_out, not_180_out, not_181_out, not_182_out, not_183_out, not_184_out, not_185_out, not_186_out, not_187_out, not_188_out, not_189_out, F1, not_190_out);
  and and_27 (and_27_out, not_191_out, not_192_out, not_193_out, not_194_out, not_195_out, not_196_out, F5, not_197_out, not_198_out, not_199_out, not_200_out, not_201_out);
  and and_28 (and_28_out, not_202_out, not_203_out, not_204_out, not_205_out, not_206_out, not_207_out, F5, not_208_out, not_209_out, not_210_out, not_211_out, F0);
  and and_29 (and_29_out, not_212_out, not_213_out, not_214_out, not_215_out, not_216_out, not_217_out, F5, not_218_out, not_219_out, not_220_out, F1, not_221_out);
  and and_30 (and_30_out, not_222_out, not_223_out, not_224_out, not_225_out, not_226_out, not_227_out, F5, not_228_out, not_229_out, F2, not_230_out, not_231_out);
  and and_31 (and_31_out, not_232_out, not_233_out, not_234_out, not_235_out, not_236_out, not_237_out, F5, not_238_out, not_239_out, F2, not_240_out, F0);
  and and_32 (and_32_out, not_241_out, not_242_out, not_243_out, not_244_out, not_245_out, not_246_out, F5, not_247_out, not_248_out, F2, F1, F0);
  and and_33 (and_33_out, not_249_out, not_250_out, not_251_out, not_252_out, not_253_out, not_254_out, F5, not_255_out, F3, not_256_out, F1, not_257_out);
  and and_34 (and_34_out, not_258_out, not_259_out, not_260_out, not_261_out, not_262_out, not_263_out, F5, not_264_out, F3, not_265_out, F1, F0);
  and and_35 (and_35_out, not_266_out, not_267_out, not_268_out, not_269_out, not_270_out, not_271_out, not_272_out, not_273_out, F3, F2, not_274_out, not_275_out);
  and and_36 (and_36_out, not_276_out, not_277_out, not_278_out, OP2, not_279_out, not_280_out);
  and and_37 (and_37_out, not_281_out, not_282_out, not_283_out, OP2, not_284_out, OP0);
  and and_38 (and_38_out, OP5, not_285_out, OP3, not_286_out, OP1, OP0);
  and and_39 (and_39_out, not_287_out, not_288_out, not_289_out, not_290_out, not_291_out, not_292_out, F5, not_293_out, not_294_out, not_295_out, F1, F0);
  and and_40 (and_40_out, not_296_out, not_297_out, not_298_out, not_299_out, not_300_out, not_301_out, F5, not_302_out, not_303_out, F2, F1, not_304_out);
  and and_41 (and_41_out, OP5, not_305_out, OP3, not_306_out, not_307_out, not_308_out);
  or or_1 (R1USED, and_1_out, and_2_out, and_3_out, and_4_out, and_5_out, and_6_out, and_7_out, and_8_out, and_9_out, and_10_out, and_11_out, and_12_out, and_13_out, and_14_out, and_15_out, and_16_out, and_17_out, and_18_out, and_19_out, and_20_out, and_21_out, and_22_out, and_23_out);
  or or_2 (R2USED, and_24_out, and_25_out, and_26_out, and_27_out, and_28_out, and_29_out, and_30_out, and_31_out, and_32_out, and_33_out, and_34_out, and_35_out, and_36_out, and_37_out, and_38_out, and_39_out, and_40_out, and_41_out);
endmodule

// 多级中断控制器
module Multistage_interrupt_control_logic (
  input  [5:0] OP,
  input  [5:0] Func,
  input  [4:0] MF,
  output MFC0,
  output MTC0
);

  and and_1 (MFC0, ~OP[0], ~OP[1], ~OP[2], ~OP[3], OP[4], ~OP[5], ~MF[0], ~MF[1], ~MF[2], ~MF[3], ~MF[4]);  // AND_Gate
  and and_2 (MTC0, ~OP[0], ~OP[1], ~OP[2], ~OP[3], OP[4], ~OP[5], ~MF[0], ~MF[1], MF[2], ~MF[3], ~MF[4]);  // AND_Gate

  // Other names for the same wires on the sheet: OP_CODE[5:0] = OP
endmodule

// ALU
module MIPS_ALU (
  input  [4:0] shamt,
  input  [31:0] X,
  input  [31:0] Y,
  input  [3:0] AluOP,
  output Equal,
  output [31:0] Result,
  output [31:0] Result_2
);

  wire [0:0] comparator_1_lt, comparator_2_lt;
  wire [31:0] adder_1_out, AND_out, divider_1_out, divider_1_rem, multiplier_1_cout, multiplier_1_out,
       NOR_out, OR_out, shifter_1_out, shifter_2_out, shifter_3_out, subtractor_1_out, XOR_out;

  assign AND_out = X & Y;  // AND_Gate AND, 32 bits wide
  assign OR_out = X | Y;  // OR_Gate OR, 32 bits wide
  Shifter #(.width(32), .shift("ll")) shifter_1 (.in(Y), .\dist (shamt), .out(shifter_1_out));
  Shifter #(.width(32), .shift("ar")) shifter_2 (.in(Y), .\dist (shamt), .out(shifter_2_out));
  Shifter #(.width(32), .shift("lr")) shifter_3 (.in(Y), .\dist (shamt), .out(shifter_3_out));
  Multiplier #(.width(32)) multiplier_1 (.a(X), .b(Y), .out(multiplier_1_out), .cout(multiplier_1_cout));  // open: cin
  Divider #(.width(32)) divider_1 (.a(X), .b(Y), .out(divider_1_out), .rem(divider_1_rem));  // open: upper
  Adder #(.width(32)) adder_1 (.a(X), .b(Y), .out(adder_1_out));  // open: cin, cout
  Subtractor #(.width(32)) subtractor_1 (.a(X), .b(Y), .out(subtractor_1_out));  // open: bin, bout
  assign XOR_out = X ^ Y;  // XOR_Gate XOR, 32 bits wide
  assign NOR_out = ~(X | Y);  // NOR_Gate NOR, 32 bits wide
  Comparator #(.width(32), .mode("twosComplement")) comparator_1 (
    .a(X), .b(Y), .eq(Equal), .lt(comparator_1_lt[0]));  // open: gt
  Comparator #(.width(32), .mode("unsigned")) comparator_2 (.a(X), .b(Y), .lt(comparator_2_lt[0]));  // open: gt, eq
  Multiplexer #(.select(4), .width(32), .disabled("Z"), .enable("false")) multiplexer_1 (
    .in0(shifter_1_out), .in1(shifter_2_out), .in2(shifter_3_out), .in3(multiplier_1_out),
    .in4(divider_1_out), .in5(adder_1_out), .in6(subtractor_1_out), .in7(AND_out), .in8(OR_out),
    .in9(XOR_out), .in10(NOR_out), .in11({{31{1'b0}}, comparator_1_lt[0]}),
    .in12({{31{1'b0}}, comparator_2_lt[0]}), .in13({32{1'b0}}), .in14({32{1'b0}}), .in15({32{1'b0}}),
    .out(Result), .sel(AluOP));
  Multiplexer #(.select(4), .width(32), .disabled("Z"), .enable("false")) multiplexer_2 (
    .in0({32{1'b0}}), .in1({32{1'b0}}), .in2({32{1'b0}}), .in3(multiplier_1_cout), .in4(divider_1_rem),
    .in5({32{1'b0}}), .in6({32{1'b0}}), .in7({32{1'b0}}), .in8({32{1'b0}}), .in9({32{1'b0}}),
    .in10({32{1'b0}}), .in11({32{1'b0}}), .in12({32{1'b0}}), .in13({32{1'b0}}), .in14({32{1'b0}}),
    .in15({32{1'b0}}), .out(Result_2), .sel(AluOP));

  // Other names for the same wires on the sheet: Result2[31:0] = Result_2; S[3:0] = AluOP

  // Notes on the sheet:
  //   不要改变此引脚区域内容，也不要改变ALU封装形式
  //   输入引脚
  //   输出引脚
endmodule

module MIPS_Regifile (
  input  [31:0] Din,
  input  Clk,
  input  WE,
  input  [4:0] R1_num,
  input  [4:0] W_num,
  input  [4:0] R2_num,
  output [31:0] R1,
  output [31:0] R2
);

  // RegisterFile registerfile_1: pin names not known; wires that end beside it: Din, Clk, WE, W_num, R1_num, R2_num, R1, R2
endmodule

module \理想流水线  (
  output RegWrite,
  output MemWrite,
  output [31:0] IF_PC,
  output [31:0] ID_PC,
  output [31:0] EX_PC,
  output [31:0] M_PC,
  output [31:0] WB_PC,
  output [31:0] RDin,
  output [31:0] MDin,
  output [31:0] LedData
);

  wire and_2_out, and_3_out, and_4_out, BGEZ, BGEZ_YES, CLK, clock_1_out, clock_2_out, comparator_1_eq,
       comparator_2_eq, comparator_2_lt, d_ff_1_q, ex_mem_1_halt_out, ex_mem_1_jal_out,
       ex_mem_1_memtoreg_out, ex_mem_1_regdst_out, ex_mem_1_regwrite_out, ex_mem_1_sb_out, Go, halt,
       id_ex_1_beq_out, id_ex_1_bne_out, id_ex_1_halt_out, id_ex_1_jal_out, id_ex_1_memtoreg_out,
       id_ex_1_memwrite_out, id_ex_1_regdst_out, id_ex_1_regwrite_out, id_ex_1_sb_out, IR1, IR2, IR3, LED,
       mem_wb_1_halt_out, mem_wb_1_jal_out, mem_wb_1_memtoreg_out, mem_wb_1_regdst_out, mips_alu_1_equal,
       nand_1_out, not_1_out, not_2_out, or_1_out, RST, W1, W2, W3, \单周期硬布线控制器_1_alu_src , \单周期硬布线控制器_1_beq ,
       \单周期硬布线控制器_1_bgez , \单周期硬布线控制器_1_bne , \单周期硬布线控制器_1_jal , \单周期硬布线控制器_1_jmp , \单周期硬布线控制器_1_jr ,
       \单周期硬布线控制器_1_memtoreg , \单周期硬布线控制器_1_memwrite , \单周期硬布线控制器_1_regdst , \单周期硬布线控制器_1_regwrite ,
       \单周期硬布线控制器_1_sb , \单周期硬布线控制器_1_signedext , \单周期硬布线控制器_1_syscall ;
  wire [1:0] id_ex_1_signedext_out;
  wire [2:0] or_2_out;
  wire [3:0] id_ex_1_aluop_out, \单周期硬布线控制器_1_alu_op ;
  wire [4:0] id_ex_1_shamt_out, if_id_1_ir_out_4, if_id_1_ir_out_5, if_id_1_ir_out_6, multiplexer_3_out,
       multiplexer_4_out, multiplexer_8_out, W_num;
  wire [5:0] if_id_1_ir_out, if_id_1_ir_out_2;
  wire [10:6] if_id_1_ir_out_3;
  wire [12:0] CNT_num;
  wire [15:0] id_ex_1_imm_out, \LoadUse次数 , \总周期数 , \插入气泡数 , \无条件分支数 , \条件分支成功数 ;
  wire [31:0] A0, adder_1_out, adder_2_out, bit_extender_1_out, bit_extender_2_out, EX_IR, ex_mem_1_alur_out,
       ex_mem_1_ir_out, ex_mem_1_pc_out, ex_mem_1_r2_out, id_ex_1_address_out, id_ex_1_ir_out,
       id_ex_1_pc_out, id_ex_1_r1_out, id_ex_1_r2_out, ID_IR, if_id_1_pc_out, IF_IR, IR, MEM_IR,
       mem_wb_1_alur_out, mem_wb_1_ir_out, mem_wb_1_memd_out, mem_wb_1_pc_out_2, mips_alu_1_result,
       mips_regifile_1_r1, mips_regifile_1_r2, multiplexer_1_out, multiplexer_2_out, multiplexer_5_out,
       multiplexer_6_out, multiplexer_9_out, ram_1_data, shifter_1_out, shifter_2_out, WB_IR;

  Button \u_总复位  (.out(RST));
  Button _1 (.out(IR1));
  Button _2 (.out(IR2));
  Button _3 (.out(IR3));
  Button \u_继续运行  (.out(Go));
  LED #(.active("true")) led_1 (.in(W1));
  LED #(.active("true")) led_2 (.in(W2));
  LED #(.active("true")) led_3 (.in(W3));
  Hex_Digit_Display hex_digit_display_1 (.value(LedData[31:28]));  // open: dp
  Hex_Digit_Display hex_digit_display_2 (.value(LedData[27:24]));  // open: dp
  Hex_Digit_Display hex_digit_display_3 (.value(LedData[23:20]));  // open: dp
  Hex_Digit_Display hex_digit_display_4 (.value(LedData[19:16]));  // open: dp
  Hex_Digit_Display hex_digit_display_5 (.value(LedData[15:12]));  // open: dp
  Multiplexer #(.select(3), .width(32), .disabled("Z"), .enable("false")) multiplexer_1 (
    .in0(adder_1_out), .in1(adder_2_out), .in2(id_ex_1_address_out), .in6(id_ex_1_r1_out),
    .out(multiplexer_1_out), .sel(or_2_out));  // open: in3, in4, in5, in7
  Hex_Digit_Display hex_digit_display_6 (.value(LedData[7:4]));  // open: dp
  Hex_Digit_Display hex_digit_display_7 (.value(LedData[11:8]));  // open: dp
  Clock #(.highDuration(1), .lowDuration(1)) clock_1 (.out(clock_1_out));
  Multiplexer #(.select(2), .width(32), .disabled("Z"), .enable("false")) multiplexer_2 (
    .in0(multiplexer_1_out), .in1(multiplexer_1_out), .in2(adder_1_out), .in3(adder_2_out),
    .out(multiplexer_2_out), .sel({BGEZ, BGEZ_YES}));
  or or_1 (or_1_out, halt, Go);
  Hex_Digit_Display hex_digit_display_8 (.value(LedData[3:0]));  // open: dp
  Register #(.width(32), .trigger("rising"), .Select("low")) PC (
    .D(multiplexer_2_out), .en(or_1_out), .Q(IF_PC), .clk(CLK), .clr(RST));
  Counter #(.width(16), .max('hffff), .ongoal("wrap"), .trigger("rising"), .behavior("new")) counter_1 (
    .count(or_1_out), .Q(\总周期数 ), .clk(CLK), .clr(RST));  // open: load, D, carry, preset, down
  // Probe on \总周期数 
  Register #(.width(32), .trigger("rising"), .Select("low")) register_1 (
    .D(A0), .en(LED), .Q(LedData), .clk(CLK), .clr(RST));
  // Probe on \总周期数 
  // Probe on \无条件分支数 
  // Probe on \条件分支成功数 
  // Probe on \插入气泡数 
  // Probe on \LoadUse次数 
  // Probe on IF_PC[11:0]
  // Mips_Probe mips_probe_1: pin names not known; wires that end beside it: IR
  ROM #(.addrWidth(10), .dataWidth(32), .Select("high")) rom_1 (.addr(IF_PC[11:2]), .data(IR));
  Adder #(.width(32)) adder_1 (.a(IF_PC), .b(32'h4), .out(adder_1_out));  // open: cin, cout
  // Probe on EX_PC[11:0]
  // Probe on ID_PC[11:0]
  // Probe on M_PC[11:0]
  IF_ID if_id_1 (
    .PC_in(adder_1_out), .IR_in(IR), .CLK(CLK), .PC_out(if_id_1_pc_out),
    .IR_out({if_id_1_ir_out, if_id_1_ir_out_6, if_id_1_ir_out_5, if_id_1_ir_out_4, if_id_1_ir_out_3, if_id_1_ir_out_2}),
    .RST(RST), .Enable(halt), .PCb_in(IF_PC), .PCb_out(ID_PC));
  // Probe on WB_PC[11:0]
  \单周期硬布线控制器  \u_单周期硬布线控制器_1  (
    .Func(if_id_1_ir_out_2), .OP(if_id_1_ir_out), .ALU_OP(\单周期硬布线控制器_1_alu_op ),
    .MemToReg(\单周期硬布线控制器_1_memtoreg ), .MemWrite(\单周期硬布线控制器_1_memwrite ), .ALU_SRC(\单周期硬布线控制器_1_alu_src ),
    .RegWrite(\单周期硬布线控制器_1_regwrite ), .SysCALL(\单周期硬布线控制器_1_syscall ), .SignedExt(\单周期硬布线控制器_1_signedext ),
    .RegDst(\单周期硬布线控制器_1_regdst ), .JR(\单周期硬布线控制器_1_jr ), .JMP(\单周期硬布线控制器_1_jmp ), .Beq(\单周期硬布线控制器_1_beq ),
    .JAL(\单周期硬布线控制器_1_jal ), .Bne(\单周期硬布线控制器_1_bne ), .BGEZ(\单周期硬布线控制器_1_bgez ), .SB(\单周期硬布线控制器_1_sb ));  // open: ERET
  Multiplexer #(.select(1), .width(5), .disabled("Z"), .enable("false")) multiplexer_3 (
    .in0(if_id_1_ir_out_6), .in1(5'b00010), .out(multiplexer_3_out), .sel(\单周期硬布线控制器_1_syscall ));
  Multiplexer #(.select(1), .width(5), .disabled("Z"), .enable("false")) multiplexer_4 (
    .in0(if_id_1_ir_out_5), .in1(5'b00100), .out(multiplexer_4_out), .sel(\单周期硬布线控制器_1_syscall ));
  MIPS_Regifile mips_regifile_1 (
    .Din(RDin), .Clk(CLK), .R1(mips_regifile_1_r1), .R2(mips_regifile_1_r2), .WE(RegWrite), .W_num(W_num),
    .R1_num(multiplexer_3_out), .R2_num(multiplexer_4_out));
  Comparator #(.width(32), .mode("twosComplement")) comparator_1 (
    .a(mips_regifile_1_r1), .b(32'h22), .eq(comparator_1_eq));  // open: gt, lt
  not not_1 (not_1_out, comparator_1_eq);
  and and_1 (LED, \单周期硬布线控制器_1_syscall , comparator_1_eq);
  and and_2 (and_2_out, \单周期硬布线控制器_1_syscall , not_1_out);
  ID_EX id_ex_1 (
    .IR_in({if_id_1_ir_out, if_id_1_ir_out_6, if_id_1_ir_out_5, if_id_1_ir_out_4, if_id_1_ir_out_3, if_id_1_ir_out_2}),
    .PC_in(if_id_1_pc_out), .BEQ_in(\单周期硬布线控制器_1_beq ), .R1_in(mips_regifile_1_r1),
    .BNE_in(\单周期硬布线控制器_1_bne ), .MemToReg_in(\单周期硬布线控制器_1_memtoreg ), .R2_in(mips_regifile_1_r2),
    .MemWrite_in(\单周期硬布线控制器_1_memwrite ), .Imm_in({if_id_1_ir_out_4, if_id_1_ir_out_3, if_id_1_ir_out_2}),
    .AluSrcB_in(\单周期硬布线控制器_1_alu_src ),
    .Address_in({if_id_1_pc_out[31:28], if_id_1_ir_out_6, if_id_1_ir_out_5, if_id_1_ir_out_4, if_id_1_ir_out_3, if_id_1_ir_out_2, 2'b00}),
    .RegWrite_in(\单周期硬布线控制器_1_regwrite ), .AluOP_in(\单周期硬布线控制器_1_alu_op ), .JAL_in(\单周期硬布线控制器_1_jal ),
    .Shamt_in(if_id_1_ir_out_3), .RegDst_in(\单周期硬布线控制器_1_regdst ), .Halt_in(and_2_out),
    .SB_in(\单周期硬布线控制器_1_sb ), .JMP_in(\单周期硬布线控制器_1_jmp ), .BGEZ_in(\单周期硬布线控制器_1_bgez ),
    .JR_in(\单周期硬布线控制器_1_jr ), .CLK(CLK), .IR_out(id_ex_1_ir_out), .PC_out(id_ex_1_pc_out),
    .BEQ_out(id_ex_1_beq_out), .R1_out(id_ex_1_r1_out), .BNE_out(id_ex_1_bne_out),
    .MemToReg_out(id_ex_1_memtoreg_out), .R2_out(id_ex_1_r2_out), .MemWrite_out(id_ex_1_memwrite_out),
    .Imm_out(id_ex_1_imm_out), .AluSrcB_out(id_ex_1_signedext_out[1]), .Address_out(id_ex_1_address_out),
    .RegWrite_out(id_ex_1_regwrite_out), .AluOP_out(id_ex_1_aluop_out), .JAL_out(id_ex_1_jal_out),
    .Shamt_out(id_ex_1_shamt_out), .RegDst_out(id_ex_1_regdst_out), .Halt_out(id_ex_1_halt_out),
    .SB_out(id_ex_1_sb_out), .JMP_out(or_2_out[1]), .BGEZ_out(BGEZ), .JR_out(or_2_out[2]), .RST(RST),
    .Enable(halt), .SignedEXT_in(\单周期硬布线控制器_1_signedext ), .SignedEXT_out(id_ex_1_signedext_out[0]),
    .PCb_in(ID_PC), .PCb_out(EX_PC));  // open: W__in, W__out, SYSCALL, SYSCALL_2, CHANGE_MEM_OR_RAM_in, CHANGE_MEM_OR_RAM_out
  not not_2 (not_2_out, mips_alu_1_equal);
  assign bit_extender_1_out = {{16{1'b0}}, id_ex_1_imm_out};  // Bit_Extender bit_extender_1
  assign bit_extender_2_out = {{16{id_ex_1_imm_out[15]}}, id_ex_1_imm_out};  // Bit_Extender bit_extender_2
  and and_3 (and_3_out, id_ex_1_beq_out, mips_alu_1_equal);
  or or_2 (or_2_out[0], and_3_out, and_4_out);
  and and_4 (and_4_out, id_ex_1_bne_out, not_2_out);
  Multiplexer #(.select(2), .width(32), .disabled("Z"), .enable("false")) multiplexer_5 (
    .in0(id_ex_1_r2_out), .in1(id_ex_1_r2_out), .in2(bit_extender_1_out), .in3(bit_extender_2_out),
    .out(multiplexer_5_out), .sel(id_ex_1_signedext_out));
  Shifter #(.width(32), .shift("ll")) shifter_1 (.in(bit_extender_2_out), .\dist (5'b00010), .out(shifter_1_out));
  Multiplexer #(.select(1), .width(32), .disabled("Z"), .enable("false")) multiplexer_6 (
    .in0(multiplexer_5_out), .in1({32{1'b0}}), .out(multiplexer_6_out), .sel(BGEZ));
  Adder #(.width(32)) adder_2 (.a(shifter_1_out), .b(id_ex_1_pc_out), .out(adder_2_out));  // open: cin, cout
  MIPS_ALU mips_alu_1 (
    .X(id_ex_1_r1_out), .Y(multiplexer_6_out), .AluOP(id_ex_1_aluop_out), .Equal(mips_alu_1_equal),
    .Result(mips_alu_1_result), .shamt(id_ex_1_shamt_out));  // open: Result_2
  not not_3 (BGEZ_YES, mips_alu_1_result[0]);
  EX_MEM ex_mem_1 (
    .MemToReg_in(id_ex_1_memtoreg_out), .IR_in(id_ex_1_ir_out), .MemWrite_in(id_ex_1_memwrite_out),
    .PC_in(id_ex_1_pc_out), .RegWrite_in(id_ex_1_regwrite_out), .R2_in(id_ex_1_r2_out),
    .JAL_in(id_ex_1_jal_out), .AluR_in(mips_alu_1_result), .RegDst_in(id_ex_1_regdst_out),
    .Halt_in(id_ex_1_halt_out), .SB_in(id_ex_1_sb_out), .CLK(CLK), .MemToReg_out(ex_mem_1_memtoreg_out),
    .IR_out(ex_mem_1_ir_out), .MemWrite_out(MemWrite), .PC_out(ex_mem_1_pc_out),
    .RegWrite_out(ex_mem_1_regwrite_out), .R2_out(ex_mem_1_r2_out), .JAL_out(ex_mem_1_jal_out),
    .AluR_out(ex_mem_1_alur_out), .RegDst_out(ex_mem_1_regdst_out), .Halt_out(ex_mem_1_halt_out),
    .SB_out(ex_mem_1_sb_out), .RST(RST), .Enable(halt), .PCb_in(EX_PC), .PCb_out(M_PC));  // open: W__in, W__out, CHANGE_MEM_OR_RAM_in, CHANGE_MEM_OR_RAM_out
  // Probe on \总周期数 
  // Probe on \总周期数 
  Shifter #(.width(32), .shift("ll")) shifter_2 (.in(ram_1_data), .\dist (5'b01000), .out(shifter_2_out));
  // Probe on IF_PC[19:0]
  // Mips_Probe mips_probe_2: pin names not known; wires that end beside it: IF_IR
  Multiplexer #(.select(1), .width(32), .disabled("Z"), .enable("false")) multiplexer_7 (
    .in0(ex_mem_1_r2_out), .in1({shifter_2_out[31:8], ex_mem_1_r2_out[7:0]}), .out(MDin),
    .sel(ex_mem_1_sb_out));
  // Probe on ID_PC[19:0]
  // Mips_Probe mips_probe_3: pin names not known; wires that end beside it: ID_IR
  // Mips_Probe mips_probe_4: pin names not known; wires that end beside it: EX_IR
  RAM #(.addrWidth(10), .dataWidth(32), .bus("separate"), .Select("high")) ram_1 (
    .addr(ex_mem_1_alur_out[11:2]), .din(MDin), .data(ram_1_data), .str(MemWrite), .clk(CLK), .clr(RST));  // open: sel, ld
  // Probe on EX_PC[19:0]
  // Probe on M_PC[19:0]
  // Mips_Probe mips_probe_5: pin names not known; wires that end beside it: MEM_IR
  MEM_WB mem_wb_1 (
    .MemToReg_in(ex_mem_1_memtoreg_out), .IR_in(ex_mem_1_ir_out), .RegWrite_in(ex_mem_1_regwrite_out),
    .PC_in(ex_mem_1_pc_out), .JAL_in(ex_mem_1_jal_out), .MemD_in(ram_1_data),
    .RegDst_in(ex_mem_1_regdst_out), .AluR_in(ex_mem_1_alur_out), .Halt_in(ex_mem_1_halt_out), .CLK(CLK),
    .MemToReg_out(mem_wb_1_memtoreg_out), .IR_out(mem_wb_1_ir_out), .RegWrite_out(RegWrite),
    .PC_out_2(mem_wb_1_pc_out_2), .JAL_out(mem_wb_1_jal_out), .MemD_out(mem_wb_1_memd_out),
    .RegDst_out(mem_wb_1_regdst_out), .AluR_out(mem_wb_1_alur_out), .Halt_out(mem_wb_1_halt_out), .RST(RST),
    .Enable(halt), .PCb_in(M_PC), .PC_out(WB_PC));  // open: W__in, W__out, CHANGE_MEM_OR_RAM_in, CHANGE_MEM_OR_RAM_out
  Multiplexer #(.select(1), .width(5), .disabled("Z"), .enable("false")) multiplexer_8 (
    .in0(mem_wb_1_ir_out[20:16]), .in1(mem_wb_1_ir_out[15:11]), .out(multiplexer_8_out),
    .sel(mem_wb_1_regdst_out));
  not not_4 (halt, mem_wb_1_halt_out);
  Multiplexer #(.select(1), .width(32), .disabled("Z"), .enable("false")) multiplexer_9 (
    .in0(mem_wb_1_alur_out), .in1(mem_wb_1_memd_out), .out(multiplexer_9_out), .sel(mem_wb_1_memtoreg_out));
  Multiplexer #(.select(1), .width(32), .disabled("Z"), .enable("false")) multiplexer_10 (
    .in0(multiplexer_9_out), .in1(mem_wb_1_pc_out_2), .out(RDin), .sel(mem_wb_1_jal_out));
  // Probe on WB_PC[19:0]
  // Mips_Probe mips_probe_6: pin names not known; wires that end beside it: WB_IR
  Multiplexer #(.select(1), .width(5), .disabled("Z"), .enable("false")) multiplexer_11 (
    .in0(multiplexer_8_out), .in1({5{1'b1}}), .out(W_num), .sel(mem_wb_1_jal_out));
  D_Flip_Flop #(.trigger("high"), .Pre_Clr_Positions("LEGACY"), .NegatePresetClear("false"), .enable("true"), .NewFFLayout("false")) d_ff_1 (.Q(d_ff_1_q));  // open: clk, D, Qn, preset, en, reset
  // Probe on 13'hc
  Clock #(.highDuration(1), .lowDuration(1)) clock_2 (.out(clock_2_out));
  Comparator #(.width(13), .mode("twosComplement")) comparator_2 (
    .a(CNT_num), .b(13'hc), .eq(comparator_2_eq), .lt(comparator_2_lt));  // open: gt
  nand nand_1 (nand_1_out, d_ff_1_q, comparator_2_eq);
  Counter #(.width(13), .max('h1fff), .ongoal("stay"), .trigger("rising"), .behavior("old")) counter_2 (
    .count(comparator_2_lt), .Q(CNT_num), .clk(clock_2_out));  // open: load, D, carry, clr, preset
  assign CLK = nand_1_out ? clock_2_out : 1'bz;  // Controlled_Buffer controlled_buffer_1
  Pull_Resistor #(.pull(1)) pull_resistor_1 (.node(CLK));

  // Other names for the same wires on the sheet: MEM_PC[31:0] = M_PC; PC[31:0] = IF_PC; RW = RegWrite

  // Notes on the sheet:
  //   中断源
  //   中断等待指示
  //   PC-JR
  //   PC+4
  //   PC+imm
  //   PC-J
  //   数码管输出
  //   指令存储器
  //   指令字
  //   contents of rom_1 (hex, n*v repeats v):
  //   20100000 20110000 20120000 20130000 36100000 36310001 36520002 36730003 ae100000 ae110004 ae120008
  //   ae13000c 2002000a 20110000 20120000 20130000 c
  //   JR
  //   JMP
  //   JMP+IF
  //   流水调试日志用
  //   IR
  //   OP
  //   Func
  //   rs
  //   rt
  //   rd
  //   addr
  //   imm
  //   shamt
  //   JMP
  //   JR
  //   SignedEXT
  //   BGEZ
  //   SB
  //   OP
  //   Func
  //   Beq
  //   Bne
  //   MemToReg
  //   MemWrite
  //   AluOP
  //   AluSrcB
  //   RegWrite
  //   JAL
  //   RegDst
  //   Syscall
  //   为方便自动评测，需要输出流水线各段保存的PC值，注意是PC不是PC+4，另外ID段寄存器写入信息，Mem段内存写入信息也要输出
  //   JMP+IF
  //   时空图监测，可删除
  //   rt
  //   rd
  //   ctrl+k关闭时钟连续运行，将控制位置零，进入单步调试模式调试
  //   用这个时钟源需要去掉电路中的其他时钟源
  //   W#
  //   控制位
  //   暂停节拍，不能为0
  //   戳工具置1进入计数暂停模式，ctrl+k时钟自动运行到对应节拍暂停
  //   可计数暂停的时钟源
endmodule
module \气泡流水线  (
  output RegWrite,
  output MemWrite,
  output [31:0] IF_PC,
  output [31:0] ID_PC,
  output [31:0] EX_PC,
  output [31:0] M_PC,
  output [31:0] WB_PC,
  output [31:0] RDin,
  output [31:0] MDin,
  output [31:0] LedData
);

  wire AddBubble, ALL_JUMP, and_1_out, and_2_out, and_4_out, and_5_out, and_6_out, and_7_out, BGEZ, BGEZ_YES,
       CLK, clock_2_out, comparator_1_eq, comparator_1_lt, comparator_2_eq, d_ff_1_q, ex_mem_1_halt_out,
       ex_mem_1_jal_out, ex_mem_1_memtoreg_out, ex_mem_1_regdst_out, ex_mem_1_sb_out, EX_Regwrite, Go, halt,
       id_ex_1_beq_out, id_ex_1_bne_out, id_ex_1_halt_out, id_ex_1_jal_out, id_ex_1_memtoreg_out,
       id_ex_1_memwrite_out, id_ex_1_regdst_out, id_ex_1_sb_out, ID_JAL, ID_RDst, IR1, IR2, IR3, LED,
       MEM_Regwrite, mem_wb_1_halt_out, mem_wb_1_jal_out, mem_wb_1_memtoreg_out, mem_wb_1_regdst_out,
       mips_alu_1_equal, nand_1_out, not_1_out, not_2_out, not_3_out, not_4_out, not_6_out, not_7_out,
       or_1_out, or_2_out, RST, W1, W2, W3, \单周期硬布线控制器_1_alu_src , \单周期硬布线控制器_1_beq , \单周期硬布线控制器_1_bgez ,
       \单周期硬布线控制器_1_bne , \单周期硬布线控制器_1_jmp , \单周期硬布线控制器_1_jr , \单周期硬布线控制器_1_memtoreg ,
       \单周期硬布线控制器_1_memwrite , \单周期硬布线控制器_1_regwrite , \单周期硬布线控制器_1_sb , \单周期硬布线控制器_1_signedext ,
       \单周期硬布线控制器_1_syscall ;
  wire [1:0] id_ex_1_signedext_out;
  wire [2:0] or_3_out;
  wire [3:0] id_ex_1_aluop_out, \单周期硬布线控制器_1_alu_op ;
  wire [4:0] EX_W_num, id_ex_1_shamt_out, ID_R1_num, ID_R2_num, MEM_W_num, multiplexer_3_out,
       multiplexer_6_out, multiplexer_11_out, W_num;
  wire [5:0] ID_FUNC, ID_OP;
  wire [12:0] CNT_num;
  wire [15:0] id_ex_1_imm_out, \LoadUse次数 , \总周期数 , \插入气泡数 , \无条件分支数 , \条件分支成功数 ;
  wire [27:8] if_id_1_ir_out;
  wire [31:0] A0, adder_1_out, adder_2_out, bit_extender_1_out, bit_extender_2_out, EX_IR, ex_mem_1_alur_out,
       ex_mem_1_ir_out, ex_mem_1_pc_out, ex_mem_1_r2_out, id_ex_1_address_out, id_ex_1_ir_out,
       id_ex_1_pc_out, id_ex_1_r1_out, id_ex_1_r2_out, ID_IR, if_id_1_pc_out, IF_IR, IR, MEM_IR,
       mem_wb_1_alur_out, mem_wb_1_ir_out, mem_wb_1_memd_out, mem_wb_1_pc_out_2, mips_alu_1_result,
       mips_regifile_1_r1, multiplexer_1_out, multiplexer_2_out, multiplexer_7_out, multiplexer_8_out,
       multiplexer_10_out, ram_1_data, shifter_1_out, shifter_2_out, WB_IR;

  Button \u_总复位  (.out(RST));
  Button _1 (.out(IR1));
  Button _2 (.out(IR2));
  Button _3 (.out(IR3));
  // Probe on \总周期数 
  // Probe on \总周期数 
  Button \u_继续运行  (.out(Go));
  LED #(.active("true")) led_1 (.in(W1));
  LED #(.active("true")) led_2 (.in(W2));
  LED #(.active("true")) led_3 (.in(W3));
  Hex_Digit_Display hex_digit_display_1 (.value(LedData[31:28]));  // open: dp
  // Probe on IF_PC[19:0]
  // Mips_Probe mips_probe_1: pin names not known; wires that end beside it: IF_IR
  Hex_Digit_Display hex_digit_display_2 (.value(LedData[27:24]));  // open: dp
  Hex_Digit_Display hex_digit_display_3 (.value(LedData[23:20]));  // open: dp
  Multiplexer #(.select(3), .width(32), .disabled("Z"), .enable("false")) multiplexer_1 (
    .in0(adder_1_out), .in1(adder_2_out), .in2(id_ex_1_address_out), .in6(id_ex_1_r1_out),
    .out(multiplexer_1_out), .sel(or_3_out));  // open: in3, in4, in5, in7
  // Probe on ID_PC[19:0]
  // Mips_Probe mips_probe_2: pin names not known; wires that end beside it: ID_IR
  Hex_Digit_Display hex_digit_display_4 (.value(LedData[19:16]));  // open: dp
  Hex_Digit_Display hex_digit_display_5 (.value(LedData[15:12]));  // open: dp
  not not_1 (not_1_out, AddBubble);
  Hex_Digit_Display hex_digit_display_6 (.value(LedData[7:4]));  // open: dp
  Hex_Digit_Display hex_digit_display_7 (.value(LedData[11:8]));  // open: dp
  Clock #(.highDuration(1), .lowDuration(1)) clock_1 ();  // open: out
  Register #(.width(32), .trigger("rising"), .Select("low")) PC (
    .D(multiplexer_2_out), .en(and_1_out), .Q(IF_PC), .clk(CLK), .clr(RST));
  Multiplexer #(.select(2), .width(32), .disabled("Z"), .enable("false")) multiplexer_2 (
    .in0(multiplexer_1_out), .in1(multiplexer_1_out), .in2(adder_1_out), .in3(adder_2_out),
    .out(multiplexer_2_out), .sel({BGEZ, BGEZ_YES}));
  and and_1 (and_1_out, not_1_out, halt);
  Counter #(.width(16), .max('hffff), .ongoal("wrap"), .trigger("rising"), .behavior("new")) counter_1 (
    .count(halt), .Q(\总周期数 ), .clk(CLK), .clr(RST));  // open: load, D, carry, preset, down
  // Probe on EX_PC[19:0]
  // Mips_Probe mips_probe_3: pin names not known; wires that end beside it: EX_IR
  Hex_Digit_Display hex_digit_display_8 (.value(LedData[3:0]));  // open: dp
  Register #(.width(32), .trigger("rising"), .Select("low")) register_1 (
    .D(A0), .en(LED), .Q(LedData), .clk(CLK), .clr(RST));
  // Probe on \总周期数 
  // Probe on M_PC[19:0]
  // Mips_Probe mips_probe_4: pin names not known; wires that end beside it: MEM_IR
  // Probe on \总周期数 
  // Probe on \无条件分支数 
  // Probe on \条件分支成功数 
  // Probe on \插入气泡数 
  // Probe on \LoadUse次数 
  ROM #(.addrWidth(10), .dataWidth(32), .Select("high")) rom_1 (.addr(IF_PC[11:2]), .data(IR));
  Adder #(.width(32)) adder_1 (.a(IF_PC), .b(32'h4), .out(adder_1_out));  // open: cin, cout
  // Probe on IF_PC[11:0]
  // Mips_Probe mips_probe_5: pin names not known; wires that end beside it: IR
  // Probe on WB_PC[19:0]
  // Mips_Probe mips_probe_6: pin names not known; wires that end beside it: WB_IR
  // Probe on ID_PC[11:0]
  // Probe on EX_PC[11:0]
  or or_1 (or_1_out, RST, ALL_JUMP);
  IF_ID if_id_1 (
    .PC_in(adder_1_out), .IR_in(IR), .CLK(CLK), .PC_out(if_id_1_pc_out),
    .IR_out({ID_OP, if_id_1_ir_out, ID_FUNC}), .RST(or_1_out), .Enable(and_2_out), .PCb_in(IF_PC),
    .PCb_out(ID_PC));
  // Probe on M_PC[11:0]
  not not_2 (not_2_out, AddBubble);
  and and_2 (and_2_out, not_2_out, halt);
  D_Flip_Flop #(.trigger("high"), .Pre_Clr_Positions("LEGACY"), .NegatePresetClear("false"), .enable("true"), .NewFFLayout("false")) d_ff_1 (.Q(d_ff_1_q));  // open: clk, D, Qn, preset, en, reset
  // Probe on 13'hc
  // Probe on WB_PC[11:0]
  Multiplexer #(.select(1), .width(5), .disabled("Z"), .enable("false")) multiplexer_3 (
    .in0(if_id_1_ir_out[22:18]), .in1(if_id_1_ir_out[17:13]), .out(multiplexer_3_out), .sel(ID_RDst));
  Comparator #(.width(13), .mode("twosComplement")) comparator_1 (
    .a(CNT_num), .b(13'hc), .eq(comparator_1_eq), .lt(comparator_1_lt));  // open: gt
  Clock #(.highDuration(1), .lowDuration(1)) clock_2 (.out(clock_2_out));
  \单周期硬布线控制器  \u_单周期硬布线控制器_1  (
    .Func(ID_FUNC), .OP(ID_OP), .ALU_OP(\单周期硬布线控制器_1_alu_op ), .MemToReg(\单周期硬布线控制器_1_memtoreg ),
    .MemWrite(\单周期硬布线控制器_1_memwrite ), .ALU_SRC(\单周期硬布线控制器_1_alu_src ), .RegWrite(\单周期硬布线控制器_1_regwrite ),
    .SysCALL(\单周期硬布线控制器_1_syscall ), .SignedExt(\单周期硬布线控制器_1_signedext ), .RegDst(ID_RDst),
    .JR(\单周期硬布线控制器_1_jr ), .JMP(\单周期硬布线控制器_1_jmp ), .Beq(\单周期硬布线控制器_1_beq ), .JAL(ID_JAL),
    .Bne(\单周期硬布线控制器_1_bne ), .BGEZ(\单周期硬布线控制器_1_bgez ), .SB(\单周期硬布线控制器_1_sb ));  // open: ERET
  Multiplexer #(.select(1), .width(5), .disabled("Z"), .enable("false")) multiplexer_4 (
    .in0(if_id_1_ir_out[27:23]), .in1(5'b00010), .out(ID_R1_num), .sel(\单周期硬布线控制器_1_syscall ));
  Multiplexer #(.select(1), .width(5), .disabled("Z"), .enable("false")) multiplexer_5 (
    .in0(if_id_1_ir_out[22:18]), .in1(5'b00100), .out(ID_R2_num), .sel(\单周期硬布线控制器_1_syscall ));
  Multiplexer #(.select(1), .width(5), .disabled("Z"), .enable("false")) multiplexer_6 (
    .in0(multiplexer_3_out), .in1({5{1'b1}}), .out(multiplexer_6_out), .sel(ID_JAL));
  nand nand_1 (nand_1_out, d_ff_1_q, comparator_1_eq);
  Counter #(.width(13), .max('h1fff), .ongoal("stay"), .trigger("rising"), .behavior("old")) counter_2 (
    .count(comparator_1_lt), .Q(CNT_num), .clk(clock_2_out));  // open: load, D, carry, clr, preset
  MIPS_Regifile mips_regifile_1 (
    .Din(RDin), .Clk(CLK), .R1(mips_regifile_1_r1), .R2(A0), .WE(RegWrite), .W_num(W_num),
    .R1_num(ID_R1_num), .R2_num(ID_R2_num));
  assign CLK = nand_1_out ? clock_2_out : 1'bz;  // Controlled_Buffer controlled_buffer_1
  Pull_Resistor #(.pull(1)) pull_resistor_1 (.node(CLK));
  Comparator #(.width(32), .mode("twosComplement")) comparator_2 (
    .a(mips_regifile_1_r1), .b(32'h22), .eq(comparator_2_eq));  // open: gt, lt
  and and_3 (LED, \单周期硬布线控制器_1_syscall , comparator_2_eq);
  and and_4 (and_4_out, \单周期硬布线控制器_1_syscall , not_3_out);
  not not_3 (not_3_out, comparator_2_eq);
  or or_2 (or_2_out, RST, ALL_JUMP, AddBubble);
  ID_EX id_ex_1 (
    .IR_in({ID_OP, if_id_1_ir_out, ID_FUNC}), .PC_in(if_id_1_pc_out), .BEQ_in(\单周期硬布线控制器_1_beq ),
    .R1_in(mips_regifile_1_r1), .BNE_in(\单周期硬布线控制器_1_bne ), .MemToReg_in(\单周期硬布线控制器_1_memtoreg ), .R2_in(A0),
    .MemWrite_in(\单周期硬布线控制器_1_memwrite ), .Imm_in({if_id_1_ir_out[17:8], ID_FUNC}),
    .AluSrcB_in(\单周期硬布线控制器_1_alu_src ), .Address_in({if_id_1_pc_out[31:28], if_id_1_ir_out, ID_FUNC, 2'b00}),
    .RegWrite_in(\单周期硬布线控制器_1_regwrite ), .AluOP_in(\单周期硬布线控制器_1_alu_op ), .JAL_in(ID_JAL),
    .Shamt_in(if_id_1_ir_out[12:8]), .RegDst_in(ID_RDst), .Halt_in(and_4_out), .SB_in(\单周期硬布线控制器_1_sb ),
    .JMP_in(\单周期硬布线控制器_1_jmp ), .BGEZ_in(\单周期硬布线控制器_1_bgez ), .W__in(multiplexer_6_out),
    .JR_in(\单周期硬布线控制器_1_jr ), .CLK(CLK), .IR_out(id_ex_1_ir_out), .PC_out(id_ex_1_pc_out),
    .BEQ_out(id_ex_1_beq_out), .R1_out(id_ex_1_r1_out), .BNE_out(id_ex_1_bne_out),
    .MemToReg_out(id_ex_1_memtoreg_out), .R2_out(id_ex_1_r2_out), .MemWrite_out(id_ex_1_memwrite_out),
    .Imm_out(id_ex_1_imm_out), .AluSrcB_out(id_ex_1_signedext_out[1]), .Address_out(id_ex_1_address_out),
    .RegWrite_out(EX_Regwrite), .AluOP_out(id_ex_1_aluop_out), .JAL_out(id_ex_1_jal_out),
    .Shamt_out(id_ex_1_shamt_out), .RegDst_out(id_ex_1_regdst_out), .Halt_out(id_ex_1_halt_out),
    .SB_out(id_ex_1_sb_out), .JMP_out(or_3_out[1]), .BGEZ_out(BGEZ), .W__out(EX_W_num), .JR_out(or_3_out[2]),
    .RST(or_2_out), .Enable(halt), .SignedEXT_in(\单周期硬布线控制器_1_signedext ),
    .SignedEXT_out(id_ex_1_signedext_out[0]), .PCb_in(ID_PC), .PCb_out(EX_PC));  // open: SYSCALL, SYSCALL_2, CHANGE_MEM_OR_RAM_in, CHANGE_MEM_OR_RAM_out
  Correlation_detection_logic correlation_detection_logic_1 (
    .ID_OP(ID_OP), .ID_FUNC(ID_FUNC), .ID_R1_num(ID_R1_num), .ID_R2_num(ID_R2_num), .EX_W_num(EX_W_num),
    .MEM_W_num(MEM_W_num), .EX_RegWrite(EX_Regwrite), .MEM_RegWrite(MEM_Regwrite), .NEED_BUBBLE(AddBubble));
  and and_5 (and_5_out, id_ex_1_beq_out, mips_alu_1_equal);
  and and_6 (and_6_out, id_ex_1_bne_out, not_4_out);
  not not_4 (not_4_out, mips_alu_1_equal);
  assign bit_extender_1_out = {{16{1'b0}}, id_ex_1_imm_out};  // Bit_Extender bit_extender_1
  assign bit_extender_2_out = {{16{id_ex_1_imm_out[15]}}, id_ex_1_imm_out};  // Bit_Extender bit_extender_2
  or or_3 (or_3_out[0], and_5_out, and_6_out);
  Multiplexer #(.select(2), .width(32), .disabled("Z"), .enable("false")) multiplexer_7 (
    .in0(id_ex_1_r2_out), .in1(id_ex_1_r2_out), .in2(bit_extender_1_out), .in3(bit_extender_2_out),
    .out(multiplexer_7_out), .sel(id_ex_1_signedext_out));
  Multiplexer #(.select(1), .width(32), .disabled("Z"), .enable("false")) multiplexer_8 (
    .in0(multiplexer_7_out), .in1({32{1'b0}}), .out(multiplexer_8_out), .sel(BGEZ));
  Adder #(.width(32)) adder_2 (.a(shifter_1_out), .b(id_ex_1_pc_out), .out(adder_2_out));  // open: cin, cout
  Shifter #(.width(32), .shift("ll")) shifter_1 (.in(bit_extender_2_out), .\dist (5'b00010), .out(shifter_1_out));
  MIPS_ALU mips_alu_1 (
    .X(id_ex_1_r1_out), .Y(multiplexer_8_out), .AluOP(id_ex_1_aluop_out), .Equal(mips_alu_1_equal),
    .Result(mips_alu_1_result), .shamt(id_ex_1_shamt_out));  // open: Result_2
  not not_5 (BGEZ_YES, mips_alu_1_result[0]);
  not not_6 (not_6_out, mips_alu_1_result[0]);
  and and_7 (and_7_out, not_6_out, BGEZ);
  or or_4 (ALL_JUMP, or_3_out[2], or_3_out[1], or_3_out[0], and_7_out);
  EX_MEM ex_mem_1 (
    .MemToReg_in(id_ex_1_memtoreg_out), .IR_in(id_ex_1_ir_out), .MemWrite_in(id_ex_1_memwrite_out),
    .PC_in(id_ex_1_pc_out), .RegWrite_in(EX_Regwrite), .R2_in(id_ex_1_r2_out), .JAL_in(id_ex_1_jal_out),
    .AluR_in(mips_alu_1_result), .RegDst_in(id_ex_1_regdst_out), .Halt_in(id_ex_1_halt_out),
    .SB_in(id_ex_1_sb_out), .W__in(EX_W_num), .CLK(CLK), .MemToReg_out(ex_mem_1_memtoreg_out),
    .IR_out(ex_mem_1_ir_out), .MemWrite_out(MemWrite), .PC_out(ex_mem_1_pc_out), .RegWrite_out(MEM_Regwrite),
    .R2_out(ex_mem_1_r2_out), .JAL_out(ex_mem_1_jal_out), .AluR_out(ex_mem_1_alur_out),
    .RegDst_out(ex_mem_1_regdst_out), .Halt_out(ex_mem_1_halt_out), .SB_out(ex_mem_1_sb_out),
    .W__out(MEM_W_num), .RST(RST), .Enable(halt), .PCb_in(EX_PC), .PCb_out(M_PC));  // open: CHANGE_MEM_OR_RAM_in, CHANGE_MEM_OR_RAM_out
  Shifter #(.width(32), .shift("ll")) shifter_2 (.in(ram_1_data), .\dist (5'b01000), .out(shifter_2_out));
  Multiplexer #(.select(1), .width(32), .disabled("Z"), .enable("false")) multiplexer_9 (
    .in0(ex_mem_1_r2_out), .in1({shifter_2_out[31:8], ex_mem_1_r2_out[7:0]}), .out(MDin),
    .sel(ex_mem_1_sb_out));
  RAM #(.addrWidth(10), .dataWidth(32), .bus("separate"), .Select("high")) ram_1 (
    .addr(ex_mem_1_alur_out[11:2]), .din(MDin), .data(ram_1_data), .str(MemWrite), .clk(CLK), .clr(RST));  // open: sel, ld
  MEM_WB mem_wb_1 (
    .MemToReg_in(ex_mem_1_memtoreg_out), .IR_in(ex_mem_1_ir_out), .RegWrite_in(MEM_Regwrite),
    .PC_in(ex_mem_1_pc_out), .JAL_in(ex_mem_1_jal_out), .MemD_in(ram_1_data),
    .RegDst_in(ex_mem_1_regdst_out), .AluR_in(ex_mem_1_alur_out), .Halt_in(ex_mem_1_halt_out),
    .W__in(MEM_W_num), .CLK(CLK), .MemToReg_out(mem_wb_1_memtoreg_out), .IR_out(mem_wb_1_ir_out),
    .RegWrite_out(RegWrite), .PC_out_2(mem_wb_1_pc_out_2), .JAL_out(mem_wb_1_jal_out),
    .MemD_out(mem_wb_1_memd_out), .RegDst_out(mem_wb_1_regdst_out), .AluR_out(mem_wb_1_alur_out),
    .Halt_out(mem_wb_1_halt_out), .RST(RST), .Enable(halt), .PCb_in(M_PC), .PC_out(WB_PC));  // open: W__out, CHANGE_MEM_OR_RAM_in, CHANGE_MEM_OR_RAM_out
  not not_7 (not_7_out, mem_wb_1_halt_out);
  Multiplexer #(.select(1), .width(32), .disabled("Z"), .enable("false")) multiplexer_10 (
    .in0(mem_wb_1_alur_out), .in1(mem_wb_1_memd_out), .out(multiplexer_10_out), .sel(mem_wb_1_memtoreg_out));
  Multiplexer #(.select(1), .width(5), .disabled("Z"), .enable("false")) multiplexer_11 (
    .in0(mem_wb_1_ir_out[20:16]), .in1(mem_wb_1_ir_out[15:11]), .out(multiplexer_11_out),
    .sel(mem_wb_1_regdst_out));
  or or_5 (halt, Go, not_7_out);
  Multiplexer #(.select(1), .width(32), .disabled("Z"), .enable("false")) multiplexer_12 (
    .in0(multiplexer_10_out), .in1(mem_wb_1_pc_out_2), .out(RDin), .sel(mem_wb_1_jal_out));
  Multiplexer #(.select(1), .width(5), .disabled("Z"), .enable("false")) multiplexer_13 (
    .in0(multiplexer_11_out), .in1({5{1'b1}}), .out(W_num), .sel(mem_wb_1_jal_out));

  // Other names for the same wires on the sheet: MEM_PC[31:0] = M_PC; PC[31:0] = IF_PC; RW = RegWrite

  // Notes on the sheet:
  //   中断源
  //   时空图监测，可删除
  //   中断等待指示
  //   PC+4
  //   PC+imm
  //   PC-J
  //   PC-JR
  //   数码管输出
  //   指令存储器
  //   contents of rom_1 (hex, n*v repeats v):
  //   20110001 8000c05 20110001 20120002 20130003 8000c09 20110001 20120002 20130003 8000c0d 20110001
  //   20120002 20130003 8000c11 20110001 20120002 20130003 c000cb8 20100001 20110001 118fc0 112020
  //   20020022 c 118882 12200001 8000c15 112020 20020022 c 20110001 118880 112020 20020022 c 12200001
  //   8000c1f 20110001 118fc0 112020 20020022 c 1188c3 112020 20020022 c 118903 112020 20020022 c 118903
  //   112020 20020022 c 118903 112020 20020022 c 118903 112020 20020022 c 118903 112020 20020022 c 118903
  //   112020 20020022 c 118903 112020 20020022 c 20100001 109fc0 139fc3 8021 2012000c 24160003 26100001
  //   3210000f 20080008 20090001 139900 2709825 132020 20020022 c 1094022 1500fff9 22100001 2018000f
  //   2188024 108700 20080008 20090001 139902 2709825 132021 20020022 c 1094022 1500fff9 108702 2c9b022
  //   12c00001 8000c50 4020 1084027 84400 3508ffff 82021 20020022 c 2010ffff 20110000 ae300000 22100001
  //   22310004 ae300000 22100001 22310004 ae300000 22100001 22310004 ae300000 22100001 22310004 ae300000
  //   22100001 22310004 ae300000 22100001 22310004 ae300000 22100001 22310004 ae300000 22100001 22310004
  //   ae300000 22100001 22310004 ae300000 22100001 22310004 ae300000 22100001 22310004 ae300000 22100001
  //   22310004 ae300000 22100001 22310004 ae300000 22100001 22310004 ae300000 22100001 22310004 ae300000
  //   22100001 22310004 22100001 8020 2011003c 8e130000 8e340000 274402a 11000002 ae330000 ae140000
  //   2231fffc 1611fff8 102020 20020022 c 22100004 2011003c 1611fff2 20020032 c 20100000 22100001 102020
  //   20020022 c 22100002 102020 20020022 c 22100003 102020 20020022 c 22100004 102020 20020022 c 22100005
  //   102020 20020022 c 22100006 102020 20020022 c 22100007 102020 20020022 c 22100008 102020 20020022
  //   20020022 c 3e00008
  //   指令字
  //   JR
  //   JMP
  //   JMP+IF
  //   流水调试日志用
  //   IR
  //   addr
  //   shamt
  //   控制位
  //   暂停节拍，不能为0
  //   SignedEXT
  //   BGEZ
  //   OP
  //   Func
  //   rs
  //   rt
  //   rd
  //   imm
  //   戳工具置1进入计数暂停模式，ctrl+k时钟自动运行到对应节拍暂停
  //   ctrl+k关闭时钟连续运行，将控制位置零，进入单步调试模式调试
  //   Beq
  //   JMP
  //   JR
  //   Bne
  //   SB
  //   OP
  //   JAL
  //   Func
  //   MemToReg
  //   MemWrite
  //   AluOP
  //   AluSrcB
  //   RegWrite
  //   RegDst
  //   Syscall
  //   可计数暂停的时钟源
  //   为方便自动评测，需要输出流水线各段保存的PC值，注意是PC不是PC+4，另外ID段寄存器写入信息，Mem段内存写入信息也要输出
  //   JMP+IF
  //   rt
  //   rd
  //   W#
endmodule

module \重定向流水线  (
  output RegWrite,
  output MemWrite,
  output [31:0] IF_PC,
  output [31:0] ID_PC,
  output [31:0] EX_PC,
  output [31:0] M_PC,
  output [31:0] WB_PC,
  output [31:0] RDin,
  output [31:0] MDin,
  output [31:0] LedData
);

  wire ALL_JUMP, and_1_out, and_2_out, and_3_out, and_4_out, and_5_out, and_7_out, BGEZ, BGEZ_YES, CLK,
       clock_1_out, clock_2_out, comparator_2_eq, comparator_2_lt, d_ff_1_q, ex_mem_1_halt_out,
       ex_mem_1_jal_out, ex_mem_1_memtoreg_out, ex_mem_1_regdst_out, ex_mem_1_sb_out, EX_Regwrite,
       EX_SYSCALL, Go, halt, id_ex_1_beq_out, id_ex_1_bne_out, id_ex_1_jal_out, id_ex_1_memtoreg_out,
       id_ex_1_memwrite_out, id_ex_1_regdst_out, id_ex_1_sb_out, ID_JAL, ID_RDst, IR1, IR2, IR3, LED,
       Load_Use, MEM_Regwrite, mem_wb_1_halt_out, mem_wb_1_jal_out, mem_wb_1_memtoreg_out,
       mem_wb_1_regdst_out, mips_alu_1_equal, nand_1_out, not_1_out, not_2_out, not_3_out, not_4_out,
       not_6_out, not_7_out, or_1_out, or_2_out, RST, SYSEQUAL, W1, W2, W3, \单周期硬布线控制器_1_alu_src ,
       \单周期硬布线控制器_1_beq , \单周期硬布线控制器_1_bgez , \单周期硬布线控制器_1_bne , \单周期硬布线控制器_1_jmp , \单周期硬布线控制器_1_jr ,
       \单周期硬布线控制器_1_memtoreg , \单周期硬布线控制器_1_memwrite , \单周期硬布线控制器_1_regwrite , \单周期硬布线控制器_1_sb ,
       \单周期硬布线控制器_1_signedext , \单周期硬布线控制器_1_syscall ;
  wire [1:0] id_ex_1_signedext_out, R1_FORWARD, R2_FORWARD, redirect_signal_logic_1_r1_forward,
       redirect_signal_logic_1_r2_forward;
  wire [2:0] or_3_out;
  wire [3:0] id_ex_1_aluop_out, \单周期硬布线控制器_1_alu_op ;
  wire [4:0] EX_W_num, id_ex_1_shamt_out, ID_R1_num, ID_R2_num, MEM_W_num, multiplexer_3_out,
       multiplexer_6_out, multiplexer_7_out, multiplexer_8_out, multiplexer_14_out, W_num, WB_W_num;
  wire [5:0] EX_FUNC, ID_FUNC;
  wire [12:0] CNT_num;
  wire [15:0] id_ex_1_imm_out, \LoadUse次数 , \总周期数 , \插入气泡数 , \无条件分支数 , \条件分支成功数 ;
  wire [31:0] A0, adder_1_out, adder_2_out, bit_extender_1_out, bit_extender_2_out, ex_mem_1_pc_out,
       ex_mem_1_r2_out, id_ex_1_address_out, id_ex_1_pc_out, id_ex_1_r1_out, id_ex_1_r2_out, if_id_1_pc_out,
       IF_IR, MEM_ALU, MEM_IR, mem_wb_1_alur_out, mem_wb_1_memd_out, mem_wb_1_pc_out_2, mips_alu_1_result,
       mips_regifile_1_r1, multiplexer_1_out, multiplexer_2_out, multiplexer_9_out, multiplexer_10_out,
       multiplexer_11_out, multiplexer_12_out, ram_1_data, shifter_1_out, shifter_2_out, WB_IR, WB_TOREG;
  wire [31:6] EX_IR, ID_IR;

  Button \u_总复位  (.out(RST));
  Button _1 (.out(IR1));
  Button _2 (.out(IR2));
  Button _3 (.out(IR3));
  // Probe on \总周期数 
  // Probe on \总周期数 
  Button \u_继续运行  (.out(Go));
  LED #(.active("true")) led_1 (.in(W1));
  LED #(.active("true")) led_2 (.in(W2));
  LED #(.active("true")) led_3 (.in(W3));
  Hex_Digit_Display hex_digit_display_1 (.value(LedData[31:28]));  // open: dp
  // Probe on IF_PC[19:0]
  // Mips_Probe mips_probe_1: pin names not known; wires that end beside it: IF_IR
  Hex_Digit_Display hex_digit_display_2 (.value(LedData[27:24]));  // open: dp
  Hex_Digit_Display hex_digit_display_3 (.value(LedData[23:20]));  // open: dp
  // Probe on ID_PC[19:0]
  // Mips_Probe mips_probe_2: pin names not known; wires that end beside it: {ID_IR, ID_FUNC}
  Multiplexer #(.select(3), .width(32), .disabled("Z"), .enable("false")) multiplexer_1 (
    .in0(adder_1_out), .in1(adder_2_out), .in2(id_ex_1_address_out), .in6(multiplexer_12_out),
    .out(multiplexer_1_out), .sel(or_3_out));  // open: in3, in4, in5, in7
  Hex_Digit_Display hex_digit_display_4 (.value(LedData[15:12]));  // open: dp
  Hex_Digit_Display hex_digit_display_5 (.value(LedData[19:16]));  // open: dp
  not not_1 (not_1_out, Load_Use);
  Hex_Digit_Display hex_digit_display_6 (.value(LedData[7:4]));  // open: dp
  Hex_Digit_Display hex_digit_display_7 (.value(LedData[11:8]));  // open: dp
  Clock #(.highDuration(1), .lowDuration(1)) clock_1 (.out(clock_1_out));
  // Probe on EX_PC[19:0]
  // Mips_Probe mips_probe_3: pin names not known; wires that end beside it: clock_1_out, {EX_IR, EX_FUNC}, CLK
  Multiplexer #(.select(2), .width(32), .disabled("Z"), .enable("false")) multiplexer_2 (
    .in0(multiplexer_1_out), .in1(multiplexer_1_out), .in2(adder_1_out), .in3(adder_2_out),
    .out(multiplexer_2_out), .sel({BGEZ, BGEZ_YES}));
  Register #(.width(32), .trigger("rising"), .Select("low")) PC (
    .D(multiplexer_2_out), .en(and_1_out), .Q(IF_PC), .clk(CLK), .clr(RST));
  and and_1 (and_1_out, not_1_out, halt);
  Counter #(.width(16), .max('hffff), .ongoal("wrap"), .trigger("rising"), .behavior("new")) counter_1 (
    .count(halt), .Q(\总周期数 ), .clk(CLK), .clr(RST));  // open: load, D, carry, preset, down
  Hex_Digit_Display hex_digit_display_8 (.value(LedData[3:0]));  // open: dp
  Register #(.width(32), .trigger("rising"), .Select("low")) register_1 (
    .D(A0), .en(LED), .Q(LedData), .clk(CLK), .clr(RST));
  // Probe on \总周期数 
  // Probe on M_PC[19:0]
  // Mips_Probe mips_probe_4: pin names not known; wires that end beside it: MEM_IR
  // Probe on \总周期数 
  // Probe on \无条件分支数 
  // Probe on \条件分支成功数 
  // Probe on \插入气泡数 
  // Probe on \LoadUse次数 
  ROM #(.addrWidth(10), .dataWidth(32), .Select("high")) rom_1 (.addr(IF_PC[11:2]), .data(IF_IR));
  Adder #(.width(32)) adder_1 (.a(IF_PC), .b(32'h4), .out(adder_1_out));  // open: cin, cout
  // Probe on IF_PC[11:0]
  // Probe on WB_PC[19:0]
  // Mips_Probe mips_probe_5: pin names not known; wires that end beside it: WB_IR
  // Probe on EX_PC[11:0]
  // Probe on ID_PC[11:0]
  or or_1 (or_1_out, RST, ALL_JUMP);
  IF_ID if_id_1 (
    .PC_in(adder_1_out), .IR_in(IF_IR), .CLK(CLK), .PC_out(if_id_1_pc_out), .IR_out({ID_IR, ID_FUNC}),
    .RST(or_1_out), .Enable(and_2_out), .PCb_in(IF_PC), .PCb_out(ID_PC));
  // Probe on M_PC[11:0]
  not not_2 (not_2_out, Load_Use);
  and and_2 (and_2_out, not_2_out, halt);
  // Probe on WB_PC[11:0]
  Multiplexer #(.select(1), .width(5), .disabled("Z"), .enable("false")) multiplexer_3 (
    .in0(ID_IR[20:16]), .in1(ID_IR[15:11]), .out(multiplexer_3_out), .sel(ID_RDst));
  \单周期硬布线控制器  \u_单周期硬布线控制器_1  (
    .Func(ID_FUNC), .OP(ID_IR[31:26]), .ALU_OP(\单周期硬布线控制器_1_alu_op ), .MemToReg(\单周期硬布线控制器_1_memtoreg ),
    .MemWrite(\单周期硬布线控制器_1_memwrite ), .ALU_SRC(\单周期硬布线控制器_1_alu_src ), .RegWrite(\单周期硬布线控制器_1_regwrite ),
    .SysCALL(\单周期硬布线控制器_1_syscall ), .SignedExt(\单周期硬布线控制器_1_signedext ), .RegDst(ID_RDst),
    .JR(\单周期硬布线控制器_1_jr ), .JMP(\单周期硬布线控制器_1_jmp ), .Beq(\单周期硬布线控制器_1_beq ), .JAL(ID_JAL),
    .Bne(\单周期硬布线控制器_1_bne ), .BGEZ(\单周期硬布线控制器_1_bgez ), .SB(\单周期硬布线控制器_1_sb ));  // open: ERET
  Multiplexer #(.select(1), .width(5), .disabled("Z"), .enable("false")) multiplexer_4 (
    .in0(ID_IR[25:21]), .in1(5'b00010), .out(ID_R1_num), .sel(\单周期硬布线控制器_1_syscall ));
  Multiplexer #(.select(1), .width(5), .disabled("Z"), .enable("false")) multiplexer_5 (
    .in0(ID_IR[20:16]), .in1(5'b00100), .out(ID_R2_num), .sel(\单周期硬布线控制器_1_syscall ));
  Multiplexer #(.select(1), .width(5), .disabled("Z"), .enable("false")) multiplexer_6 (
    .in0(multiplexer_3_out), .in1({5{1'b1}}), .out(multiplexer_6_out), .sel(ID_JAL));
  MIPS_Regifile mips_regifile_1 (
    .Din(RDin), .Clk(CLK), .R1(mips_regifile_1_r1), .R2(A0), .WE(RegWrite), .W_num(W_num),
    .R1_num(ID_R1_num), .R2_num(ID_R2_num));
  or or_2 (or_2_out, RST, ALL_JUMP, Load_Use);
  ID_EX id_ex_1 (
    .IR_in({ID_IR, ID_FUNC}), .PC_in(if_id_1_pc_out), .BEQ_in(\单周期硬布线控制器_1_beq ), .R1_in(mips_regifile_1_r1),
    .BNE_in(\单周期硬布线控制器_1_bne ), .MemToReg_in(\单周期硬布线控制器_1_memtoreg ), .R2_in(A0),
    .MemWrite_in(\单周期硬布线控制器_1_memwrite ), .Imm_in({ID_IR[15:6], ID_FUNC}),
    .AluSrcB_in(\单周期硬布线控制器_1_alu_src ), .Address_in({if_id_1_pc_out[31:28], ID_IR[25:6], ID_FUNC, 2'b00}),
    .RegWrite_in(\单周期硬布线控制器_1_regwrite ), .AluOP_in(\单周期硬布线控制器_1_alu_op ), .JAL_in(ID_JAL),
    .Shamt_in(ID_IR[10:6]), .RegDst_in(ID_RDst), .SB_in(\单周期硬布线控制器_1_sb ), .JMP_in(\单周期硬布线控制器_1_jmp ),
    .BGEZ_in(\单周期硬布线控制器_1_bgez ), .W__in(multiplexer_6_out), .JR_in(\单周期硬布线控制器_1_jr ), .CLK(CLK),
    .IR_out({EX_IR, EX_FUNC}), .PC_out(id_ex_1_pc_out), .BEQ_out(id_ex_1_beq_out), .R1_out(id_ex_1_r1_out),
    .BNE_out(id_ex_1_bne_out), .MemToReg_out(id_ex_1_memtoreg_out), .R2_out(id_ex_1_r2_out),
    .MemWrite_out(id_ex_1_memwrite_out), .Imm_out(id_ex_1_imm_out), .AluSrcB_out(id_ex_1_signedext_out[1]),
    .Address_out(id_ex_1_address_out), .RegWrite_out(EX_Regwrite), .AluOP_out(id_ex_1_aluop_out),
    .JAL_out(id_ex_1_jal_out), .Shamt_out(id_ex_1_shamt_out), .RegDst_out(id_ex_1_regdst_out),
    .SB_out(id_ex_1_sb_out), .JMP_out(or_3_out[1]), .BGEZ_out(BGEZ), .W__out(EX_W_num), .JR_out(or_3_out[2]),
    .RST(or_2_out), .Enable(halt), .SignedEXT_in(\单周期硬布线控制器_1_signedext ),
    .SignedEXT_out(id_ex_1_signedext_out[0]), .PCb_in(ID_PC), .PCb_out(EX_PC),
    .SYSCALL(\单周期硬布线控制器_1_syscall ), .SYSCALL_2(EX_SYSCALL));  // open: Halt_in, Halt_out, CHANGE_MEM_OR_RAM_in, CHANGE_MEM_OR_RAM_out
  Multiplexer #(.select(1), .width(5), .disabled("Z"), .enable("false")) multiplexer_7 (
    .in0(EX_IR[25:21]), .in1(5'b00010), .out(multiplexer_7_out), .sel(EX_SYSCALL));
  Multiplexer #(.select(1), .width(5), .disabled("Z"), .enable("false")) multiplexer_8 (
    .in0(EX_IR[20:16]), .in1(5'b00100), .out(multiplexer_8_out), .sel(EX_SYSCALL));
  and and_3 (and_3_out, id_ex_1_beq_out, mips_alu_1_equal);
  and and_4 (and_4_out, id_ex_1_bne_out, not_3_out);
  not not_3 (not_3_out, mips_alu_1_equal);
  Multiplexer #(.select(2), .width(32), .disabled("Z"), .enable("false")) multiplexer_9 (
    .in0(id_ex_1_r2_out), .in1(MEM_ALU), .in2(WB_TOREG), .in3(WB_TOREG), .out(multiplexer_9_out),
    .sel(R2_FORWARD));
  assign bit_extender_1_out = {{16{id_ex_1_imm_out[15]}}, id_ex_1_imm_out};  // Bit_Extender bit_extender_1
  or or_3 (or_3_out[0], and_3_out, and_4_out);
  Multiplexer #(.select(2), .width(32), .disabled("Z"), .enable("false")) multiplexer_10 (
    .in0(multiplexer_9_out), .in1(multiplexer_9_out), .in2(bit_extender_2_out), .in3(bit_extender_1_out),
    .out(multiplexer_10_out), .sel(id_ex_1_signedext_out));
  assign bit_extender_2_out = {{16{1'b0}}, id_ex_1_imm_out};  // Bit_Extender bit_extender_2
  Redirect_signal_logic redirect_signal_logic_1 (
    .ID_OP(ID_IR[31:26]), .ID_FUNC(ID_FUNC), .ID_R1_num(ID_R1_num), .ID_R2_num(ID_R2_num),
    .EX_W_num(EX_W_num), .MEM_W_num(MEM_W_num), .WB_W_num(WB_W_num), .EX_RegWrite(EX_Regwrite),
    .MEM_RegWrite(MEM_Regwrite), .WB_RegWrite(RegWrite), .EX_OP(EX_IR[31:26]), .EX_FUNC(EX_FUNC),
    .EX_R1_num(multiplexer_7_out), .EX_R2_num(multiplexer_8_out), .Load_Use(Load_Use),
    .R1_Forward(redirect_signal_logic_1_r1_forward), .R2_Forward(redirect_signal_logic_1_r2_forward));
  not not_4 (not_4_out, mips_alu_1_result[0]);
  Multiplexer #(.select(1), .width(32), .disabled("Z"), .enable("false")) multiplexer_11 (
    .in0(multiplexer_10_out), .in1({32{1'b0}}), .out(multiplexer_11_out), .sel(BGEZ));
  Register #(.width(4), .trigger("falling"), .Select("low")) register_2 (
    .D({redirect_signal_logic_1_r2_forward, redirect_signal_logic_1_r1_forward}),
    .Q({R2_FORWARD, R1_FORWARD}), .clk(CLK), .clr(RST));  // open: en
  or or_4 (ALL_JUMP, or_3_out[2], or_3_out[1], or_3_out[0], and_5_out);
  and and_5 (and_5_out, not_4_out, BGEZ);
  Multiplexer #(.select(2), .width(32), .disabled("Z"), .enable("false")) multiplexer_12 (
    .in0(id_ex_1_r1_out), .in1(MEM_ALU), .in2(WB_TOREG), .in3(WB_TOREG), .out(multiplexer_12_out),
    .sel(R1_FORWARD));
  Shifter #(.width(32), .shift("ll")) shifter_1 (.in(bit_extender_1_out), .\dist (5'b00010), .out(shifter_1_out));
  Comparator #(.width(32), .mode("twosComplement")) comparator_1 (
    .a(32'h22), .b(multiplexer_12_out), .eq(SYSEQUAL));  // open: gt, lt
  Adder #(.width(32)) adder_2 (.a(shifter_1_out), .b(id_ex_1_pc_out), .out(adder_2_out));  // open: cin, cout
  MIPS_ALU mips_alu_1 (
    .X(multiplexer_12_out), .Y(multiplexer_11_out), .AluOP(id_ex_1_aluop_out), .Equal(mips_alu_1_equal),
    .Result(mips_alu_1_result), .shamt(id_ex_1_shamt_out));  // open: Result_2
  not not_5 (BGEZ_YES, mips_alu_1_result[0]);
  and and_6 (LED, EX_SYSCALL, SYSEQUAL);
  and and_7 (and_7_out, EX_SYSCALL, not_6_out);
  not not_6 (not_6_out, SYSEQUAL);
  D_Flip_Flop #(.trigger("high"), .Pre_Clr_Positions("LEGACY"), .NegatePresetClear("false"), .enable("true"), .NewFFLayout("false")) d_ff_1 (.Q(d_ff_1_q));  // open: clk, D, Qn, preset, en, reset
  // Probe on 13'hc
  EX_MEM ex_mem_1 (
    .MemToReg_in(id_ex_1_memtoreg_out), .IR_in({EX_IR, EX_FUNC}), .MemWrite_in(id_ex_1_memwrite_out),
    .PC_in(id_ex_1_pc_out), .RegWrite_in(EX_Regwrite), .R2_in(multiplexer_9_out), .JAL_in(id_ex_1_jal_out),
    .AluR_in(mips_alu_1_result), .RegDst_in(id_ex_1_regdst_out), .Halt_in(and_7_out), .SB_in(id_ex_1_sb_out),
    .W__in(EX_W_num), .CLK(CLK), .MemToReg_out(ex_mem_1_memtoreg_out), .IR_out(MEM_IR),
    .MemWrite_out(MemWrite), .PC_out(ex_mem_1_pc_out), .RegWrite_out(MEM_Regwrite), .R2_out(ex_mem_1_r2_out),
    .JAL_out(ex_mem_1_jal_out), .AluR_out(MEM_ALU), .RegDst_out(ex_mem_1_regdst_out),
    .Halt_out(ex_mem_1_halt_out), .SB_out(ex_mem_1_sb_out), .W__out(MEM_W_num), .RST(RST), .Enable(halt),
    .PCb_in(EX_PC), .PCb_out(M_PC));  // open: CHANGE_MEM_OR_RAM_in, CHANGE_MEM_OR_RAM_out
  Comparator #(.width(13), .mode("twosComplement")) comparator_2 (
    .a(CNT_num), .b(13'hc), .eq(comparator_2_eq), .lt(comparator_2_lt));  // open: gt
  Clock #(.highDuration(1), .lowDuration(1)) clock_2 (.out(clock_2_out));
  Shifter #(.width(32), .shift("ll")) shifter_2 (.in(ram_1_data), .\dist (5'b01000), .out(shifter_2_out));
  nand nand_1 (nand_1_out, d_ff_1_q, comparator_2_eq);
  Counter #(.width(13), .max('h1fff), .ongoal("stay"), .trigger("rising"), .behavior("old")) counter_2 (
    .count(comparator_2_lt), .Q(CNT_num), .clk(clock_2_out));  // open: load, D, carry, clr, preset
  Multiplexer #(.select(1), .width(32), .disabled("Z"), .enable("false")) multiplexer_13 (
    .in0(ex_mem_1_r2_out), .in1({shifter_2_out[31:8], ex_mem_1_r2_out[7:0]}), .out(MDin),
    .sel(ex_mem_1_sb_out));
  assign CLK = nand_1_out ? clock_2_out : 1'bz;  // Controlled_Buffer controlled_buffer_1
  Pull_Resistor #(.pull(1)) pull_resistor_1 (.node(CLK));
  RAM #(.addrWidth(10), .dataWidth(32), .bus("separate"), .Select("high")) ram_1 (
    .addr(MEM_ALU[11:2]), .din(MDin), .data(ram_1_data), .str(MemWrite), .clk(CLK), .clr(RST));  // open: sel, ld
  MEM_WB mem_wb_1 (
    .MemToReg_in(ex_mem_1_memtoreg_out), .IR_in(MEM_IR), .RegWrite_in(MEM_Regwrite), .PC_in(ex_mem_1_pc_out),
    .JAL_in(ex_mem_1_jal_out), .MemD_in(ram_1_data), .RegDst_in(ex_mem_1_regdst_out), .AluR_in(MEM_ALU),
    .Halt_in(ex_mem_1_halt_out), .W__in(MEM_W_num), .CLK(CLK), .MemToReg_out(mem_wb_1_memtoreg_out),
    .IR_out(WB_IR), .RegWrite_out(RegWrite), .PC_out_2(mem_wb_1_pc_out_2), .JAL_out(mem_wb_1_jal_out),
    .MemD_out(mem_wb_1_memd_out), .RegDst_out(mem_wb_1_regdst_out), .AluR_out(mem_wb_1_alur_out),
    .Halt_out(mem_wb_1_halt_out), .W__out(WB_W_num), .RST(RST), .Enable(halt), .PCb_in(M_PC), .PC_out(WB_PC));  // open: CHANGE_MEM_OR_RAM_in, CHANGE_MEM_OR_RAM_out
  Multiplexer #(.select(1), .width(5), .disabled("Z"), .enable("false")) multiplexer_14 (
    .in0(WB_IR[20:16]), .in1(WB_IR[15:11]), .out(multiplexer_14_out), .sel(mem_wb_1_regdst_out));
  or or_5 (halt, Go, not_7_out);
  not not_7 (not_7_out, mem_wb_1_halt_out);
  Multiplexer #(.select(1), .width(32), .disabled("Z"), .enable("false")) multiplexer_15 (
    .in0(mem_wb_1_alur_out), .in1(mem_wb_1_memd_out), .out(WB_TOREG), .sel(mem_wb_1_memtoreg_out));
  Multiplexer #(.select(1), .width(32), .disabled("Z"), .enable("false")) multiplexer_16 (
    .in0(WB_TOREG), .in1(mem_wb_1_pc_out_2), .out(RDin), .sel(mem_wb_1_jal_out));
  Multiplexer #(.select(1), .width(5), .disabled("Z"), .enable("false")) multiplexer_17 (
    .in0(multiplexer_14_out), .in1({5{1'b1}}), .out(W_num), .sel(mem_wb_1_jal_out));

  // Other names for the same wires on the sheet: ID_IR[5:0] = ID_FUNC; EX_IR[5:0] = EX_FUNC;
  //   EX_rt[4:0] = EX_IR[20:16]; EX_rs[4:0] = EX_IR[25:21]; EX_OP[5:0] = EX_IR[31:26]; ID_OP[5:0] = ID_IR[31:26];
  //   IR[31:0] = IF_IR; MEM_PC[31:0] = M_PC; PC[31:0] = IF_PC; RW = RegWrite; WB_Regwrite = RegWrite

  // Notes on the sheet:
  //   中断源
  //   时空图监测，可删除
  //   中断等待指示
  //   PC+4
  //   PC+imm
  //   PC-J
  //   PC-JR
  //   数码管输出
  //   指令存储器
  //   JR
  //   JMP
  //   JMP+IF
  //   流水调试日志用
  //   IR
  //   addr
  //   shamt
  //   SignedEXT
  //   BGEZ
  //   SB
  //   OP
  //   Func
  //   rs
  //   rt
  //   rd
  //   imm
  //   Beq
  //   JMP
  //   JR
  //   Bne
  //   OP
  //   JAL
  //   Func
  //   MemToReg
  //   MemWrite
  //   AluOP
  //   AluSrcB
  //   RegWrite
  //   RegDst
  //   Syscall
  //   为方便自动评测，需要输出流水线各段保存的PC值，注意是PC不是PC+4，另外ID段寄存器写入信息，Mem段内存写入信息也要输出
  //   JMP+IF
  //   控制位
  //   暂停节拍，不能为0
  //   戳工具置1进入计数暂停模式，ctrl+k时钟自动运行到对应节拍暂停
  //   ctrl+k关闭时钟连续运行，将控制位置零，进入单步调试模式调试
  //   可计数暂停的时钟源
  //   rt
  //   rd
  //   W#
endmodule

module \中断按键参考电路  (
  input  \同步清零信号 ,
  output \与中断屏蔽位与 
);

  wire \_1号中断_out , and_1_out, clock_1_out, d_ff_1_q, or_1_out, or_2_out;

  Clock #(.highDuration(1), .lowDuration(1)) clock_1 (.out(clock_1_out));
  Button \_1号中断  (.out(\_1号中断_out ));
  LED #(.active("true")) \_1号中断等待指示灯  (.in(or_1_out));
  or or_1 (or_1_out, \与中断屏蔽位与 , d_ff_1_q);
  D_Flip_Flop #(.trigger("rising"), .Pre_Clr_Positions("LEGACY"), .NegatePresetClear("false"), .enable("true"), .NewFFLayout("false")) d_ff_1 (
    .clk(\_1号中断_out ), .D(1'b1), .Q(d_ff_1_q), .reset(\与中断屏蔽位与 ));  // open: Qn, preset, en
  or or_2 (or_2_out, d_ff_1_q, \与中断屏蔽位与 );
  and and_1 (and_1_out, or_2_out, ~\同步清零信号 );  // AND_Gate
  D_Flip_Flop #(.trigger("rising"), .Pre_Clr_Positions("LEGACY"), .NegatePresetClear("false"), .enable("true"), .NewFFLayout("false")) IR1 (
    .clk(clock_1_out), .D(and_1_out), .Q(\与中断屏蔽位与 ));  // open: Qn, preset, en, reset
  \单周期硬布线控制器  \u_单周期硬布线控制器_1  ();  // open: Func, OP, ALU_OP, MemToReg, MemWrite, ALU_SRC, RegWrite, SysCALL, SignedExt, RegDst, JR, JMP, Beq, JAL, Bne, BGEZ, SB, ERET

  // Notes on the sheet:
  //   中断信号采样参考电路
  //   Reset 
endmodule

module \单周期MIPS_单级中断  (
  input  IR1,
  input  IR2,
  input  IR3,
  output RegWrite,
  output MemWrite,
  output [31:0] PC,
  output [31:0] IR,
  output [31:0] RDin,
  output [31:0] MDin,
  output [31:0] LedData
);

  wire and_3_out, and_4_out, and_5_out, and_6_out, and_7_out, and_8_out, and_9_out, and_10_out, and_11_out,
       and_12_out, BEQ, BGEZ, BGEZ_YES, BNE, CLK, comparator_1_eq, comparator_2_eq, comparator_3_eq,
       comparator_4_eq, comparator_5_eq, comparator_6_eq, d_ff_1_q, d_ff_2_q, d_ff_3_q, equal, ERET, Go,
       halt, IR1_q, IR1_t, IR2_q, IR2_t, IR3_q, IR3_t, IRA, IRB, IRC, JAL, JMP, JMP_IF, JR, LED,
       multiplexer_4_out, not_1_out, not_2_out, not_3_out, not_4_out, or_1_out, or_5_out, or_6_out, or_7_out,
       or_8_out, or_9_out, priority_encoder_1_gs, RegDst, RST, SB, SignedExt, syscall, W1, W2, W3, \中断状态_q ,
       \单周期硬布线控制器_1_memtoreg ;
  wire [1:0] IR_now, priority_encoder_1_out;
  wire [1:1] \单周期硬布线控制器_1_alu_src ;
  wire [3:0] \单周期硬布线控制器_1_alu_op ;
  wire [4:0] multiplexer_7_out, multiplexer_9_out, multiplexer_10_out, multiplexer_11_out;
  wire [15:0] \总周期数 ;
  wire [31:0] A0, bit_extender_1_out, bit_extender_2_out, EPC_q, mips_alu_1_result, MOUT, multiplexer_1_out,
       multiplexer_5_out, multiplexer_6_out, multiplexer_13_out, multiplexer_14_out, multiplexer_15_out,
       nextPC, PC_4, PC_imm, PC_JR, PCout, shifter_1_out, shifter_2_out;

  Clock #(.highDuration(1), .lowDuration(1)) clock_1 (.out(CLK));
  Button _1 ();  // open: out
  Button _2 ();  // open: out
  Button _3 ();  // open: out
  Button \u_继续运行  (.out(Go));
  LED #(.active("true")) led_1 (.in(W1));
  LED #(.active("true")) led_2 (.in(W2));
  LED #(.active("true")) led_3 (.in(W3));
  Hex_Digit_Display hex_digit_display_1 (.value(LedData[31:28]));  // open: dp
  Comparator #(.width(16), .mode("twosComplement")) comparator_1 (
    .a(16'h23b), .b(\总周期数 ), .eq(comparator_1_eq));  // open: gt, lt
  or or_1 (or_1_out, comparator_1_eq, comparator_2_eq);
  Comparator #(.width(16), .mode("twosComplement")) comparator_2 (
    .a(\总周期数 ), .b(16'h1), .eq(comparator_2_eq));  // open: gt, lt
  Comparator #(.width(16), .mode("twosComplement")) comparator_3 (
    .a(\总周期数 ), .b(16'h4), .eq(comparator_3_eq));  // open: gt, lt
  Comparator #(.width(16), .mode("twosComplement")) comparator_4 (
    .a(\总周期数 ), .b(16'h7), .eq(comparator_4_eq));  // open: gt, lt
  Comparator #(.width(32), .mode("twosComplement")) comparator_5 (
    .a(PC_JR), .b(32'h22), .eq(comparator_5_eq));  // open: gt, lt
  not not_1 (not_1_out, comparator_5_eq);
  or or_2 (W1, IR1_q, d_ff_1_q);
  or or_3 (W2, IR2_q, d_ff_2_q);
  or or_4 (W3, IR3_q, d_ff_3_q);
  Hex_Digit_Display hex_digit_display_2 (.value(LedData[23:20]));  // open: dp
  Hex_Digit_Display hex_digit_display_3 (.value(LedData[27:24]));  // open: dp
  Pull_Resistor #(.pull(0)) pull_resistor_1 (.node(IRA));
  assign IRA = or_1_out ? ~CLK : 1'bz;  // Controlled_Inverter controlled_inverter_1
  Pull_Resistor #(.pull(0)) pull_resistor_2 (.node(IRB));
  assign IRB = comparator_3_eq ? ~CLK : 1'bz;  // Controlled_Inverter controlled_inverter_2
  Pull_Resistor #(.pull(0)) pull_resistor_3 (.node(IRC));
  assign IRC = comparator_4_eq ? ~CLK : 1'bz;  // Controlled_Inverter controlled_inverter_3
  and and_1 (LED, syscall, comparator_5_eq);
  and and_2 (halt, syscall, not_1_out);
  D_Flip_Flop #(.trigger("rising"), .Pre_Clr_Positions("LEGACY"), .NegatePresetClear("false"), .enable("true"), .NewFFLayout("false")) d_ff_1 (
    .clk(IR1_t), .D(1'b1), .Q(d_ff_1_q), .reset(IR1_q));  // open: Qn, preset, en
  D_Flip_Flop #(.trigger("rising"), .Pre_Clr_Positions("LEGACY"), .NegatePresetClear("false"), .enable("true"), .NewFFLayout("false")) d_ff_2 (
    .clk(IR2_t), .D(1'b1), .Q(d_ff_2_q), .reset(IR2_q));  // open: Qn, preset, en
  D_Flip_Flop #(.trigger("rising"), .Pre_Clr_Positions("LEGACY"), .NegatePresetClear("false"), .enable("true"), .NewFFLayout("false")) d_ff_3 (
    .clk(IR3_t), .D(1'b1), .Q(d_ff_3_q), .reset(IR3_q));  // open: Qn, preset, en
  Hex_Digit_Display hex_digit_display_4 (.value(LedData[19:16]));  // open: dp
  Hex_Digit_Display hex_digit_display_5 (.value(LedData[15:12]));  // open: dp
  Multiplexer #(.select(3), .width(32), .disabled("Z"), .enable("false")) multiplexer_1 (
    .in0(PC_4), .in1(PC_imm), .in2({PC_4[31:28], IR[25:0], 2'b00}), .in6(PC_JR), .out(multiplexer_1_out),
    .sel({JR, JMP, JMP_IF}));  // open: in3, in4, in5, in7
  or or_5 (or_5_out, d_ff_1_q, IR1_q);
  or or_6 (or_6_out, d_ff_2_q, IR2_q);
  or or_7 (or_7_out, d_ff_3_q, IR3_q);
  Hex_Digit_Display hex_digit_display_6 (.value(LedData[7:4]));  // open: dp
  Hex_Digit_Display hex_digit_display_7 (.value(LedData[11:8]));  // open: dp
  // Probe on \总周期数 
  Shifter #(.width(32), .shift("ll")) shifter_1 (.in(MOUT), .\dist (5'b01000), .out(shifter_1_out));
  not not_2 (not_2_out, halt);
  Multiplexer #(.select(2), .width(32), .disabled("Z"), .enable("false")) multiplexer_2 (
    .in0(multiplexer_1_out), .in1(multiplexer_1_out), .in2(PC_4), .in3(PC_imm), .out(nextPC),
    .sel({BGEZ, BGEZ_YES}));
  not not_3 (not_3_out, halt);
  and and_3 (and_3_out, ERET, IR_now[0], ~IR_now[1]);  // AND_Gate
  and and_4 (and_4_out, ERET, ~IR_now[0], IR_now[1]);  // AND_Gate
  and and_5 (and_5_out, ERET, IR_now[0], IR_now[1]);
  Hex_Digit_Display hex_digit_display_8 (.value(LedData[3:0]));  // open: dp
  Counter #(.width(16), .max('hffff), .ongoal("wrap"), .trigger("rising"), .behavior("new")) counter_1 (
    .count(not_2_out), .Q(\总周期数 ), .clk(CLK), .clr(RST));  // open: load, D, carry, preset, down
  Register #(.width(32), .trigger("rising"), .Select("low")) u_PC (
    .D(PCout), .en(or_8_out), .Q(PC), .clk(CLK), .clr(RST));
  or or_8 (or_8_out, not_3_out, Go);
  and and_6 (and_6_out, or_5_out, ~and_3_out);  // AND_Gate
  and and_7 (and_7_out, or_6_out, ~and_4_out);  // AND_Gate
  and and_8 (and_8_out, or_7_out, ~and_5_out);  // AND_Gate
  // Probe on PC
  Multiplexer #(.select(1), .width(32), .disabled("Z"), .enable("false")) multiplexer_3 (
    .in0(A0), .in1({shifter_1_out[31:8], A0[7:0]}), .out(MDin), .sel(SB));
  D_Flip_Flop #(.trigger("rising"), .Pre_Clr_Positions("LEGACY"), .NegatePresetClear("false"), .enable("true"), .NewFFLayout("false")) u_IR1 (
    .clk(CLK), .D(and_6_out), .Q(IR1_q));  // open: Qn, preset, en, reset
  D_Flip_Flop #(.trigger("rising"), .Pre_Clr_Positions("LEGACY"), .NegatePresetClear("false"), .enable("true"), .NewFFLayout("false")) u_IR2 (
    .clk(CLK), .D(and_7_out), .Q(IR2_q));  // open: Qn, preset, en, reset
  D_Flip_Flop #(.trigger("rising"), .Pre_Clr_Positions("LEGACY"), .NegatePresetClear("false"), .enable("true"), .NewFFLayout("false")) u_IR3 (
    .clk(CLK), .D(and_8_out), .Q(IR3_q));  // open: Qn, preset, en, reset
  // Probe on IR
  Priority_Encoder #(.select(2), .disabled("Z")) priority_encoder_1 (
    .in0(1'b1), .in1(IR1_q), .in2(IR2_q), .in3(IR3_q), .out(priority_encoder_1_out),
    .gs(priority_encoder_1_gs));  // open: en_out, en_in
  Adder #(.width(32)) adder_1 (.a(PC), .b(32'h4), .out(PC_4));  // open: cin, cout
  Register #(.width(32), .trigger("rising"), .Select("low")) register_1 (
    .D(A0), .en(LED), .Q(LedData), .clk(CLK), .clr(RST));
  // Mips_Probe mips_probe_1: pin names not known; wires that end beside it: IR
  ROM #(.addrWidth(10), .dataWidth(32), .Select("high")) rom_1 (.addr(PC[11:2]), .data(IR));
  // Probe on priority_encoder_1_out
  Multiplexer #(.select(2), .width(1), .disabled("Z"), .enable("false")) multiplexer_4 (
    .in0(1'b0), .in1(priority_encoder_1_gs), .in2(priority_encoder_1_gs), .in3(priority_encoder_1_gs),
    .out(multiplexer_4_out), .sel(priority_encoder_1_out));
  Multiplexer #(.select(2), .width(32), .disabled("Z"), .enable("false")) multiplexer_5 (
    .in0(nextPC), .in1(32'h30ac), .in2(32'h3150), .in3(32'h31f4), .out(multiplexer_5_out),
    .sel(priority_encoder_1_out));
  and and_9 (and_9_out, multiplexer_4_out, ~\中断状态_q );  // AND_Gate
  // Probe on RDin
  Multiplexer #(.select(1), .width(32), .disabled("Z"), .enable("false")) multiplexer_6 (
    .in0(nextPC), .in1(multiplexer_5_out), .out(multiplexer_6_out), .sel(and_9_out));
  and and_10 (and_10_out, and_9_out, ~ERET);  // AND_Gate
  or or_9 (or_9_out, and_9_out, \中断状态_q );
  not not_4 (not_4_out, equal);
  Multiplexer #(.select(1), .width(5), .disabled("Z"), .enable("false")) multiplexer_7 (
    .in0(IR[20:16]), .in1(IR[15:11]), .out(multiplexer_7_out), .sel(RegDst));
  Multiplexer #(.select(1), .width(32), .disabled("Z"), .enable("false")) multiplexer_8 (
    .in0(multiplexer_6_out), .in1(EPC_q), .out(PCout), .sel(ERET));
  Register #(.width(32), .trigger("rising"), .Select("low")) EPC (
    .D(nextPC), .en(and_9_out), .Q(EPC_q), .clk(CLK));  // open: clr
  Register #(.width(1), .trigger("rising"), .Select("low")) \u_中断状态  (
    .D(or_9_out), .Q(\中断状态_q ), .clk(CLK), .clr(ERET));  // open: en
  and and_11 (and_11_out, BEQ, equal);
  and and_12 (and_12_out, BNE, not_4_out);
  \单周期硬布线控制器  \u_单周期硬布线控制器_1  (
    .Func(IR[5:0]), .OP(IR[31:26]), .ALU_OP(\单周期硬布线控制器_1_alu_op ), .MemToReg(\单周期硬布线控制器_1_memtoreg ),
    .MemWrite(MemWrite), .ALU_SRC(\单周期硬布线控制器_1_alu_src [1]), .RegWrite(RegWrite), .SysCALL(syscall),
    .SignedExt(SignedExt), .RegDst(RegDst), .JR(JR), .JMP(JMP), .Beq(BEQ), .JAL(JAL), .Bne(BNE), .BGEZ(BGEZ),
    .SB(SB), .ERET(ERET));
  Multiplexer #(.select(1), .width(5), .disabled("Z"), .enable("false")) multiplexer_9 (
    .in0(IR[25:21]), .in1(5'b00010), .out(multiplexer_9_out), .sel(syscall));
  Multiplexer #(.select(1), .width(5), .disabled("Z"), .enable("false")) multiplexer_10 (
    .in0(IR[20:16]), .in1(5'b00100), .out(multiplexer_10_out), .sel(syscall));
  Multiplexer #(.select(1), .width(5), .disabled("Z"), .enable("false")) multiplexer_11 (
    .in0(multiplexer_7_out), .in1({5{1'b1}}), .out(multiplexer_11_out), .sel(JAL));
  Multiplexer #(.select(1), .width(32), .disabled("Z"), .enable("false")) multiplexer_12 (
    .in0(multiplexer_15_out), .in1(PC_4), .out(RDin), .sel(JAL));
  // Probe on PCout
  Register #(.width(2), .trigger("rising"), .Select("low")) cause (
    .D(priority_encoder_1_out), .en(and_10_out), .Q(IR_now), .clk(CLK), .clr(comparator_6_eq));
  // Probe on MDin
  or or_10 (JMP_IF, and_11_out, and_12_out);
  Comparator #(.width(2), .mode("twosComplement")) comparator_6 (
    .a(priority_encoder_1_out), .b(2'b00), .eq(comparator_6_eq));  // open: gt, lt
  // Probe on LedData
  MIPS_Regifile mips_regifile_1 (
    .Din(RDin), .Clk(CLK), .R1(PC_JR), .R2(A0), .WE(RegWrite), .W_num(multiplexer_11_out),
    .R1_num(multiplexer_9_out), .R2_num(multiplexer_10_out));
  assign bit_extender_1_out = {{16{1'b0}}, IR[15:0]};  // Bit_Extender bit_extender_1
  assign bit_extender_2_out = {{16{IR[15]}}, IR[15:0]};  // Bit_Extender bit_extender_2
  Shifter #(.width(32), .shift("ll")) shifter_2 (.in(bit_extender_2_out), .\dist (5'b00010), .out(shifter_2_out));
  Button u_RST (.out(RST));
  Multiplexer #(.select(2), .width(32), .disabled("Z"), .enable("false")) multiplexer_13 (
    .in0(A0), .in1(A0), .in2(bit_extender_1_out), .in3(bit_extender_2_out), .out(multiplexer_13_out),
    .sel({\单周期硬布线控制器_1_alu_src [1], SignedExt}));
  Multiplexer #(.select(1), .width(32), .disabled("Z"), .enable("false")) multiplexer_14 (
    .in0(multiplexer_13_out), .in1({32{1'b0}}), .out(multiplexer_14_out), .sel(BGEZ));
  Adder #(.width(32)) adder_2 (.a(shifter_2_out), .b(PC_4), .out(PC_imm));  // open: cin, cout
  or or_11 (IR1_t, IR1, IRA);
  MIPS_ALU mips_alu_1 (
    .X(PC_JR), .Y(multiplexer_14_out), .AluOP(\单周期硬布线控制器_1_alu_op ), .Equal(equal),
    .Result(mips_alu_1_result), .shamt(IR[10:6]));  // open: Result_2
  or or_12 (IR2_t, IR2, IRB);
  not not_5 (BGEZ_YES, mips_alu_1_result[0]);
  or or_13 (IR3_t, IR3, IRC);
  RAM #(.addrWidth(10), .dataWidth(32), .bus("separate"), .Select("high")) ram_1 (
    .addr(mips_alu_1_result[11:2]), .din(MDin), .data(MOUT), .str(MemWrite), .clk(CLK), .clr(RST));  // open: sel, ld
  Multiplexer #(.select(1), .width(32), .disabled("Z"), .enable("false")) multiplexer_15 (
    .in0(mips_alu_1_result), .in1(MOUT), .out(multiplexer_15_out), .sel(\单周期硬布线控制器_1_memtoreg ));

  // Other names for the same wires on the sheet: addr[25:0] = IR[25:0]; imm[15:0] = IR[15:0];
  //   PC_J[31:2] = {PC_4[31:28], IR[25:0]}; shamt[4:0] = IR[10:6]; V0[31:0] = PC_JR

  // Notes on the sheet:
  //   中断源
  //   中断等待指示
  //   单级中断测试信号模拟器
  //   数码管输出
  //   Reset 
  //   Reset 
  //   Reset 
  //   指令存储器
  //   OP
  //   Func
  //   rs
  //   指令字
  //   contents of rom_1 (hex, n*v repeats v):
  //   201d07d0 20100001 109fc0 139fc3 8021 2012000c 24160008 26100001 3210000f 20080008 20090001 139900
  //   2709825 132020 20020022 c 1094022 1500fff9 22100001 2018000f 2188024 108700 20080008 20090001 139902
  //   2709825 132021 20020022 c 1094022 1500fff9 108702 2c9b022 12c00001 8000c07 4020 1084027 84400
  //   3508ffff 82021 20020022 c 8000c01 afa20000 23bd0004 afa40000 23bd0004 afb00000 23bd0004 afb30000
  //   23bd0004 afb40000 23bd0004 afb50000 23bd0004 afb60000 23bd0004 20160001 20140003 20150001 168020
  //   108100 2149825 132020 20020022 c 1600fffa 295a022 1680fff7 23bdfffc 8fb60000 23bdfffc 8fb50000
  //   23bdfffc 8fb40000 23bdfffc 8fb30000 23bdfffc 8fb00000 23bdfffc 8fa40000 23bdfffc 8fa20000 42000018
  //   afa20000 23bd0004 afa40000 23bd0004 afb00000 23bd0004 afb30000 23bd0004 afb40000 23bd0004 afb50000
  //   23bd0004 afb60000 23bd0004 20160002 20140003 20150001 168020 108100 2149825 132020 20020022 c
  //   1600fffa 295a022 1680fff7 23bdfffc 8fb60000 23bdfffc 8fb50000 23bdfffc 8fb40000 23bdfffc 8fb30000
  //   23bdfffc 8fb00000 23bdfffc 8fa40000 23bdfffc 8fa20000 42000018 afa20000 23bd0004 afa40000 23bd0004
  //   afb00000 23bd0004 afb30000 23bd0004 afb40000 23bd0004 afb50000 23bd0004 afb60000 23bd0004 20160003
  //   20140003 20150001 168020 108100 2149825 132020 20020022 c 1600fffa 295a022 1680fff7 23bdfffc
  //   8fb60000 23bdfffc 8fb50000 23bdfffc 8fb40000 23bdfffc 8fb30000 23bdfffc 8fb00000 23bdfffc 8fa40000
  //   23bdfffc 8fa20000 42000018
  //   rt
  //   rd
  //   IR
  //   IE
  //   JMP
  //   JR
  //   OP
  //   Func
  //   Beq
  //   Bne
  //   MemToReg
  //   MemWrite
  //   AluOP
  //   AluSrcB
  //   RegWrite
  //   JAL
  //   RegDst
  //   Syscall
  //   为方便自动评测，需要输出PC，IR，寄存器堆写如数据RDin
  //   RAM写使能MemWrite、RAM写入数据MDin等信号
  //   总复位信号应将除ROM以外所有存储组件全部清零
  //   数码管输出应该用寄存器锁存，否则显示数据只能一闪而过
endmodule

module \单周期MIPS_多级中断  (
  input  IR1,
  input  IR2,
  input  IR3,
  output RegWrite,
  output MemWrite,
  output [31:0] PC,
  output [31:0] IR,
  output [31:0] RDin,
  output [31:0] MDin,
  output [31:0] LedData
);

  wire and_3_out, and_4_out, and_5_out, and_9_out, and_10_out, BEQ, BGEZ, BGEZ_YES, BNE, CLK,
       comparator_1_eq, comparator_2_eq, comparator_3_eq, comparator_4_eq, comparator_5_eq, comparator_6_eq,
       comparator_7_gt, d_ff_1_q, d_ff_2_q, d_ff_3_q, decoder_1_out1, decoder_1_out2, decoder_1_out3, equal,
       ERET, Go, halt, IE_Ctrl, IE_q, IR1_q, IR1_t, IR2_q, IR2_t, IR3_q, IR3_t, IRA, IRB, IRC, JAL, JMP,
       JMP_IF, JR, LED, MFC0, MTC0, not_1_out, not_2_out, not_3_out, not_4_out, or_1_out, or_2_out, or_9_out,
       or_10_out, or_11_out, or_12_out, or_14_out, or_15_out, or_16_out, priority_encoder_1_gs, RegDst, RST,
       RST1, RST2, RST3, SB, SignedExt, syscall, W1, W2, W3, \单周期硬布线控制器_1_memtoreg ;
  wire [1:0] multiplexer_14_out, multiplexer_17_out, multiplexer_19_out, register_3_q, register_4_q, \当前中断号 ,
       \当前最优中断号 ;
  wire [1:1] \单周期硬布线控制器_1_alu_src ;
  wire [3:0] \单周期硬布线控制器_1_alu_op ;
  wire [4:0] multiplexer_4_out, multiplexer_5_out, multiplexer_6_out, multiplexer_7_out;
  wire [15:0] \总周期数 ;
  wire [31:0] A0, bit_extender_1_out, bit_extender_2_out, EPC, EPC2_q, EPC3_q, mips_alu_1_result, MOUT,
       multiplexer_1_out, multiplexer_9_out, multiplexer_10_out, multiplexer_12_out, multiplexer_13_out,
       multiplexer_15_out, multiplexer_16_out, multiplexer_18_out, multiplexer_20_out, nextPC, PC_4, PC_imm,
       PC_JR, PCout, shifter_1_out, shifter_2_out;

  Clock #(.highDuration(1), .lowDuration(1)) clock_1 (.out(CLK));
  Button _1 ();  // open: out
  Button _2 ();  // open: out
  Button _3 ();  // open: out
  Button \u_继续运行  (.out(Go));
  LED #(.active("true")) led_1 (.in(W1));
  LED #(.active("true")) led_2 (.in(W2));
  LED #(.active("true")) led_3 (.in(W3));
  Hex_Digit_Display hex_digit_display_1 (.value(LedData[31:28]));  // open: dp
  Comparator #(.width(16), .mode("twosComplement")) comparator_1 (
    .a(\总周期数 ), .b(16'h7), .eq(comparator_1_eq));  // open: gt, lt
  Comparator #(.width(16), .mode("twosComplement")) comparator_2 (
    .a(\总周期数 ), .b(16'h241), .eq(comparator_2_eq));  // open: gt, lt
  Hex_Digit_Display hex_digit_display_2 (.value(LedData[27:24]));  // open: dp
  Hex_Digit_Display hex_digit_display_3 (.value(LedData[23:20]));  // open: dp
  Comparator #(.width(16), .mode("twosComplement")) comparator_3 (
    .a(16'h258), .b(\总周期数 ), .eq(comparator_3_eq));  // open: gt, lt
  or or_1 (or_1_out, comparator_3_eq, comparator_4_eq);
  Comparator #(.width(16), .mode("twosComplement")) comparator_4 (
    .a(\总周期数 ), .b(16'h1), .eq(comparator_4_eq));  // open: gt, lt
  Comparator #(.width(16), .mode("twosComplement")) comparator_5 (
    .a(\总周期数 ), .b(16'h4), .eq(comparator_5_eq));  // open: gt, lt
  or or_2 (or_2_out, comparator_1_eq, comparator_2_eq);
  Hex_Digit_Display hex_digit_display_4 (.value(LedData[15:12]));  // open: dp
  Hex_Digit_Display hex_digit_display_5 (.value(LedData[19:16]));  // open: dp
  Pull_Resistor #(.pull(0)) pull_resistor_1 (.node(IRA));
  assign IRA = or_1_out ? ~CLK : 1'bz;  // Controlled_Inverter controlled_inverter_1
  Pull_Resistor #(.pull(0)) pull_resistor_2 (.node(IRB));
  assign IRB = comparator_5_eq ? ~CLK : 1'bz;  // Controlled_Inverter controlled_inverter_2
  Pull_Resistor #(.pull(0)) pull_resistor_3 (.node(IRC));
  assign IRC = or_2_out ? ~CLK : 1'bz;  // Controlled_Inverter controlled_inverter_3
  Hex_Digit_Display hex_digit_display_6 (.value(LedData[7:4]));  // open: dp
  Hex_Digit_Display hex_digit_display_7 (.value(LedData[11:8]));  // open: dp
  // Probe on \总周期数 
  Hex_Digit_Display hex_digit_display_8 (.value(LedData[3:0]));  // open: dp
  Button u_RST (.out(RST));
  or or_3 (IR1_t, IR1, IRA);
  or or_4 (IR2_t, IR2, IRB);
  Comparator #(.width(32), .mode("twosComplement")) comparator_6 (
    .a(PC_JR), .b(32'h22), .eq(comparator_6_eq));  // open: gt, lt
  and and_1 (LED, syscall, comparator_6_eq);
  and and_2 (halt, syscall, not_1_out);
  not not_1 (not_1_out, comparator_6_eq);
  D_Flip_Flop #(.trigger("rising"), .Pre_Clr_Positions("LEGACY"), .NegatePresetClear("false"), .enable("true"), .NewFFLayout("false")) d_ff_1 (
    .clk(IR1_t), .D(1'b1), .Q(d_ff_1_q), .reset(IR1_q));  // open: Qn, preset, en
  or or_5 (W1, IR1_q, d_ff_1_q);
  D_Flip_Flop #(.trigger("rising"), .Pre_Clr_Positions("LEGACY"), .NegatePresetClear("false"), .enable("true"), .NewFFLayout("false")) d_ff_2 (
    .clk(IR2_t), .D(1'b1), .Q(d_ff_2_q), .reset(IR2_q));  // open: Qn, preset, en
  or or_6 (W2, IR2_q, d_ff_2_q);
  D_Flip_Flop #(.trigger("rising"), .Pre_Clr_Positions("LEGACY"), .NegatePresetClear("false"), .enable("true"), .NewFFLayout("false")) d_ff_3 (
    .clk(IR3_t), .D(1'b1), .Q(d_ff_3_q), .reset(IR3_q));  // open: Qn, preset, en
  or or_7 (W3, IR3_q, d_ff_3_q);
  or or_8 (IR3_t, IR3, IRC);
  Multiplexer #(.select(3), .width(32), .disabled("Z"), .enable("false")) multiplexer_1 (
    .in0(PC_4), .in1(PC_imm), .in2({PC_4[31:28], IR[25:0], 2'b00}), .in6(PC_JR), .out(multiplexer_1_out),
    .sel({JR, JMP, JMP_IF}));  // open: in3, in4, in5, in7
  or or_9 (or_9_out, d_ff_1_q, IR1_q);
  or or_10 (or_10_out, d_ff_2_q, IR2_q);
  or or_11 (or_11_out, d_ff_3_q, IR3_q);
  not not_2 (not_2_out, halt);
  Multiplexer #(.select(2), .width(32), .disabled("Z"), .enable("false")) multiplexer_2 (
    .in0(multiplexer_1_out), .in1(multiplexer_1_out), .in2(PC_4), .in3(PC_imm), .out(nextPC),
    .sel({BGEZ, BGEZ_YES}));
  Shifter #(.width(32), .shift("ll")) shifter_1 (.in(MOUT), .\dist (5'b01000), .out(shifter_1_out));
  Counter #(.width(16), .max('hffff), .ongoal("wrap"), .trigger("rising"), .behavior("new")) counter_1 (
    .count(not_2_out), .Q(\总周期数 ), .clk(CLK), .clr(RST));  // open: load, D, carry, preset, down
  Register #(.width(32), .trigger("rising"), .Select("low")) u_PC (
    .D(PCout), .en(or_12_out), .Q(PC), .clk(CLK), .clr(RST));
  or or_12 (or_12_out, not_3_out, Go);
  not not_3 (not_3_out, halt);
  and and_3 (and_3_out, or_9_out, ~RST1);  // AND_Gate
  and and_4 (and_4_out, or_10_out, ~RST2);  // AND_Gate
  and and_5 (and_5_out, or_11_out, ~RST3);  // AND_Gate
  Multiplexer #(.select(1), .width(32), .disabled("Z"), .enable("false")) multiplexer_3 (
    .in0(A0), .in1({shifter_1_out[31:8], A0[7:0]}), .out(MDin), .sel(SB));
  // Mips_Probe mips_probe_1: pin names not known; wires that end beside it: {BGEZ, BGEZ_YES}, IR
  D_Flip_Flop #(.trigger("rising"), .Pre_Clr_Positions("LEGACY"), .NegatePresetClear("false"), .enable("true"), .NewFFLayout("false")) u_IR1 (
    .clk(CLK), .D(and_3_out), .Q(IR1_q));  // open: Qn, preset, en, reset
  D_Flip_Flop #(.trigger("rising"), .Pre_Clr_Positions("LEGACY"), .NegatePresetClear("false"), .enable("true"), .NewFFLayout("false")) u_IR2 (
    .clk(CLK), .D(and_4_out), .Q(IR2_q));  // open: Qn, preset, en, reset
  D_Flip_Flop #(.trigger("rising"), .Pre_Clr_Positions("LEGACY"), .NegatePresetClear("false"), .enable("true"), .NewFFLayout("false")) u_IR3 (
    .clk(CLK), .D(and_5_out), .Q(IR3_q));  // open: Qn, preset, en, reset
  ROM #(.addrWidth(10), .dataWidth(32), .Select("high")) rom_1 (.addr(PC[11:2]), .data(IR));
  Priority_Encoder #(.select(2), .disabled("Z")) priority_encoder_1 (
    .in0(1'b1), .in1(IR1_q), .in2(IR2_q), .in3(IR3_q), .out(\当前最优中断号 ), .gs(priority_encoder_1_gs));  // open: en_out, en_in
  Adder #(.width(32)) adder_1 (.a(PC), .b(32'h4), .out(PC_4));  // open: cin, cout
  Register #(.width(32), .trigger("rising"), .Select("low")) register_1 (
    .D(A0), .en(LED), .Q(LedData), .clk(CLK), .clr(RST));
  Decoder #(.select(2), .tristate("false"), .disabled("Z"), .enable("false")) decoder_1 (
    .out1(decoder_1_out1), .out2(decoder_1_out2), .out3(decoder_1_out3), .sel(\当前最优中断号 ));  // open: out0
  Multistage_interrupt_control_logic multistage_interrupt_control_logic_1 (
    .OP(IR[31:26]), .Func(IR[5:0]), .MF(IR[25:21]), .MFC0(MFC0), .MTC0(MTC0));
  and and_6 (RST1, decoder_1_out1, ERET);
  and and_7 (RST2, decoder_1_out2, ERET);
  and and_8 (RST3, decoder_1_out3, ERET);
  Multiplexer #(.select(1), .width(5), .disabled("Z"), .enable("false")) multiplexer_4 (
    .in0(IR[20:16]), .in1(IR[15:11]), .out(multiplexer_4_out), .sel(RegDst));
  and and_9 (and_9_out, BEQ, equal);
  and and_10 (and_10_out, BNE, not_4_out);
  not not_4 (not_4_out, equal);
  \单周期硬布线控制器  \u_单周期硬布线控制器_1  (
    .Func(IR[5:0]), .OP(IR[31:26]), .ALU_OP(\单周期硬布线控制器_1_alu_op ), .MemToReg(\单周期硬布线控制器_1_memtoreg ),
    .MemWrite(MemWrite), .ALU_SRC(\单周期硬布线控制器_1_alu_src [1]), .RegWrite(RegWrite), .SysCALL(syscall),
    .SignedExt(SignedExt), .RegDst(RegDst), .JR(JR), .JMP(JMP), .Beq(BEQ), .JAL(JAL), .Bne(BNE), .BGEZ(BGEZ),
    .SB(SB), .ERET(ERET));
  Multiplexer #(.select(1), .width(5), .disabled("Z"), .enable("false")) multiplexer_5 (
    .in0(IR[25:21]), .in1(5'b00010), .out(multiplexer_5_out), .sel(syscall));
  Multiplexer #(.select(1), .width(5), .disabled("Z"), .enable("false")) multiplexer_6 (
    .in0(IR[20:16]), .in1(5'b00100), .out(multiplexer_6_out), .sel(syscall));
  Multiplexer #(.select(1), .width(5), .disabled("Z"), .enable("false")) multiplexer_7 (
    .in0(multiplexer_4_out), .in1({5{1'b1}}), .out(multiplexer_7_out), .sel(JAL));
  or or_13 (JMP_IF, and_9_out, and_10_out);
  Multiplexer #(.select(1), .width(32), .disabled("Z"), .enable("false")) multiplexer_8 (
    .in0(multiplexer_16_out), .in1(PC_4), .out(RDin), .sel(JAL));
  Multiplexer #(.select(2), .width(32), .disabled("Z"), .enable("true")) multiplexer_9 (
    .in0(nextPC), .in1(32'h30ac), .in2(32'h3158), .in3(32'h3204), .out(multiplexer_9_out), .sel(\当前最优中断号 ),
    .en(priority_encoder_1_gs));
  MIPS_Regifile mips_regifile_1 (
    .Din(RDin), .Clk(CLK), .R1(PC_JR), .R2(A0), .WE(RegWrite), .W_num(multiplexer_7_out),
    .R1_num(multiplexer_5_out), .R2_num(multiplexer_6_out));
  assign bit_extender_1_out = {{16{1'b0}}, IR[15:0]};  // Bit_Extender bit_extender_1
  assign bit_extender_2_out = {{16{IR[15]}}, IR[15:0]};  // Bit_Extender bit_extender_2
  Multiplexer #(.select(1), .width(32), .disabled("Z"), .enable("false")) multiplexer_10 (
    .in0(nextPC), .in1(multiplexer_9_out), .out(multiplexer_10_out), .sel(IE_Ctrl));
  Shifter #(.width(32), .shift("ll")) shifter_2 (.in(bit_extender_2_out), .\dist (5'b00010), .out(shifter_2_out));
  Multiplexer #(.select(1), .width(32), .disabled("Z"), .enable("false")) multiplexer_11 (
    .in0(multiplexer_10_out), .in1(EPC), .out(PCout), .sel(ERET));
  Multiplexer #(.select(2), .width(32), .disabled("Z"), .enable("false")) multiplexer_12 (
    .in0(A0), .in1(A0), .in2(bit_extender_1_out), .in3(bit_extender_2_out), .out(multiplexer_12_out),
    .sel({\单周期硬布线控制器_1_alu_src [1], SignedExt}));
  Adder #(.width(32)) adder_2 (.a(shifter_2_out), .b(PC_4), .out(PC_imm));  // open: cin, cout
  // Probe on PCout
  Multiplexer #(.select(1), .width(32), .disabled("Z"), .enable("false")) multiplexer_13 (
    .in0(multiplexer_12_out), .in1({32{1'b0}}), .out(multiplexer_13_out), .sel(BGEZ));
  MIPS_ALU mips_alu_1 (
    .X(PC_JR), .Y(multiplexer_13_out), .AluOP(\单周期硬布线控制器_1_alu_op ), .Equal(equal),
    .Result(mips_alu_1_result), .shamt(IR[10:6]));  // open: Result_2
  not not_5 (BGEZ_YES, mips_alu_1_result[0]);
  or or_14 (or_14_out, ERET, IE_Ctrl);
  RAM #(.addrWidth(10), .dataWidth(32), .bus("separate"), .Select("high")) ram_1 (
    .addr(mips_alu_1_result[11:2]), .din(MDin), .data(MOUT), .str(MemWrite), .clk(CLK), .clr(RST));  // open: sel, ld
  or or_15 (or_15_out, ERET, MFC0, MTC0, IE_Ctrl);
  Multiplexer #(.select(1), .width(2), .disabled("Z"), .enable("false")) multiplexer_14 (
    .in0(\当前最优中断号 ), .in1(register_3_q), .out(multiplexer_14_out), .sel(ERET));
  Multiplexer #(.select(1), .width(32), .disabled("Z"), .enable("false")) multiplexer_15 (
    .in0(nextPC), .in1(EPC2_q), .out(multiplexer_15_out), .sel(ERET));
  Multiplexer #(.select(1), .width(32), .disabled("Z"), .enable("false")) multiplexer_16 (
    .in0(mips_alu_1_result), .in1(MOUT), .out(multiplexer_16_out), .sel(\单周期硬布线控制器_1_memtoreg ));
  or or_16 (or_16_out, MTC0, IE_Ctrl);
  Register #(.width(1), .trigger("rising"), .Select("low")) IE (
    .D(or_16_out), .en(or_15_out), .Q(IE_q), .clk(CLK));  // open: clr
  Comparator #(.width(2), .mode("unsigned")) comparator_7 (
    .a(\当前最优中断号 ), .b(\当前中断号 ), .gt(comparator_7_gt));  // open: eq, lt
  Register #(.width(2), .trigger("rising"), .Select("low")) register_2 (
    .D(multiplexer_14_out), .en(or_14_out), .Q(\当前中断号 ), .clk(CLK));  // open: clr
  Register #(.width(32), .trigger("rising"), .Select("low")) EPC1 (
    .D(multiplexer_15_out), .en(or_14_out), .Q(EPC), .clk(CLK));  // open: clr
  and and_11 (IE_Ctrl, ~IE_q, comparator_7_gt);  // AND_Gate
  Multiplexer #(.select(1), .width(2), .disabled("Z"), .enable("false")) multiplexer_17 (
    .in0(\当前中断号 ), .in1(register_4_q), .out(multiplexer_17_out), .sel(ERET));
  Multiplexer #(.select(1), .width(32), .disabled("Z"), .enable("false")) multiplexer_18 (
    .in0(EPC), .in1(EPC3_q), .out(multiplexer_18_out), .sel(ERET));
  Register #(.width(2), .trigger("rising"), .Select("low")) register_3 (
    .D(multiplexer_17_out), .en(or_14_out), .Q(register_3_q), .clk(CLK));  // open: clr
  Register #(.width(32), .trigger("rising"), .Select("low")) EPC2 (
    .D(multiplexer_18_out), .en(or_14_out), .Q(EPC2_q), .clk(CLK));  // open: clr
  Multiplexer #(.select(1), .width(2), .disabled("Z"), .enable("false")) multiplexer_19 (
    .in0(register_3_q), .in1(2'b00), .out(multiplexer_19_out), .sel(ERET));
  Multiplexer #(.select(1), .width(32), .disabled("Z"), .enable("false")) multiplexer_20 (
    .in0(EPC2_q), .in1({32{1'b0}}), .out(multiplexer_20_out), .sel(ERET));
  Register #(.width(2), .trigger("rising"), .Select("low")) register_4 (
    .D(multiplexer_19_out), .en(or_14_out), .Q(register_4_q), .clk(CLK));  // open: clr
  Register #(.width(32), .trigger("rising"), .Select("low")) EPC3 (
    .D(multiplexer_20_out), .en(or_14_out), .Q(EPC3_q), .clk(CLK));  // open: clr

  // Other names for the same wires on the sheet: addr[25:0] = IR[25:0]; imm[15:0] = IR[15:0];
  //   PC_J[31:2] = {PC_4[31:28], IR[25:0]}; shamt[4:0] = IR[10:6]; V0[31:0] = PC_JR

  // Notes on the sheet:
  //   中断源
  //   中断等待指示
  //   总复位信号应将除ROM以外所有存储组件全部清零
  //   多级中断测试信号模拟器
  //   数码管输出
  //   数码管输出应该用寄存器锁存，否则显示数据只能一闪而过
  //   为方便自动评测，需要输出PC，IR，寄存器堆写如数据RDin
  //   Reset 
  //   Reset 
  //   Reset 
  //   RAM写使能MemWrite、RAM写入数据MDin等信号
  //   指令存储器
  //   指令字
  //   contents of rom_1 (hex, n*v repeats v):
  //   201d07d0 20100001 109fc0 139fc3 8021 2012000c 24160008 26100001 3210000f 20080008 20090001 139900
  //   2709825 132020 20020022 c 1094022 1500fff9 22100001 2018000f 2188024 108700 20080008 20090001 139902
  //   2709825 132021 20020022 c 1094022 1500fff9 108702 2c9b022 12c00001 8000c07 4020 1084027 84400
  //   3508ffff 82021 20020022 c 8000c01 afa20000 23bd0004 afa40000 23bd0004 afb00000 23bd0004 afb30000
  //   23bd0004 afb40000 23bd0004 afb50000 23bd0004 afb60000 23bd0004 40000000 20160001 20140003 20150001
  //   168020 108100 2149825 132020 20020022 c 1600fffa 295a022 1680fff7 40800000 23bdfffc 8fb60000
  //   23bdfffc 8fb50000 23bdfffc 8fb40000 23bdfffc 8fb30000 23bdfffc 8fb00000 23bdfffc 8fa40000 23bdfffc
  //   8fa20000 42000018 afa20000 23bd0004 afa40000 23bd0004 afb00000 23bd0004 afb30000 23bd0004 afb40000
  //   23bd0004 afb50000 23bd0004 afb60000 23bd0004 40000000 20160002 20140003 20150001 168020 108100
  //   2149825 132020 20020022 c 1600fffa 295a022 1680fff7 40800000 23bdfffc 8fb60000 23bdfffc 8fb50000
  //   23bdfffc 8fb40000 23bdfffc 8fb30000 23bdfffc 8fb00000 23bdfffc 8fa40000 23bdfffc 8fa20000 42000018
  //   afa20000 23bd0004 afa40000 23bd0004 afb00000 23bd0004 afb30000 23bd0004 afb40000 23bd0004 afb50000
  //   23bd0004 afb60000 23bd0004 40000000 20160003 20140003 20150001 168020 108100 2149825 132020 20020022
  //   c 1600fffa 295a022 1680fff7 40800000 23bdfffc 8fb60000 23bdfffc 8fb50000 23bdfffc 8fb40000 23bdfffc
  //   8fb30000 23bdfffc 8fb00000 23bdfffc 8fa40000 23bdfffc 8fa20000 42000018
  //   MF
  //   OP
  //   Func
  //   rs
  //   rt
  //   rd
  //   JMP
  //   JR
  //   OP
  //   Func
  //   Beq
  //   Bne
  //   MemToReg
  //   MemWrite
  //   AluOP
  //   AluSrcB
  //   RegWrite
  //   JAL
  //   RegDst
  //   Syscall
endmodule

module \流水中断控制逻辑  (
  input  [5:0] OP,
  input  [5:0] Func,
  input  [31:0] IR,
  output CHANGE_MEM_OR_RAM,
  output IS_NOP
);

  \流水中断控制器自动生成  \u_流水中断控制器自动生成_1  (
    .OP0(OP[0]), .OP1(OP[1]), .OP2(OP[2]), .OP3(OP[3]), .OP4(OP[4]), .OP5(OP[5]), .F0(Func[0]), .F1(Func[1]),
    .F2(Func[2]), .F3(Func[3]), .F4(Func[4]), .F5(Func[5]), .CHANGE_MEM_OR_RAM(CHANGE_MEM_OR_RAM));
  and and_1 (IS_NOP, ~IR[0], ~IR[1], ~IR[2], ~IR[3], ~IR[4], ~IR[5], ~IR[6], ~IR[7], ~IR[8], ~IR[9], ~IR[10], ~IR[11], ~IR[12], ~IR[13], ~IR[14], ~IR[15], ~IR[16], ~IR[17], ~IR[18], ~IR[19], ~IR[20], ~IR[21], ~IR[22], ~IR[23], ~IR[24], ~IR[25], ~IR[26], ~IR[27], ~IR[28], ~IR[29], ~IR[30], ~IR[31]);  // AND_Gate

  // Other names for the same wires on the sheet: OP_CODE[5:0] = OP
endmodule

module \流水中断控制器自动生成  (
  input  OP0,
  input  OP1,
  input  OP2,
  input  OP3,
  input  OP4,
  input  OP5,
  input  F0,
  input  F1,
  input  F2,
  input  F3,
  input  F4,
  input  F5,
  output CHANGE_MEM_OR_RAM
);

  wire and_1_out, and_2_out, and_3_out, and_4_out, and_5_out, and_6_out, and_7_out, and_8_out, and_9_out,
       and_10_out, and_11_out, and_12_out, and_13_out, and_14_out, and_15_out, and_16_out, and_17_out,
       and_18_out, and_19_out, and_20_out, and_21_out, and_22_out, not_1_out, not_2_out, not_3_out,
       not_4_out, not_5_out, not_6_out, not_7_out, not_8_out, not_9_out, not_10_out, not_11_out, not_12_out,
       not_13_out, not_14_out, not_15_out, not_16_out, not_17_out, not_18_out, not_19_out, not_20_out,
       not_21_out, not_22_out, not_23_out, not_24_out, not_25_out, not_26_out, not_27_out, not_28_out,
       not_29_out, not_30_out, not_31_out, not_32_out, not_33_out, not_34_out, not_35_out, not_36_out,
       not_37_out, not_38_out, not_39_out, not_40_out, not_41_out, not_42_out, not_43_out, not_44_out,
       not_45_out, not_46_out, not_47_out, not_48_out, not_49_out, not_50_out, not_51_out, not_52_out,
       not_53_out, not_54_out, not_55_out, not_56_out, not_57_out, not_58_out, not_59_out, not_60_out,
       not_61_out, not_62_out, not_63_out, not_64_out, not_65_out, not_66_out, not_67_out, not_68_out,
       not_69_out, not_70_out, not_71_out, not_72_out, not_73_out, not_74_out, not_75_out, not_76_out,
       not_77_out, not_78_out, not_79_out, not_80_out, not_81_out, not_82_out, not_83_out, not_84_out,
       not_85_out, not_86_out, not_87_out, not_88_out, not_89_out, not_90_out, not_91_out, not_92_out,
       not_93_out, not_94_out, not_95_out, not_96_out, not_97_out, not_98_out, not_99_out, not_100_out,
       not_101_out, not_102_out, not_103_out, not_104_out, not_105_out, not_106_out, not_107_out,
       not_108_out, not_109_out, not_110_out, not_111_out, not_112_out, not_113_out, not_114_out,
       not_115_out, not_116_out, not_117_out, not_118_out, not_119_out, not_120_out, not_121_out,
       not_122_out, not_123_out, not_124_out, not_125_out, not_126_out, not_127_out, not_128_out,
       not_129_out, not_130_out, not_131_out, not_132_out, not_133_out, not_134_out, not_135_out,
       not_136_out, not_137_out, not_138_out, not_139_out, not_140_out, not_141_out, not_142_out,
       not_143_out, not_144_out, not_145_out, not_146_out, not_147_out, not_148_out, not_149_out,
       not_150_out, not_151_out, not_152_out, not_153_out, not_154_out, not_155_out, not_156_out,
       not_157_out, not_158_out, not_159_out;

  not not_1 (not_1_out, OP5);
  not not_2 (not_2_out, OP4);
  not not_3 (not_3_out, OP3);
  not not_4 (not_4_out, OP2);
  not not_5 (not_5_out, OP1);
  not not_6 (not_6_out, OP0);
  not not_7 (not_7_out, F5);
  not not_8 (not_8_out, F4);
  not not_9 (not_9_out, F3);
  not not_10 (not_10_out, F2);
  not not_11 (not_11_out, F1);
  not not_12 (not_12_out, F0);
  not not_13 (not_13_out, OP5);
  not not_14 (not_14_out, OP4);
  not not_15 (not_15_out, OP3);
  not not_16 (not_16_out, OP2);
  not not_17 (not_17_out, OP1);
  not not_18 (not_18_out, OP0);
  not not_19 (not_19_out, F5);
  not not_20 (not_20_out, F4);
  not not_21 (not_21_out, F3);
  not not_22 (not_22_out, F2);
  not not_23 (not_23_out, OP5);
  not not_24 (not_24_out, OP4);
  not not_25 (not_25_out, OP3);
  not not_26 (not_26_out, OP2);
  not not_27 (not_27_out, OP1);
  not not_28 (not_28_out, OP0);
  not not_29 (not_29_out, F5);
  not not_30 (not_30_out, F4);
  not not_31 (not_31_out, F3);
  not not_32 (not_32_out, F2);
  not not_33 (not_33_out, F0);
  not not_34 (not_34_out, OP5);
  not not_35 (not_35_out, OP4);
  not not_36 (not_36_out, OP3);
  not not_37 (not_37_out, OP2);
  not not_38 (not_38_out, OP1);
  not not_39 (not_39_out, OP0);
  not not_40 (not_40_out, F4);
  not not_41 (not_41_out, F3);
  not not_42 (not_42_out, F2);
  not not_43 (not_43_out, F1);
  not not_44 (not_44_out, F0);
  not not_45 (not_45_out, OP5);
  not not_46 (not_46_out, OP4);
  not not_47 (not_47_out, OP3);
  not not_48 (not_48_out, OP2);
  not not_49 (not_49_out, OP1);
  not not_50 (not_50_out, OP0);
  not not_51 (not_51_out, F4);
  not not_52 (not_52_out, F3);
  not not_53 (not_53_out, F2);
  not not_54 (not_54_out, F1);
  not not_55 (not_55_out, OP5);
  not not_56 (not_56_out, OP4);
  not not_57 (not_57_out, OP3);
  not not_58 (not_58_out, OP2);
  not not_59 (not_59_out, OP1);
  not not_60 (not_60_out, OP0);
  not not_61 (not_61_out, F4);
  not not_62 (not_62_out, F3);
  not not_63 (not_63_out, F2);
  not not_64 (not_64_out, F0);
  not not_65 (not_65_out, OP5);
  not not_66 (not_66_out, OP4);
  not not_67 (not_67_out, OP3);
  not not_68 (not_68_out, OP2);
  not not_69 (not_69_out, OP1);
  not not_70 (not_70_out, OP0);
  not not_71 (not_71_out, F4);
  not not_72 (not_72_out, F3);
  not not_73 (not_73_out, F1);
  not not_74 (not_74_out, F0);
  not not_75 (not_75_out, OP5);
  not not_76 (not_76_out, OP4);
  not not_77 (not_77_out, OP3);
  not not_78 (not_78_out, OP2);
  not not_79 (not_79_out, OP1);
  not not_80 (not_80_out, OP0);
  not not_81 (not_81_out, F4);
  not not_82 (not_82_out, F3);
  not not_83 (not_83_out, F1);
  not not_84 (not_84_out, OP5);
  not not_85 (not_85_out, OP4);
  not not_86 (not_86_out, OP3);
  not not_87 (not_87_out, OP2);
  not not_88 (not_88_out, OP1);
  not not_89 (not_89_out, OP0);
  not not_90 (not_90_out, F4);
  not not_91 (not_91_out, F3);
  not not_92 (not_92_out, OP5);
  not not_93 (not_93_out, OP4);
  not not_94 (not_94_out, OP3);
  not not_95 (not_95_out, OP2);
  not not_96 (not_96_out, OP1);
  not not_97 (not_97_out, OP0);
  not not_98 (not_98_out, F4);
  not not_99 (not_99_out, F2);
  not not_100 (not_100_out, F0);
  not not_101 (not_101_out, OP5);
  not not_102 (not_102_out, OP4);
  not not_103 (not_103_out, OP3);
  not not_104 (not_104_out, OP2);
  not not_105 (not_105_out, OP1);
  not not_106 (not_106_out, OP0);
  not not_107 (not_107_out, F4);
  not not_108 (not_108_out, F2);
  not not_109 (not_109_out, OP5);
  not not_110 (not_110_out, OP4);
  not not_111 (not_111_out, OP3);
  not not_112 (not_112_out, OP2);
  not not_113 (not_113_out, OP5);
  not not_114 (not_114_out, OP4);
  not not_115 (not_115_out, OP2);
  not not_116 (not_116_out, OP1);
  not not_117 (not_117_out, OP0);
  not not_118 (not_118_out, OP5);
  not not_119 (not_119_out, OP4);
  not not_120 (not_120_out, OP1);
  not not_121 (not_121_out, OP0);
  not not_122 (not_122_out, OP5);
  not not_123 (not_123_out, OP4);
  not not_124 (not_124_out, OP2);
  not not_125 (not_125_out, OP1);
  not not_126 (not_126_out, OP5);
  not not_127 (not_127_out, OP4);
  not not_128 (not_128_out, OP2);
  not not_129 (not_129_out, OP0);
  not not_130 (not_130_out, OP5);
  not not_131 (not_131_out, OP4);
  not not_132 (not_132_out, OP1);
  not not_133 (not_133_out, OP4);
  not not_134 (not_134_out, OP3);
  not not_135 (not_135_out, OP2);
  not not_136 (not_136_out, OP4);
  not not_137 (not_137_out, OP2);
  not not_138 (not_138_out, OP5);
  not not_139 (not_139_out, OP4);
  not not_140 (not_140_out, OP3);
  not not_141 (not_141_out, OP2);
  not not_142 (not_142_out, OP1);
  not not_143 (not_143_out, OP0);
  not not_144 (not_144_out, F4);
  not not_145 (not_145_out, F3);
  not not_146 (not_146_out, F2);
  not not_147 (not_147_out, OP5);
  not not_148 (not_148_out, OP4);
  not not_149 (not_149_out, OP3);
  not not_150 (not_150_out, OP2);
  not not_151 (not_151_out, OP1);
  not not_152 (not_152_out, OP0);
  not not_153 (not_153_out, F4);
  not not_154 (not_154_out, F3);
  not not_155 (not_155_out, F0);
  not not_156 (not_156_out, OP4);
  not not_157 (not_157_out, OP2);
  not not_158 (not_158_out, OP1);
  not not_159 (not_159_out, OP0);
  and and_1 (and_1_out, not_1_out, not_2_out, not_3_out, not_4_out, not_5_out, not_6_out, not_7_out, not_8_out, not_9_out, not_10_out, not_11_out, not_12_out);
  and and_2 (and_2_out, not_13_out, not_14_out, not_15_out, not_16_out, not_17_out, not_18_out, not_19_out, not_20_out, not_21_out, not_22_out, F1, F0);
  and and_3 (and_3_out, not_23_out, not_24_out, not_25_out, not_26_out, not_27_out, not_28_out, not_29_out, not_30_out, not_31_out, not_32_out, F1, not_33_out);
  and and_4 (and_4_out, not_34_out, not_35_out, not_36_out, not_37_out, not_38_out, not_39_out, F5, not_40_out, not_41_out, not_42_out, not_43_out, not_44_out);
  and and_5 (and_5_out, not_45_out, not_46_out, not_47_out, not_48_out, not_49_out, not_50_out, F5, not_51_out, not_52_out, not_53_out, not_54_out, F0);
  and and_6 (and_6_out, not_55_out, not_56_out, not_57_out, not_58_out, not_59_out, not_60_out, F5, not_61_out, not_62_out, not_63_out, F1, not_64_out);
  and and_7 (and_7_out, not_65_out, not_66_out, not_67_out, not_68_out, not_69_out, not_70_out, F5, not_71_out, not_72_out, F2, not_73_out, not_74_out);
  and and_8 (and_8_out, not_75_out, not_76_out, not_77_out, not_78_out, not_79_out, not_80_out, F5, not_81_out, not_82_out, F2, not_83_out, F0);
  and and_9 (and_9_out, not_84_out, not_85_out, not_86_out, not_87_out, not_88_out, not_89_out, F5, not_90_out, not_91_out, F2, F1, F0);
  and and_10 (and_10_out, not_92_out, not_93_out, not_94_out, not_95_out, not_96_out, not_97_out, F5, not_98_out, F3, not_99_out, F1, not_100_out);
  and and_11 (and_11_out, not_101_out, not_102_out, not_103_out, not_104_out, not_105_out, not_106_out, F5, not_107_out, F3, not_108_out, F1, F0);
  and and_12 (and_12_out, not_109_out, not_110_out, not_111_out, not_112_out, OP1, OP0);
  and and_13 (and_13_out, not_113_out, not_114_out, OP3, not_115_out, not_116_out, not_117_out);
  and and_14 (and_14_out, not_118_out, not_119_out, OP3, OP2, not_120_out, not_121_out);
  and and_15 (and_15_out, not_122_out, not_123_out, OP3, not_124_out, not_125_out, OP0);
  and and_16 (and_16_out, not_126_out, not_127_out, OP3, not_128_out, OP1, not_129_out);
  and and_17 (and_17_out, not_130_out, not_131_out, OP3, OP2, not_132_out, OP0);
  and and_18 (and_18_out, OP5, not_133_out, not_134_out, not_135_out, OP1, OP0);
  and and_19 (and_19_out, OP5, not_136_out, OP3, not_137_out, OP1, OP0);
  and and_20 (and_20_out, not_138_out, not_139_out, not_140_out, not_141_out, not_142_out, not_143_out, F5, not_144_out, not_145_out, not_146_out, F1, F0);
  and and_21 (and_21_out, not_147_out, not_148_out, not_149_out, not_150_out, not_151_out, not_152_out, F5, not_153_out, not_154_out, F2, F1, not_155_out);
  and and_22 (and_22_out, OP5, not_156_out, OP3, not_157_out, not_158_out, not_159_out);
  or or_1 (CHANGE_MEM_OR_RAM, and_1_out, and_2_out, and_3_out, and_4_out, and_5_out, and_6_out, and_7_out, and_8_out, and_9_out, and_10_out, and_11_out, and_12_out, and_13_out, and_14_out, and_15_out, and_16_out, and_17_out, and_18_out, and_19_out, and_20_out, and_21_out, and_22_out);
endmodule
module \流水中断  (
  input  IR1,
  input  IR2,
  input  IR3,
  output RegWrite,
  output MemWrite,
  output [31:0] IF_PC,
  output [31:0] ID_PC,
  output [31:0] EX_PC,
  output [31:0] M_PC,
  output [31:0] WB_PC,
  output [31:0] RDin,
  output [31:0] MDin,
  output [31:0] LedData
);

  wire ALL_JUMP, and_1_out, and_2_out, and_3_out, and_4_out, and_5_out, and_6_out, and_7_out, and_8_out,
       and_9_out, and_10_out, and_11_out, and_12_out, and_13_out, and_14_out, and_15_out, BGEZ, BGEZ_YES,
       CHANGE, CLK, clock_1_out, clock_2_out, comparator_1_eq, comparator_2_eq, comparator_3_eq,
       comparator_4_eq, comparator_5_eq, comparator_7_eq, comparator_7_lt, d_ff_1_q, d_ff_2_q, d_ff_3_q,
       d_ff_4_q, ERET, ex_mem_1_halt_out, ex_mem_1_jal_out, ex_mem_1_memtoreg_out, ex_mem_1_regdst_out,
       ex_mem_1_sb_out, EX_NOP, EX_Regwrite, EX_SYSCALL, Go, halt, id_ex_1_beq_out, id_ex_1_bne_out,
       id_ex_1_change_mem_or_ram_out, id_ex_1_jal_out, id_ex_1_memtoreg_out, id_ex_1_memwrite_out,
       id_ex_1_regdst_out, id_ex_1_sb_out, ID_JAL, ID_RDst, INTERUPT_STATE, IR1_q, IR1_t, IR2_q, IR2_t,
       IR3_q, IR3_t, IRA, IRB, IRC, LED, Load_Use, MEM_CHANGE, MEM_Regwrite, mem_wb_1_halt_out,
       mem_wb_1_jal_out, mem_wb_1_memtoreg_out, mem_wb_1_regdst_out, mips_alu_1_equal, multiplexer_9_out,
       multiplexer_12_out, nand_1_out, not_1_out, not_2_out, not_3_out, not_4_out, not_6_out, not_7_out,
       not_8_out, or_1_out, or_2_out, or_6_out, or_7_out, or_8_out, or_10_out, or_12_out, or_15_out,
       or_18_out, or_19_out, or_20_out, priority_encoder_1_gs, READY_CHANGE, register_4_q, RST, SYSEQUAL, W1,
       W2, W3, WB_CHANGE, \中断状态_q , \单周期硬布线控制器_1_alu_src , \单周期硬布线控制器_1_beq , \单周期硬布线控制器_1_bgez ,
       \单周期硬布线控制器_1_bne , \单周期硬布线控制器_1_jmp , \单周期硬布线控制器_1_jr , \单周期硬布线控制器_1_memtoreg ,
       \单周期硬布线控制器_1_memwrite , \单周期硬布线控制器_1_regwrite , \单周期硬布线控制器_1_sb , \单周期硬布线控制器_1_signedext ,
       \单周期硬布线控制器_1_syscall , \流水中断控制逻辑_1_change_mem_or_ram , \流水中断控制逻辑_1_is_nop ;
  wire [1:0] id_ex_1_signedext_out, IR_now, priority_encoder_1_out, R1_FORWARD, R2_FORWARD,
       redirect_signal_logic_1_r1_forward, redirect_signal_logic_1_r2_forward;
  wire [2:0] or_16_out;
  wire [3:0] id_ex_1_aluop_out, if_id_1_pc_out_2, \单周期硬布线控制器_1_alu_op ;
  wire [4:0] EX_W_num, id_ex_1_shamt_out, ID_R1_num, ID_R2_num, MEM_W_num, multiplexer_1_out,
       multiplexer_2_out, multiplexer_5_out, multiplexer_8_out, multiplexer_21_out, W_num, WB_W_num;
  wire [5:0] EX_FUNC, ID_FUNC;
  wire [12:0] CNT_num;
  wire [15:0] id_ex_1_imm_out, \LoadUse次数 , \总周期数 , \插入气泡数 , \无条件分支数 , \条件分支成功数 ;
  wire [27:0] if_id_1_pc_out;
  wire [31:0] A0, adder_1_out, adder_2_out, bit_extender_1_out, bit_extender_2_out, EPC_q, ex_mem_1_pc_out,
       ex_mem_1_r2_out, id_ex_1_address_out, id_ex_1_pc_out, id_ex_1_r1_out, id_ex_1_r2_out, IF_IR, MEM_ALU,
       MEM_IR, mem_wb_1_alur_out, mem_wb_1_memd_out, mem_wb_1_pc_out_2, mips_alu_1_result,
       mips_regifile_1_r1, multiplexer_3_out, multiplexer_10_out, multiplexer_11_out, multiplexer_13_out,
       multiplexer_15_out, multiplexer_16_out, multiplexer_17_out, multiplexer_18_out, nextPC, PCout,
       ram_1_data, shifter_1_out, shifter_2_out, WB_IR, WB_TOREG;
  wire [31:6] EX_IR, ID_IR;

  Button \u_总复位  (.out(RST));
  Button _1 ();  // open: out
  Button _2 ();  // open: out
  Button _3 ();  // open: out
  // Probe on \总周期数 
  // Probe on \总周期数 
  Button \u_继续运行  (.out(Go));
  LED #(.active("true")) led_1 (.in(W1));
  LED #(.active("true")) led_2 (.in(W2));
  LED #(.active("true")) led_3 (.in(W3));
  Hex_Digit_Display hex_digit_display_1 (.value(LedData[31:28]));  // open: dp
  // Probe on IF_PC[19:0]
  // Mips_Probe mips_probe_1: pin names not known; wires that end beside it: IR1_t, IR2_t, IR3_t, IF_IR
  Multiplexer #(.select(1), .width(5), .disabled("Z"), .enable("false")) multiplexer_1 (
    .in0(EX_IR[25:21]), .in1(5'b00010), .out(multiplexer_1_out), .sel(EX_SYSCALL));
  Multiplexer #(.select(1), .width(5), .disabled("Z"), .enable("false")) multiplexer_2 (
    .in0(EX_IR[20:16]), .in1(5'b00100), .out(multiplexer_2_out), .sel(EX_SYSCALL));
  Hex_Digit_Display hex_digit_display_2 (.value(LedData[27:24]));  // open: dp
  Hex_Digit_Display hex_digit_display_3 (.value(LedData[23:20]));  // open: dp
  // Probe on ID_PC[19:0]
  // Mips_Probe mips_probe_2: pin names not known; wires that end beside it: {ID_IR, ID_FUNC}
  Multiplexer #(.select(3), .width(32), .disabled("Z"), .enable("false")) multiplexer_3 (
    .in0(adder_1_out), .in1(adder_2_out), .in2(id_ex_1_address_out), .in6(multiplexer_18_out),
    .out(multiplexer_3_out), .sel(or_16_out));  // open: in3, in4, in5, in7
  Comparator #(.width(16), .mode("twosComplement")) comparator_1 (
    .a(16'h23b), .b(\总周期数 ), .eq(comparator_1_eq));  // open: gt, lt
  or or_1 (or_1_out, comparator_1_eq, comparator_2_eq);
  Comparator #(.width(16), .mode("twosComplement")) comparator_2 (
    .a(\总周期数 ), .b(16'h1), .eq(comparator_2_eq));  // open: gt, lt
  Comparator #(.width(16), .mode("twosComplement")) comparator_3 (
    .a(\总周期数 ), .b(16'h4), .eq(comparator_3_eq));  // open: gt, lt
  Comparator #(.width(16), .mode("twosComplement")) comparator_4 (
    .a(\总周期数 ), .b(16'h6), .eq(comparator_4_eq));  // open: gt, lt
  Hex_Digit_Display hex_digit_display_4 (.value(LedData[19:16]));  // open: dp
  Hex_Digit_Display hex_digit_display_5 (.value(LedData[15:12]));  // open: dp
  Redirect_signal_logic redirect_signal_logic_1 (
    .ID_OP(ID_IR[31:26]), .ID_FUNC(ID_FUNC), .ID_R1_num(ID_R1_num), .ID_R2_num(ID_R2_num),
    .EX_W_num(EX_W_num), .MEM_W_num(MEM_W_num), .WB_W_num(WB_W_num), .EX_RegWrite(EX_Regwrite),
    .MEM_RegWrite(MEM_Regwrite), .WB_RegWrite(RegWrite), .EX_OP(EX_IR[31:26]), .EX_FUNC(EX_FUNC),
    .EX_R1_num(multiplexer_1_out), .EX_R2_num(multiplexer_2_out), .Load_Use(Load_Use),
    .R1_Forward(redirect_signal_logic_1_r1_forward), .R2_Forward(redirect_signal_logic_1_r2_forward));
  Multiplexer #(.select(2), .width(32), .disabled("Z"), .enable("false")) multiplexer_4 (
    .in0(multiplexer_3_out), .in1(multiplexer_3_out), .in2(adder_1_out), .in3(adder_2_out), .out(nextPC),
    .sel({BGEZ, BGEZ_YES}));
  not not_1 (not_1_out, Load_Use);
  Pull_Resistor #(.pull(0)) pull_resistor_1 (.node(IRA));
  assign IRA = or_1_out ? ~CLK : 1'bz;  // Controlled_Inverter controlled_inverter_1
  Pull_Resistor #(.pull(0)) pull_resistor_2 (.node(IRB));
  assign IRB = comparator_3_eq ? ~CLK : 1'bz;  // Controlled_Inverter controlled_inverter_2
  Pull_Resistor #(.pull(0)) pull_resistor_3 (.node(IRC));
  assign IRC = comparator_4_eq ? ~CLK : 1'bz;  // Controlled_Inverter controlled_inverter_3
  Hex_Digit_Display hex_digit_display_6 (.value(LedData[7:4]));  // open: dp
  Hex_Digit_Display hex_digit_display_7 (.value(LedData[11:8]));  // open: dp
  Clock #(.highDuration(1), .lowDuration(1)) clock_1 (.out(clock_1_out));
  // Probe on EX_PC[19:0]
  // Mips_Probe mips_probe_3: pin names not known; wires that end beside it: clock_1_out, {EX_IR, EX_FUNC}, CLK
  Register #(.width(4), .trigger("falling"), .Select("low")) register_1 (
    .D({redirect_signal_logic_1_r2_forward, redirect_signal_logic_1_r1_forward}),
    .Q({R2_FORWARD, R1_FORWARD}), .clk(CLK), .clr(RST));  // open: en
  or or_2 (or_2_out, CHANGE, not_1_out);
  and and_1 (and_1_out, or_2_out, halt);
  Hex_Digit_Display hex_digit_display_8 (.value(LedData[3:0]));  // open: dp
  Register #(.width(32), .trigger("rising"), .Select("low")) PC (
    .D(PCout), .en(and_1_out), .Q(IF_PC), .clk(CLK), .clr(RST));
  Counter #(.width(16), .max('hffff), .ongoal("wrap"), .trigger("rising"), .behavior("new")) counter_1 (
    .count(halt), .Q(\总周期数 ), .clk(CLK), .clr(RST));  // open: load, D, carry, preset, down
  // Probe on \总周期数 
  // Probe on M_PC[19:0]
  // Mips_Probe mips_probe_4: pin names not known; wires that end beside it: MEM_IR
  or or_3 (W1, IR1_q, d_ff_1_q);
  or or_4 (W2, IR2_q, d_ff_2_q);
  or or_5 (W3, IR3_q, d_ff_3_q);
  // Probe on \总周期数 
  // Probe on \无条件分支数 
  // Probe on \条件分支成功数 
  // Probe on \插入气泡数 
  // Probe on \LoadUse次数 
  Register #(.width(32), .trigger("rising"), .Select("low")) register_2 (
    .D(A0), .en(LED), .Q(LedData), .clk(CLK), .clr(RST));
  D_Flip_Flop #(.trigger("rising"), .Pre_Clr_Positions("LEGACY"), .NegatePresetClear("false"), .enable("true"), .NewFFLayout("false")) d_ff_1 (
    .clk(IR1_t), .D(1'b1), .Q(d_ff_1_q), .reset(IR1_q));  // open: Qn, preset, en
  D_Flip_Flop #(.trigger("rising"), .Pre_Clr_Positions("LEGACY"), .NegatePresetClear("false"), .enable("true"), .NewFFLayout("false")) d_ff_2 (
    .clk(IR2_t), .D(1'b1), .Q(d_ff_2_q), .reset(IR2_q));  // open: Qn, preset, en
  D_Flip_Flop #(.trigger("rising"), .Pre_Clr_Positions("LEGACY"), .NegatePresetClear("false"), .enable("true"), .NewFFLayout("false")) d_ff_3 (
    .clk(IR3_t), .D(1'b1), .Q(d_ff_3_q), .reset(IR3_q));  // open: Qn, preset, en
  // Probe on IF_PC[11:0]
  // Probe on WB_PC[19:0]
  // Mips_Probe mips_probe_5: pin names not known; wires that end beside it: WB_IR
  ROM #(.addrWidth(10), .dataWidth(32), .Select("high")) rom_1 (.addr(IF_PC[11:2]), .data(IF_IR));
  Adder #(.width(32)) adder_1 (.a(IF_PC), .b(32'h4), .out(adder_1_out));  // open: cin, cout
  or or_6 (or_6_out, d_ff_1_q, IR1_q);
  or or_7 (or_7_out, d_ff_2_q, IR2_q);
  or or_8 (or_8_out, d_ff_3_q, IR3_q);
  // Probe on ID_PC[11:0]
  // Probe on EX_PC[11:0]
  and and_2 (and_2_out, ERET, IR_now[0], ~IR_now[1]);  // AND_Gate
  and and_3 (and_3_out, ERET, ~IR_now[0], IR_now[1]);  // AND_Gate
  and and_4 (and_4_out, ERET, IR_now[0], IR_now[1]);
  // Probe on M_PC[11:0]
  or or_9 (IR1_t, IR1, IRA);
  or or_10 (or_10_out, RST, CHANGE, ALL_JUMP);
  IF_ID if_id_1 (
    .PC_in(adder_1_out), .IR_in(IF_IR), .CLK(CLK), .PC_out({if_id_1_pc_out_2, if_id_1_pc_out}),
    .IR_out({ID_IR, ID_FUNC}), .RST(or_10_out), .Enable(and_8_out), .PCb_in(IF_PC), .PCb_out(ID_PC));
  and and_5 (and_5_out, or_6_out, ~and_2_out);  // AND_Gate
  and and_6 (and_6_out, or_7_out, ~and_3_out);  // AND_Gate
  and and_7 (and_7_out, or_8_out, ~and_4_out);  // AND_Gate
  // Probe on WB_PC[11:0]
  or or_11 (IR2_t, IR2, IRB);
  or or_12 (or_12_out, CHANGE, not_2_out);
  not not_2 (not_2_out, Load_Use);
  and and_8 (and_8_out, or_12_out, halt);
  D_Flip_Flop #(.trigger("rising"), .Pre_Clr_Positions("LEGACY"), .NegatePresetClear("false"), .enable("true"), .NewFFLayout("false")) u_IR1 (
    .clk(CLK), .D(and_5_out), .Q(IR1_q));  // open: Qn, preset, en, reset
  D_Flip_Flop #(.trigger("rising"), .Pre_Clr_Positions("LEGACY"), .NegatePresetClear("false"), .enable("true"), .NewFFLayout("false")) u_IR2 (
    .clk(CLK), .D(and_6_out), .Q(IR2_q));  // open: Qn, preset, en, reset
  D_Flip_Flop #(.trigger("rising"), .Pre_Clr_Positions("LEGACY"), .NegatePresetClear("false"), .enable("true"), .NewFFLayout("false")) u_IR3 (
    .clk(CLK), .D(and_7_out), .Q(IR3_q));  // open: Qn, preset, en, reset
  Multiplexer #(.select(1), .width(5), .disabled("Z"), .enable("false")) multiplexer_5 (
    .in0(ID_IR[20:16]), .in1(ID_IR[15:11]), .out(multiplexer_5_out), .sel(ID_RDst));
  Priority_Encoder #(.select(2), .disabled("Z")) priority_encoder_1 (
    .in0(1'b1), .in1(IR1_q), .in2(IR2_q), .in3(IR3_q), .out(priority_encoder_1_out),
    .gs(priority_encoder_1_gs));  // open: en_out, en_in
  or or_13 (IR3_t, IR3, IRC);
  \单周期硬布线控制器  \u_单周期硬布线控制器_1  (
    .Func(ID_FUNC), .OP(ID_IR[31:26]), .ALU_OP(\单周期硬布线控制器_1_alu_op ), .MemToReg(\单周期硬布线控制器_1_memtoreg ),
    .MemWrite(\单周期硬布线控制器_1_memwrite ), .ALU_SRC(\单周期硬布线控制器_1_alu_src ), .RegWrite(\单周期硬布线控制器_1_regwrite ),
    .SysCALL(\单周期硬布线控制器_1_syscall ), .SignedExt(\单周期硬布线控制器_1_signedext ), .RegDst(ID_RDst),
    .JR(\单周期硬布线控制器_1_jr ), .JMP(\单周期硬布线控制器_1_jmp ), .Beq(\单周期硬布线控制器_1_beq ), .JAL(ID_JAL),
    .Bne(\单周期硬布线控制器_1_bne ), .BGEZ(\单周期硬布线控制器_1_bgez ), .SB(\单周期硬布线控制器_1_sb ), .ERET(ERET));
  Multiplexer #(.select(1), .width(5), .disabled("Z"), .enable("false")) multiplexer_6 (
    .in0(ID_IR[25:21]), .in1(5'b00010), .out(ID_R1_num), .sel(\单周期硬布线控制器_1_syscall ));
  Multiplexer #(.select(1), .width(5), .disabled("Z"), .enable("false")) multiplexer_7 (
    .in0(ID_IR[20:16]), .in1(5'b00100), .out(ID_R2_num), .sel(\单周期硬布线控制器_1_syscall ));
  Multiplexer #(.select(1), .width(5), .disabled("Z"), .enable("false")) multiplexer_8 (
    .in0(multiplexer_5_out), .in1({5{1'b1}}), .out(multiplexer_8_out), .sel(ID_JAL));
  // Probe on priority_encoder_1_out
  Multiplexer #(.select(2), .width(1), .disabled("Z"), .enable("false")) multiplexer_9 (
    .in0(1'b0), .in1(priority_encoder_1_gs), .in2(priority_encoder_1_gs), .in3(priority_encoder_1_gs),
    .out(multiplexer_9_out), .sel(priority_encoder_1_out));
  MIPS_Regifile mips_regifile_1 (
    .Din(RDin), .Clk(CLK), .R1(mips_regifile_1_r1), .R2(A0), .WE(RegWrite), .W_num(W_num),
    .R1_num(ID_R1_num), .R2_num(ID_R2_num));
  \流水中断控制逻辑  \u_流水中断控制逻辑_1  (
    .OP(ID_IR[31:26]), .Func(ID_FUNC), .IR({ID_IR, ID_FUNC}),
    .CHANGE_MEM_OR_RAM(\流水中断控制逻辑_1_change_mem_or_ram ), .IS_NOP(\流水中断控制逻辑_1_is_nop ));
  Multiplexer #(.select(1), .width(32), .disabled("Z"), .enable("false")) multiplexer_10 (
    .in0(nextPC), .in1(multiplexer_11_out), .out(multiplexer_10_out), .sel(CHANGE));
  Multiplexer #(.select(2), .width(32), .disabled("Z"), .enable("false")) multiplexer_11 (
    .in0(nextPC), .in1(32'h30ac), .in2(32'h3150), .in3(32'h31f4), .out(multiplexer_11_out),
    .sel(priority_encoder_1_out));
  and and_9 (and_9_out, and_10_out, ~ERET);  // AND_Gate
  and and_10 (and_10_out, multiplexer_9_out, ~\中断状态_q );  // AND_Gate
  or or_14 (INTERUPT_STATE, and_10_out, \中断状态_q );
  Register #(.width(1), .trigger("rising"), .Select("low")) \u_中断状态  (
    .D(INTERUPT_STATE), .Q(\中断状态_q ), .clk(CLK), .clr(ERET));  // open: en
  Multiplexer #(.select(1), .width(1), .disabled("Z"), .enable("false")) multiplexer_12 (
    .in0(\流水中断控制逻辑_1_change_mem_or_ram ), .in1(1'b0), .out(multiplexer_12_out), .sel(\流水中断控制逻辑_1_is_nop ));
  Multiplexer #(.select(1), .width(32), .disabled("Z"), .enable("false")) multiplexer_13 (
    .in0(EX_PC), .in1(ID_PC), .out(multiplexer_13_out), .sel(EX_NOP));
  or or_15 (or_15_out, RST, RST, Load_Use, CHANGE);
  ID_EX id_ex_1 (
    .IR_in({ID_IR, ID_FUNC}), .PC_in({if_id_1_pc_out_2, if_id_1_pc_out}), .BEQ_in(\单周期硬布线控制器_1_beq ),
    .R1_in(mips_regifile_1_r1), .BNE_in(\单周期硬布线控制器_1_bne ), .MemToReg_in(\单周期硬布线控制器_1_memtoreg ), .R2_in(A0),
    .MemWrite_in(\单周期硬布线控制器_1_memwrite ), .Imm_in({ID_IR[15:6], ID_FUNC}),
    .AluSrcB_in(\单周期硬布线控制器_1_alu_src ), .Address_in({if_id_1_pc_out_2, ID_IR[25:6], ID_FUNC, 2'b00}),
    .RegWrite_in(\单周期硬布线控制器_1_regwrite ), .AluOP_in(\单周期硬布线控制器_1_alu_op ), .JAL_in(ID_JAL),
    .Shamt_in(ID_IR[10:6]), .RegDst_in(ID_RDst), .SB_in(\单周期硬布线控制器_1_sb ), .JMP_in(\单周期硬布线控制器_1_jmp ),
    .BGEZ_in(\单周期硬布线控制器_1_bgez ), .W__in(multiplexer_8_out), .JR_in(\单周期硬布线控制器_1_jr ), .CLK(CLK),
    .IR_out({EX_IR, EX_FUNC}), .PC_out(id_ex_1_pc_out), .BEQ_out(id_ex_1_beq_out), .R1_out(id_ex_1_r1_out),
    .BNE_out(id_ex_1_bne_out), .MemToReg_out(id_ex_1_memtoreg_out), .R2_out(id_ex_1_r2_out),
    .MemWrite_out(id_ex_1_memwrite_out), .Imm_out(id_ex_1_imm_out), .AluSrcB_out(id_ex_1_signedext_out[1]),
    .Address_out(id_ex_1_address_out), .RegWrite_out(EX_Regwrite), .AluOP_out(id_ex_1_aluop_out),
    .JAL_out(id_ex_1_jal_out), .Shamt_out(id_ex_1_shamt_out), .RegDst_out(id_ex_1_regdst_out),
    .SB_out(id_ex_1_sb_out), .JMP_out(or_16_out[1]), .BGEZ_out(BGEZ), .W__out(EX_W_num),
    .JR_out(or_16_out[2]), .RST(or_15_out), .Enable(halt), .SignedEXT_in(\单周期硬布线控制器_1_signedext ),
    .SignedEXT_out(id_ex_1_signedext_out[0]), .PCb_in(ID_PC), .PCb_out(EX_PC),
    .SYSCALL(\单周期硬布线控制器_1_syscall ), .SYSCALL_2(EX_SYSCALL), .CHANGE_MEM_OR_RAM_in(multiplexer_12_out),
    .CHANGE_MEM_OR_RAM_out(id_ex_1_change_mem_or_ram_out));  // open: Halt_in, Halt_out
  Register #(.width(32), .trigger("rising"), .Select("low")) EPC (
    .D(multiplexer_13_out), .en(CHANGE), .Q(EPC_q), .clk(CLK));  // open: clr
  // Probe on PCout
  Multiplexer #(.select(1), .width(32), .disabled("Z"), .enable("false")) multiplexer_14 (
    .in0(multiplexer_10_out), .in1(EPC_q), .out(PCout), .sel(ERET));
  Register #(.width(2), .trigger("rising"), .Select("low")) cause (
    .D(priority_encoder_1_out), .en(and_9_out), .Q(IR_now), .clk(CLK), .clr(comparator_5_eq));
  not not_3 (not_3_out, mips_alu_1_equal);
  Multiplexer #(.select(2), .width(32), .disabled("Z"), .enable("false")) multiplexer_15 (
    .in0(id_ex_1_r2_out), .in1(MEM_ALU), .in2(WB_TOREG), .in3(WB_TOREG), .out(multiplexer_15_out),
    .sel(R2_FORWARD));
  Comparator #(.width(2), .mode("twosComplement")) comparator_5 (
    .a(priority_encoder_1_out), .b(2'b00), .eq(comparator_5_eq));  // open: gt, lt
  and and_11 (and_11_out, id_ex_1_beq_out, mips_alu_1_equal);
  and and_12 (and_12_out, id_ex_1_bne_out, not_3_out);
  assign bit_extender_1_out = {{16{1'b0}}, id_ex_1_imm_out};  // Bit_Extender bit_extender_1
  assign bit_extender_2_out = {{16{id_ex_1_imm_out[15]}}, id_ex_1_imm_out};  // Bit_Extender bit_extender_2
  or or_16 (or_16_out[0], and_11_out, and_12_out);
  Multiplexer #(.select(2), .width(32), .disabled("Z"), .enable("false")) multiplexer_16 (
    .in0(multiplexer_15_out), .in1(multiplexer_15_out), .in2(bit_extender_1_out), .in3(bit_extender_2_out),
    .out(multiplexer_16_out), .sel(id_ex_1_signedext_out));
  Multiplexer #(.select(1), .width(32), .disabled("Z"), .enable("false")) multiplexer_17 (
    .in0(multiplexer_16_out), .in1({32{1'b0}}), .out(multiplexer_17_out), .sel(BGEZ));
  \流水中断控制逻辑  \u_流水中断控制逻辑_2  (.IR({EX_IR, EX_FUNC}), .IS_NOP(EX_NOP));  // open: OP, Func, CHANGE_MEM_OR_RAM
  not not_4 (not_4_out, mips_alu_1_result[0]);
  and and_13 (and_13_out, not_4_out, BGEZ);
  Register #(.width(1), .trigger("falling"), .Select("low")) register_3 (
    .D(READY_CHANGE), .en(and_9_out), .Q(CHANGE), .clk(CLK), .clr(register_4_q));
  and and_14 (and_14_out, CHANGE, READY_CHANGE);
  Register #(.width(1), .trigger("rising"), .Select("low")) register_4 (
    .D(and_14_out), .Q(register_4_q), .clk(CLK));  // open: en, clr
  or or_17 (ALL_JUMP, or_16_out[2], or_16_out[1], or_16_out[0], and_13_out);
  Comparator #(.width(32), .mode("twosComplement")) comparator_6 (
    .a(32'h22), .b(multiplexer_18_out), .eq(SYSEQUAL));  // open: gt, lt
  Multiplexer #(.select(2), .width(32), .disabled("Z"), .enable("false")) multiplexer_18 (
    .in0(id_ex_1_r1_out), .in1(MEM_ALU), .in2(WB_TOREG), .in3(WB_TOREG), .out(multiplexer_18_out),
    .sel(R1_FORWARD));
  Shifter #(.width(32), .shift("ll")) shifter_1 (.in(bit_extender_2_out), .\dist (5'b00010), .out(shifter_1_out));
  Adder #(.width(32)) adder_2 (.a(shifter_1_out), .b(id_ex_1_pc_out), .out(adder_2_out));  // open: cin, cout
  MIPS_ALU mips_alu_1 (
    .X(multiplexer_18_out), .Y(multiplexer_17_out), .AluOP(id_ex_1_aluop_out), .Equal(mips_alu_1_equal),
    .Result(mips_alu_1_result), .shamt(id_ex_1_shamt_out));  // open: Result_2
  not not_5 (BGEZ_YES, mips_alu_1_result[0]);
  and and_15 (and_15_out, EX_SYSCALL, not_6_out);
  not not_6 (not_6_out, SYSEQUAL);
  and and_16 (LED, EX_SYSCALL, SYSEQUAL);
  D_Flip_Flop #(.trigger("high"), .Pre_Clr_Positions("LEGACY"), .NegatePresetClear("false"), .enable("true"), .NewFFLayout("false")) d_ff_4 (.Q(d_ff_4_q));  // open: clk, D, Qn, preset, en, reset
  // Probe on 13'hc
  or or_18 (or_18_out, RST, CHANGE);
  EX_MEM ex_mem_1 (
    .MemToReg_in(id_ex_1_memtoreg_out), .IR_in({EX_IR, EX_FUNC}), .MemWrite_in(id_ex_1_memwrite_out),
    .PC_in(id_ex_1_pc_out), .RegWrite_in(EX_Regwrite), .R2_in(multiplexer_15_out), .JAL_in(id_ex_1_jal_out),
    .AluR_in(mips_alu_1_result), .RegDst_in(id_ex_1_regdst_out), .Halt_in(and_15_out),
    .SB_in(id_ex_1_sb_out), .W__in(EX_W_num), .CLK(CLK), .MemToReg_out(ex_mem_1_memtoreg_out),
    .IR_out(MEM_IR), .MemWrite_out(MemWrite), .PC_out(ex_mem_1_pc_out), .RegWrite_out(MEM_Regwrite),
    .R2_out(ex_mem_1_r2_out), .JAL_out(ex_mem_1_jal_out), .AluR_out(MEM_ALU),
    .RegDst_out(ex_mem_1_regdst_out), .Halt_out(ex_mem_1_halt_out), .SB_out(ex_mem_1_sb_out),
    .W__out(MEM_W_num), .RST(or_18_out), .Enable(halt), .PCb_in(EX_PC), .PCb_out(M_PC),
    .CHANGE_MEM_OR_RAM_in(id_ex_1_change_mem_or_ram_out), .CHANGE_MEM_OR_RAM_out(MEM_CHANGE));
  Comparator #(.width(13), .mode("twosComplement")) comparator_7 (
    .a(CNT_num), .b(13'hc), .eq(comparator_7_eq), .lt(comparator_7_lt));  // open: gt
  Clock #(.highDuration(1), .lowDuration(1)) clock_2 (.out(clock_2_out));
  nand nand_1 (nand_1_out, d_ff_4_q, comparator_7_eq);
  Counter #(.width(13), .max('h1fff), .ongoal("stay"), .trigger("rising"), .behavior("old")) counter_2 (
    .count(comparator_7_lt), .Q(CNT_num), .clk(clock_2_out));  // open: load, D, carry, clr, preset
  Shifter #(.width(32), .shift("ll")) shifter_2 (.in(ram_1_data), .\dist (5'b01000), .out(shifter_2_out));
  assign CLK = nand_1_out ? clock_2_out : 1'bz;  // Controlled_Buffer controlled_buffer_1
  Pull_Resistor #(.pull(1)) pull_resistor_4 (.node(CLK));
  Multiplexer #(.select(1), .width(32), .disabled("Z"), .enable("false")) multiplexer_19 (
    .in0(ex_mem_1_r2_out), .in1({shifter_2_out[31:8], ex_mem_1_r2_out[7:0]}), .out(MDin),
    .sel(ex_mem_1_sb_out));
  or or_19 (or_19_out, MEM_CHANGE, WB_CHANGE);
  not not_7 (not_7_out, or_19_out);
  and and_17 (READY_CHANGE, not_7_out, INTERUPT_STATE);
  RAM #(.addrWidth(10), .dataWidth(32), .bus("separate"), .Select("high")) ram_1 (
    .addr(MEM_ALU[11:2]), .din(MDin), .data(ram_1_data), .str(MemWrite), .clk(CLK), .clr(RST));  // open: sel, ld
  or or_20 (or_20_out, RST, CHANGE);
  MEM_WB mem_wb_1 (
    .MemToReg_in(ex_mem_1_memtoreg_out), .IR_in(MEM_IR), .RegWrite_in(MEM_Regwrite), .PC_in(ex_mem_1_pc_out),
    .JAL_in(ex_mem_1_jal_out), .MemD_in(ram_1_data), .RegDst_in(ex_mem_1_regdst_out), .AluR_in(MEM_ALU),
    .Halt_in(ex_mem_1_halt_out), .W__in(MEM_W_num), .CLK(CLK), .MemToReg_out(mem_wb_1_memtoreg_out),
    .IR_out(WB_IR), .RegWrite_out(RegWrite), .PC_out_2(mem_wb_1_pc_out_2), .JAL_out(mem_wb_1_jal_out),
    .MemD_out(mem_wb_1_memd_out), .RegDst_out(mem_wb_1_regdst_out), .AluR_out(mem_wb_1_alur_out),
    .Halt_out(mem_wb_1_halt_out), .W__out(WB_W_num), .RST(or_20_out), .Enable(halt), .PCb_in(M_PC),
    .PC_out(WB_PC), .CHANGE_MEM_OR_RAM_in(MEM_CHANGE), .CHANGE_MEM_OR_RAM_out(WB_CHANGE));
  not not_8 (not_8_out, mem_wb_1_halt_out);
  Multiplexer #(.select(1), .width(32), .disabled("Z"), .enable("false")) multiplexer_20 (
    .in0(mem_wb_1_alur_out), .in1(mem_wb_1_memd_out), .out(WB_TOREG), .sel(mem_wb_1_memtoreg_out));
  Multiplexer #(.select(1), .width(5), .disabled("Z"), .enable("false")) multiplexer_21 (
    .in0(WB_IR[20:16]), .in1(WB_IR[15:11]), .out(multiplexer_21_out), .sel(mem_wb_1_regdst_out));
  or or_21 (halt, not_8_out, Go);
  Multiplexer #(.select(1), .width(32), .disabled("Z"), .enable("false")) multiplexer_22 (
    .in0(WB_TOREG), .in1(mem_wb_1_pc_out_2), .out(RDin), .sel(mem_wb_1_jal_out));
  Multiplexer #(.select(1), .width(5), .disabled("Z"), .enable("false")) multiplexer_23 (
    .in0(multiplexer_21_out), .in1({5{1'b1}}), .out(W_num), .sel(mem_wb_1_jal_out));

  // Other names for the same wires on the sheet: ID_IR[5:0] = ID_FUNC; EX_IR[5:0] = EX_FUNC;
  //   EX_rt[4:0] = EX_IR[20:16]; EX_rs[4:0] = EX_IR[25:21]; EX_OP[5:0] = EX_IR[31:26]; ID_OP[5:0] = ID_IR[31:26];
  //   IR[31:0] = IF_IR; MEM_PC[31:0] = M_PC; PC[31:0] = IF_PC; RW = RegWrite; WB_Regwrite = RegWrite

  // Notes on the sheet:
  //   中断源
  //   时空图监测，可删除
  //   中断等待指示
  //   PC+4
  //   PC+imm
  //   PC-J
  //   PC-JR
  //   单级中断测试信号模拟器
  //   数码管输出
  //   指令存储器
  //   contents of rom_1 (hex, n*v repeats v):
  //   8e160000 2d09825 109fc0 139fc3 8021 2012000c 24160008 26100001 3210000f 20080008 20090001 139900
  //   2709825 132020 20020022 c 1094022 1500fff9 22100001 2018000f 2188024 108700 20080008 20090001 139902
  //   2709825 132021 20020022 c 1094022 1500fff9 108702 2c9b022 12c00001 8000c07 4020 1084027 84400
  //   3508ffff 82021 20020022 c 8000c00 afa20000 23bd0004 42000018 afa20000 23bd0004 afa40000 23bd0004
  //   afb00000 23bd0004 afb30000 23bd0004 afb40000 23bd0004 afb50000 23bd0004 afb60000 23bd0004 20160002
  //   20140003 20150001 168020 108100 2149825 132020 20020022 c 1600fffa 295a022 1680fff7 23bdfffc
  //   8fb60000 23bdfffc 8fb50000 23bdfffc 8fb40000 23bdfffc 8fb30000 23bdfffc 8fb00000 23bdfffc 8fa40000
  //   23bdfffc 8fa20000 42000018 afa20000 23bd0004 afa40000 23bd0004 afb00000 23bd0004 afb30000 23bd0004
  //   afb40000 23bd0004 afb50000 23bd0004 afb60000 23bd0004 20160003 20140003 20150001 168020 108100
  //   2149825 132020 20020022 c 1600fffa 295a022 1680fff7 23bdfffc 8fb60000 23bdfffc 8fb50000 23bdfffc
  //   8fb40000 23bdfffc 8fb30000 23bdfffc 8fb00000 23bdfffc 8fa40000 23bdfffc 8fa20000 42000018
  //   JR
  //   JMP
  //   JMP+IF
  //   流水调试日志用
  //   IR
  //   Reset 
  //   Reset 
  //   Reset 
  //   OP
  //   Func
  //   rs
  //   rt
  //   rd
  //   addr
  //   imm
  //   shamt
  //   JMP
  //   JR
  //   SignedEXT
  //   BGEZ
  //   SB
  //   OP
  //   Func
  //   Beq
  //   Bne
  //   MemToReg
  //   MemWrite
  //   AluOP
  //   AluSrcB
  //   RegWrite
  //   JAL
  //   RegDst
  //   Syscall
  //   IR
  //   IE
  //   为方便自动评测，需要输出流水线各段保存的PC值，注意是PC不是PC+4，另外ID段寄存器写入信息，Mem段内存写入信息也要输出
  //   JMP+IF
  //   控制位
  //   暂停节拍，不能为0
  //   戳工具置1进入计数暂停模式，ctrl+k时钟自动运行到对应节拍暂停
  //   ctrl+k关闭时钟连续运行，将控制位置零，进入单步调试模式调试
  //   可计数暂停的时钟源
  //   rt
  //   rd
  //   W#
endmodule

module \封装正确性测试  (
);

  wire IR1, IR2, IR3, MemW, RegW;
  wire [31:0] EX_PC, ID_PC, IF_PC, IR, LED, MDin, MDinr, MEM_PC, PC, RDin, RDinr, WB_PC;

  \单周期MIPS  \u_单周期mips_1  (
    .RegWrite(RegW), .MemWrite(MemW), .PC(PC), .IR(IR), .RDin(RDin), .MDin(MDin), .LedData(LED));  // open: IR1, IR2, IR3
  \气泡流水线  \u_气泡流水线_1  (
    .RegWrite(RegW), .MemWrite(MemW), .IF_PC(IF_PC), .ID_PC(ID_PC), .EX_PC(EX_PC), .M_PC(MEM_PC),
    .WB_PC(WB_PC), .RDin(RDinr), .MDin(MDinr), .LedData(LED));
  \单周期MIPS_单级中断  \u_单周期mips_单级中断_1  (
    .IR1(IR1), .IR2(IR2), .IR3(IR3), .RegWrite(RegW), .MemWrite(MemW), .PC(PC), .IR(IR), .RDin(RDin),
    .MDin(MDin), .LedData(LED));
  \理想流水线  \u_理想流水线_1  (
    .RegWrite(RegW), .MemWrite(MemW), .IF_PC(IF_PC), .ID_PC(ID_PC), .EX_PC(EX_PC), .M_PC(MEM_PC),
    .WB_PC(WB_PC), .RDin(RDinr), .MDin(MDinr), .LedData(LED));
  \重定向流水线  \u_重定向流水线_1  (
    .RegWrite(RegW), .MemWrite(MemW), .IF_PC(IF_PC), .ID_PC(ID_PC), .EX_PC(EX_PC), .M_PC(MEM_PC),
    .WB_PC(WB_PC), .RDin(RDinr), .MDin(MDinr), .LedData(LED));
  \单周期MIPS_多级中断  \u_单周期mips_多级中断_1  (
    .IR1(IR1), .IR2(IR2), .IR3(IR3), .RegWrite(RegW), .MemWrite(MemW), .PC(PC), .IR(IR), .RDin(RDin),
    .MDin(MDin), .LedData(LED));

  // Notes on the sheet:
  //   单周期封装测试
  //   气泡流水封装测试
  //   单周期+单级中断封装测试
  //   请检查上面封装有无位宽不匹配，引脚标签是否和连接的标签相对应，否则无法在educoder平台上正确测试
  //   理想流水封装测试
  //   重定向流水封装测试
  //   单周期+多级中断封装测试
endmodule

module IF_ID (
  input  [31:0] PCb_in,
  input  [31:0] PC_in,
  input  [31:0] IR_in,
  input  CLK,
  input  RST,
  input  Enable,
  output [31:0] PCb_out,
  output [31:0] PC_out,
  output [31:0] IR_out
);

  wire [31:0] multiplexer_1_out, multiplexer_2_out, multiplexer_3_out;

  Multiplexer #(.select(1), .width(32), .disabled("Z"), .enable("false")) multiplexer_1 (
    .in0(PCb_in), .in1({32{1'b0}}), .out(multiplexer_1_out), .sel(RST));
  Multiplexer #(.select(1), .width(32), .disabled("Z"), .enable("false")) multiplexer_2 (
    .in0(PC_in), .in1({32{1'b0}}), .out(multiplexer_2_out), .sel(RST));
  Multiplexer #(.select(1), .width(32), .disabled("Z"), .enable("false")) multiplexer_3 (
    .in0(IR_in), .in1({32{1'b0}}), .out(multiplexer_3_out), .sel(RST));
  Pull_Resistor #(.pull(0)) pull_resistor_1 (.node(RST));
  Pull_Resistor #(.pull(0)) pull_resistor_2 (.node(Enable));
  Register #(.width(32), .trigger("rising"), .Select("low")) register_1 (
    .D(multiplexer_1_out), .en(Enable), .Q(PCb_out), .clk(CLK));  // open: clr
  Register #(.width(32), .trigger("rising"), .Select("low")) register_2 (
    .D(multiplexer_2_out), .en(Enable), .Q(PC_out), .clk(CLK));  // open: clr
  Register #(.width(32), .trigger("rising"), .Select("low")) register_3 (
    .D(multiplexer_3_out), .en(Enable), .Q(IR_out), .clk(CLK));  // open: clr

  // Notes on the sheet:
  //   高电平有效
endmodule

module ID_EX (
  input  [31:0] PCb_in,
  input  [31:0] IR_in,
  input  SignedEXT_in,
  input  [31:0] PC_in,
  input  BEQ_in,
  input  [31:0] R1_in,
  input  BNE_in,
  input  MemToReg_in,
  input  [31:0] R2_in,
  input  MemWrite_in,
  input  [15:0] Imm_in,
  input  AluSrcB_in,
  input  [31:0] Address_in,
  input  RegWrite_in,
  input  [3:0] AluOP_in,
  input  JAL_in,
  input  [4:0] Shamt_in,
  input  RegDst_in,
  input  Halt_in,
  input  SYSCALL,
  input  SB_in,
  input  JMP_in,
  input  BGEZ_in,
  input  [4:0] W__in,
  input  JR_in,
  input  CHANGE_MEM_OR_RAM_in,
  input  CLK,
  input  RST,
  input  Enable,
  output [31:0] PCb_out,
  output [31:0] IR_out,
  output SignedEXT_out,
  output [31:0] PC_out,
  output BEQ_out,
  output [31:0] R1_out,
  output BNE_out,
  output MemToReg_out,
  output [31:0] R2_out,
  output MemWrite_out,
  output [15:0] Imm_out,
  output AluSrcB_out,
  output [31:0] Address_out,
  output RegWrite_out,
  output [3:0] AluOP_out,
  output JAL_out,
  output [4:0] Shamt_out,
  output RegDst_out,
  output Halt_out,
  output SYSCALL_2,
  output SB_out,
  output JMP_out,
  output BGEZ_out,
  output [4:0] W__out,
  output JR_out,
  output CHANGE_MEM_OR_RAM_out
);

  wire multiplexer_10_out, multiplexer_11_out, multiplexer_12_out, multiplexer_14_out, multiplexer_15_out,
       multiplexer_16_out, multiplexer_17_out, multiplexer_18_out, multiplexer_19_out, multiplexer_20_out,
       multiplexer_21_out, multiplexer_22_out, multiplexer_23_out, multiplexer_24_out, multiplexer_25_out,
       multiplexer_26_out;
  wire [3:0] multiplexer_8_out;
  wire [4:0] multiplexer_9_out, multiplexer_13_out;
  wire [15:0] multiplexer_6_out;
  wire [31:0] multiplexer_1_out, multiplexer_2_out, multiplexer_3_out, multiplexer_4_out, multiplexer_5_out,
       multiplexer_7_out;

  Multiplexer #(.select(1), .width(32), .disabled("Z"), .enable("false")) multiplexer_1 (
    .in0(PCb_in), .in1({32{1'b0}}), .out(multiplexer_1_out), .sel(RST));
  Multiplexer #(.select(1), .width(32), .disabled("Z"), .enable("false")) multiplexer_2 (
    .in0(IR_in), .in1({32{1'b0}}), .out(multiplexer_2_out), .sel(RST));
  Multiplexer #(.select(1), .width(32), .disabled("Z"), .enable("false")) multiplexer_3 (
    .in0(PC_in), .in1({32{1'b0}}), .out(multiplexer_3_out), .sel(RST));
  Multiplexer #(.select(1), .width(32), .disabled("Z"), .enable("false")) multiplexer_4 (
    .in0(R1_in), .in1({32{1'b0}}), .out(multiplexer_4_out), .sel(RST));
  Multiplexer #(.select(1), .width(32), .disabled("Z"), .enable("false")) multiplexer_5 (
    .in0(R2_in), .in1({32{1'b0}}), .out(multiplexer_5_out), .sel(RST));
  Multiplexer #(.select(1), .width(16), .disabled("Z"), .enable("false")) multiplexer_6 (
    .in0(Imm_in), .in1({16{1'b0}}), .out(multiplexer_6_out), .sel(RST));
  Multiplexer #(.select(1), .width(32), .disabled("Z"), .enable("false")) multiplexer_7 (
    .in0(Address_in), .in1({32{1'b0}}), .out(multiplexer_7_out), .sel(RST));
  Multiplexer #(.select(1), .width(4), .disabled("Z"), .enable("false")) multiplexer_8 (
    .in0(AluOP_in), .in1(4'b0000), .out(multiplexer_8_out), .sel(RST));
  Multiplexer #(.select(1), .width(5), .disabled("Z"), .enable("false")) multiplexer_9 (
    .in0(Shamt_in), .in1({5{1'b0}}), .out(multiplexer_9_out), .sel(RST));
  Multiplexer #(.select(1), .width(1), .disabled("Z"), .enable("false")) multiplexer_10 (
    .in0(Halt_in), .in1(1'b0), .out(multiplexer_10_out), .sel(RST));
  Multiplexer #(.select(1), .width(1), .disabled("Z"), .enable("false")) multiplexer_11 (
    .in0(SB_in), .in1(1'b0), .out(multiplexer_11_out), .sel(RST));
  Multiplexer #(.select(1), .width(1), .disabled("Z"), .enable("false")) multiplexer_12 (
    .in0(BGEZ_in), .in1(1'b0), .out(multiplexer_12_out), .sel(RST));
  Multiplexer #(.select(1), .width(5), .disabled("Z"), .enable("false")) multiplexer_13 (
    .in0(W__in), .in1({5{1'b0}}), .out(multiplexer_13_out), .sel(RST));
  Pull_Resistor #(.pull(0)) pull_resistor_1 (.node(RST));
  Pull_Resistor #(.pull(0)) pull_resistor_2 (.node(Enable));
  Register #(.width(32), .trigger("rising"), .Select("low")) register_1 (
    .D(multiplexer_1_out), .en(Enable), .Q(PCb_out), .clk(CLK));  // open: clr
  Register #(.width(32), .trigger("rising"), .Select("low")) register_2 (
    .D(multiplexer_2_out), .en(Enable), .Q(IR_out), .clk(CLK));  // open: clr
  Register #(.width(32), .trigger("rising"), .Select("low")) register_3 (
    .D(multiplexer_3_out), .en(Enable), .Q(PC_out), .clk(CLK));  // open: clr
  Register #(.width(32), .trigger("rising"), .Select("low")) register_4 (
    .D(multiplexer_4_out), .en(Enable), .Q(R1_out), .clk(CLK));  // open: clr
  Register #(.width(32), .trigger("rising"), .Select("low")) register_5 (
    .D(multiplexer_5_out), .en(Enable), .Q(R2_out), .clk(CLK));  // open: clr
  Register #(.width(16), .trigger("rising"), .Select("low")) register_6 (
    .D(multiplexer_6_out), .en(Enable), .Q(Imm_out), .clk(CLK));  // open: clr
  Register #(.width(32), .trigger("rising"), .Select("low")) register_7 (
    .D(multiplexer_7_out), .en(Enable), .Q(Address_out), .clk(CLK));  // open: clr
  Register #(.width(4), .trigger("rising"), .Select("low")) register_8 (
    .D(multiplexer_8_out), .en(Enable), .Q(AluOP_out), .clk(CLK));  // open: clr
  Register #(.width(5), .trigger("rising"), .Select("low")) register_9 (
    .D(multiplexer_9_out), .en(Enable), .Q(Shamt_out), .clk(CLK));  // open: clr
  Register #(.width(1), .trigger("rising"), .Select("low")) register_10 (
    .D(multiplexer_10_out), .en(Enable), .Q(Halt_out), .clk(CLK));  // open: clr
  Register #(.width(1), .trigger("rising"), .Select("low")) register_11 (
    .D(multiplexer_11_out), .en(Enable), .Q(SB_out), .clk(CLK));  // open: clr
  Register #(.width(1), .trigger("rising"), .Select("low")) register_12 (
    .D(multiplexer_12_out), .en(Enable), .Q(BGEZ_out), .clk(CLK));  // open: clr
  Register #(.width(5), .trigger("rising"), .Select("low")) register_13 (
    .D(multiplexer_13_out), .en(Enable), .Q(W__out), .clk(CLK));  // open: clr
  Multiplexer #(.select(1), .width(1), .disabled("Z"), .enable("false")) multiplexer_14 (
    .in0(SignedEXT_in), .in1(1'b0), .out(multiplexer_14_out), .sel(RST));
  Multiplexer #(.select(1), .width(1), .disabled("Z"), .enable("false")) multiplexer_15 (
    .in0(BEQ_in), .in1(1'b0), .out(multiplexer_15_out), .sel(RST));
  Multiplexer #(.select(1), .width(1), .disabled("Z"), .enable("false")) multiplexer_16 (
    .in0(BNE_in), .in1(1'b0), .out(multiplexer_16_out), .sel(RST));
  Multiplexer #(.select(1), .width(1), .disabled("Z"), .enable("false")) multiplexer_17 (
    .in0(MemToReg_in), .in1(1'b0), .out(multiplexer_17_out), .sel(RST));
  Multiplexer #(.select(1), .width(1), .disabled("Z"), .enable("false")) multiplexer_18 (
    .in0(MemWrite_in), .in1(1'b0), .out(multiplexer_18_out), .sel(RST));
  Multiplexer #(.select(1), .width(1), .disabled("Z"), .enable("false")) multiplexer_19 (
    .in0(AluSrcB_in), .in1(1'b0), .out(multiplexer_19_out), .sel(RST));
  Multiplexer #(.select(1), .width(1), .disabled("Z"), .enable("false")) multiplexer_20 (
    .in0(RegWrite_in), .in1(1'b0), .out(multiplexer_20_out), .sel(RST));
  Multiplexer #(.select(1), .width(1), .disabled("Z"), .enable("false")) multiplexer_21 (
    .in0(JAL_in), .in1(1'b0), .out(multiplexer_21_out), .sel(RST));
  Multiplexer #(.select(1), .width(1), .disabled("Z"), .enable("false")) multiplexer_22 (
    .in0(RegDst_in), .in1(1'b0), .out(multiplexer_22_out), .sel(RST));
  Multiplexer #(.select(1), .width(1), .disabled("Z"), .enable("false")) multiplexer_23 (
    .in0(SYSCALL), .in1(1'b0), .out(multiplexer_23_out), .sel(RST));
  Multiplexer #(.select(1), .width(1), .disabled("Z"), .enable("false")) multiplexer_24 (
    .in0(JMP_in), .in1(1'b0), .out(multiplexer_24_out), .sel(RST));
  Multiplexer #(.select(1), .width(1), .disabled("Z"), .enable("false")) multiplexer_25 (
    .in0(JR_in), .in1(1'b0), .out(multiplexer_25_out), .sel(RST));
  Multiplexer #(.select(1), .width(1), .disabled("Z"), .enable("false")) multiplexer_26 (
    .in0(CHANGE_MEM_OR_RAM_in), .in1(1'b0), .out(multiplexer_26_out), .sel(RST));
  Register #(.width(1), .trigger("rising"), .Select("low")) register_14 (
    .D(multiplexer_14_out), .en(Enable), .Q(SignedEXT_out), .clk(CLK));  // open: clr
  Register #(.width(1), .trigger("rising"), .Select("low")) register_15 (
    .D(multiplexer_15_out), .en(Enable), .Q(BEQ_out), .clk(CLK));  // open: clr
  Register #(.width(1), .trigger("rising"), .Select("low")) register_16 (
    .D(multiplexer_16_out), .en(Enable), .Q(BNE_out), .clk(CLK));  // open: clr
  Register #(.width(1), .trigger("rising"), .Select("low")) register_17 (
    .D(multiplexer_17_out), .en(Enable), .Q(MemToReg_out), .clk(CLK));  // open: clr
  Register #(.width(1), .trigger("rising"), .Select("low")) register_18 (
    .D(multiplexer_18_out), .en(Enable), .Q(MemWrite_out), .clk(CLK));  // open: clr
  Register #(.width(1), .trigger("rising"), .Select("low")) register_19 (
    .D(multiplexer_19_out), .en(Enable), .Q(AluSrcB_out), .clk(CLK));  // open: clr
  Register #(.width(1), .trigger("rising"), .Select("low")) register_20 (
    .D(multiplexer_20_out), .en(Enable), .Q(RegWrite_out), .clk(CLK));  // open: clr
  Register #(.width(1), .trigger("rising"), .Select("low")) register_21 (
    .D(multiplexer_21_out), .en(Enable), .Q(JAL_out), .clk(CLK));  // open: clr
  Register #(.width(1), .trigger("rising"), .Select("low")) register_22 (
    .D(multiplexer_22_out), .en(Enable), .Q(RegDst_out), .clk(CLK));  // open: clr
  Register #(.width(1), .trigger("rising"), .Select("low")) register_23 (
    .D(multiplexer_23_out), .en(Enable), .Q(SYSCALL_2), .clk(CLK));  // open: clr
  Register #(.width(1), .trigger("rising"), .Select("low")) register_24 (
    .D(multiplexer_24_out), .en(Enable), .Q(JMP_out), .clk(CLK));  // open: clr
  Register #(.width(1), .trigger("rising"), .Select("low")) register_25 (
    .D(multiplexer_25_out), .en(Enable), .Q(JR_out), .clk(CLK));  // open: clr
  Register #(.width(1), .trigger("rising"), .Select("low")) register_26 (
    .D(multiplexer_26_out), .en(Enable), .Q(CHANGE_MEM_OR_RAM_out), .clk(CLK));  // open: clr
endmodule

module EX_MEM (
  input  [31:0] PCb_in,
  input  MemToReg_in,
  input  [31:0] IR_in,
  input  MemWrite_in,
  input  [31:0] PC_in,
  input  RegWrite_in,
  input  [31:0] R2_in,
  input  JAL_in,
  input  [31:0] AluR_in,
  input  RegDst_in,
  input  Halt_in,
  input  CHANGE_MEM_OR_RAM_in,
  input  SB_in,
  input  [4:0] W__in,
  input  CLK,
  input  RST,
  input  Enable,
  output [31:0] PCb_out,
  output MemToReg_out,
  output [31:0] IR_out,
  output MemWrite_out,
  output [31:0] PC_out,
  output RegWrite_out,
  output [31:0] R2_out,
  output JAL_out,
  output [31:0] AluR_out,
  output RegDst_out,
  output Halt_out,
  output CHANGE_MEM_OR_RAM_out,
  output SB_out,
  output [4:0] W__out
);

  wire multiplexer_6_out, multiplexer_7_out, multiplexer_9_out, multiplexer_10_out, multiplexer_11_out,
       multiplexer_12_out, multiplexer_13_out, multiplexer_14_out;
  wire [4:0] multiplexer_8_out;
  wire [31:0] multiplexer_1_out, multiplexer_2_out, multiplexer_3_out, multiplexer_4_out, multiplexer_5_out;

  Multiplexer #(.select(1), .width(32), .disabled("Z"), .enable("false")) multiplexer_1 (
    .in0(PCb_in), .in1({32{1'b0}}), .out(multiplexer_1_out), .sel(RST));
  Multiplexer #(.select(1), .width(32), .disabled("Z"), .enable("false")) multiplexer_2 (
    .in0(IR_in), .in1({32{1'b0}}), .out(multiplexer_2_out), .sel(RST));
  Multiplexer #(.select(1), .width(32), .disabled("Z"), .enable("false")) multiplexer_3 (
    .in0(PC_in), .in1({32{1'b0}}), .out(multiplexer_3_out), .sel(RST));
  Multiplexer #(.select(1), .width(32), .disabled("Z"), .enable("false")) multiplexer_4 (
    .in0(R2_in), .in1({32{1'b0}}), .out(multiplexer_4_out), .sel(RST));
  Multiplexer #(.select(1), .width(32), .disabled("Z"), .enable("false")) multiplexer_5 (
    .in0(AluR_in), .in1({32{1'b0}}), .out(multiplexer_5_out), .sel(RST));
  Multiplexer #(.select(1), .width(1), .disabled("Z"), .enable("false")) multiplexer_6 (
    .in0(Halt_in), .in1(1'b0), .out(multiplexer_6_out), .sel(RST));
  Multiplexer #(.select(1), .width(1), .disabled("Z"), .enable("false")) multiplexer_7 (
    .in0(SB_in), .in1(1'b0), .out(multiplexer_7_out), .sel(RST));
  Multiplexer #(.select(1), .width(5), .disabled("Z"), .enable("false")) multiplexer_8 (
    .in0(W__in), .in1({5{1'b0}}), .out(multiplexer_8_out), .sel(RST));
  Pull_Resistor #(.pull(0)) pull_resistor_1 (.node(RST));
  Pull_Resistor #(.pull(0)) pull_resistor_2 (.node(Enable));
  Register #(.width(32), .trigger("rising"), .Select("low")) register_1 (
    .D(multiplexer_1_out), .en(Enable), .Q(PCb_out), .clk(CLK));  // open: clr
  Register #(.width(32), .trigger("rising"), .Select("low")) register_2 (
    .D(multiplexer_2_out), .en(Enable), .Q(IR_out), .clk(CLK));  // open: clr
  Register #(.width(32), .trigger("rising"), .Select("low")) register_3 (
    .D(multiplexer_3_out), .en(Enable), .Q(PC_out), .clk(CLK));  // open: clr
  Register #(.width(32), .trigger("rising"), .Select("low")) register_4 (
    .D(multiplexer_4_out), .en(Enable), .Q(R2_out), .clk(CLK));  // open: clr
  Register #(.width(32), .trigger("rising"), .Select("low")) register_5 (
    .D(multiplexer_5_out), .en(Enable), .Q(AluR_out), .clk(CLK));  // open: clr
  Register #(.width(1), .trigger("rising"), .Select("low")) register_6 (
    .D(multiplexer_6_out), .en(Enable), .Q(Halt_out), .clk(CLK));  // open: clr
  Register #(.width(1), .trigger("rising"), .Select("low")) register_7 (
    .D(multiplexer_7_out), .en(Enable), .Q(SB_out), .clk(CLK));  // open: clr
  Register #(.width(5), .trigger("rising"), .Select("low")) register_8 (
    .D(multiplexer_8_out), .en(Enable), .Q(W__out), .clk(CLK));  // open: clr
  Multiplexer #(.select(1), .width(1), .disabled("Z"), .enable("false")) multiplexer_9 (
    .in0(MemToReg_in), .in1(1'b0), .out(multiplexer_9_out), .sel(RST));
  Multiplexer #(.select(1), .width(1), .disabled("Z"), .enable("false")) multiplexer_10 (
    .in0(MemWrite_in), .in1(1'b0), .out(multiplexer_10_out), .sel(RST));
  Multiplexer #(.select(1), .width(1), .disabled("Z"), .enable("false")) multiplexer_11 (
    .in0(RegWrite_in), .in1(1'b0), .out(multiplexer_11_out), .sel(RST));
  Multiplexer #(.select(1), .width(1), .disabled("Z"), .enable("false")) multiplexer_12 (
    .in0(JAL_in), .in1(1'b0), .out(multiplexer_12_out), .sel(RST));
  Multiplexer #(.select(1), .width(1), .disabled("Z"), .enable("false")) multiplexer_13 (
    .in0(RegDst_in), .in1(1'b0), .out(multiplexer_13_out), .sel(RST));
  Multiplexer #(.select(1), .width(1), .disabled("Z"), .enable("false")) multiplexer_14 (
    .in0(CHANGE_MEM_OR_RAM_in), .in1(1'b0), .out(multiplexer_14_out), .sel(RST));
  Register #(.width(1), .trigger("rising"), .Select("low")) register_9 (
    .D(multiplexer_9_out), .en(Enable), .Q(MemToReg_out), .clk(CLK));  // open: clr
  Register #(.width(1), .trigger("rising"), .Select("low")) register_10 (
    .D(multiplexer_10_out), .en(Enable), .Q(MemWrite_out), .clk(CLK));  // open: clr
  Register #(.width(1), .trigger("rising"), .Select("low")) register_11 (
    .D(multiplexer_11_out), .en(Enable), .Q(RegWrite_out), .clk(CLK));  // open: clr
  Register #(.width(1), .trigger("rising"), .Select("low")) register_12 (
    .D(multiplexer_12_out), .en(Enable), .Q(JAL_out), .clk(CLK));  // open: clr
  Register #(.width(1), .trigger("rising"), .Select("low")) register_13 (
    .D(multiplexer_13_out), .en(Enable), .Q(RegDst_out), .clk(CLK));  // open: clr
  Register #(.width(1), .trigger("rising"), .Select("low")) register_14 (
    .D(multiplexer_14_out), .en(Enable), .Q(CHANGE_MEM_OR_RAM_out), .clk(CLK));  // open: clr
endmodule

module MEM_WB (
  input  [31:0] PCb_in,
  input  MemToReg_in,
  input  [31:0] IR_in,
  input  RegWrite_in,
  input  [31:0] PC_in,
  input  JAL_in,
  input  [31:0] MemD_in,
  input  RegDst_in,
  input  [31:0] AluR_in,
  input  CHANGE_MEM_OR_RAM_in,
  input  Halt_in,
  input  [4:0] W__in,
  input  CLK,
  input  RST,
  input  Enable,
  output [31:0] PC_out,
  output MemToReg_out,
  output [31:0] IR_out,
  output RegWrite_out,
  output [31:0] PC_out_2,
  output JAL_out,
  output [31:0] MemD_out,
  output RegDst_out,
  output [31:0] AluR_out,
  output CHANGE_MEM_OR_RAM_out,
  output Halt_out,
  output [4:0] W__out
);

  wire multiplexer_6_out, multiplexer_8_out, multiplexer_9_out, multiplexer_10_out, multiplexer_11_out,
       multiplexer_12_out;
  wire [4:0] multiplexer_7_out;
  wire [31:0] multiplexer_1_out, multiplexer_2_out, multiplexer_3_out, multiplexer_4_out, multiplexer_5_out;

  Multiplexer #(.select(1), .width(32), .disabled("Z"), .enable("false")) multiplexer_1 (
    .in0(PCb_in), .in1({32{1'b0}}), .out(multiplexer_1_out), .sel(RST));
  Multiplexer #(.select(1), .width(32), .disabled("Z"), .enable("false")) multiplexer_2 (
    .in0(IR_in), .in1({32{1'b0}}), .out(multiplexer_2_out), .sel(RST));
  Multiplexer #(.select(1), .width(32), .disabled("Z"), .enable("false")) multiplexer_3 (
    .in0(PC_in), .in1({32{1'b0}}), .out(multiplexer_3_out), .sel(RST));
  Multiplexer #(.select(1), .width(32), .disabled("Z"), .enable("false")) multiplexer_4 (
    .in0(MemD_in), .in1({32{1'b0}}), .out(multiplexer_4_out), .sel(RST));
  Multiplexer #(.select(1), .width(32), .disabled("Z"), .enable("false")) multiplexer_5 (
    .in0(AluR_in), .in1({32{1'b0}}), .out(multiplexer_5_out), .sel(RST));
  Multiplexer #(.select(1), .width(1), .disabled("Z"), .enable("false")) multiplexer_6 (
    .in0(Halt_in), .in1(1'b0), .out(multiplexer_6_out), .sel(RST));
  Multiplexer #(.select(1), .width(5), .disabled("Z"), .enable("false")) multiplexer_7 (
    .in0(W__in), .in1({5{1'b0}}), .out(multiplexer_7_out), .sel(RST));
  Pull_Resistor #(.pull(0)) pull_resistor_1 (.node(RST));
  Pull_Resistor #(.pull(0)) pull_resistor_2 (.node(Enable));
  Register #(.width(32), .trigger("rising"), .Select("low")) register_1 (
    .D(multiplexer_1_out), .en(Enable), .Q(PC_out), .clk(CLK));  // open: clr
  Register #(.width(32), .trigger("rising"), .Select("low")) register_2 (
    .D(multiplexer_2_out), .en(Enable), .Q(IR_out), .clk(CLK));  // open: clr
  Register #(.width(32), .trigger("rising"), .Select("low")) register_3 (
    .D(multiplexer_3_out), .en(Enable), .Q(PC_out_2), .clk(CLK));  // open: clr
  Register #(.width(32), .trigger("rising"), .Select("low")) register_4 (
    .D(multiplexer_4_out), .en(Enable), .Q(MemD_out), .clk(CLK));  // open: clr
  Register #(.width(32), .trigger("rising"), .Select("low")) register_5 (
    .D(multiplexer_5_out), .en(Enable), .Q(AluR_out), .clk(CLK));  // open: clr
  Register #(.width(1), .trigger("rising"), .Select("low")) register_6 (
    .D(multiplexer_6_out), .en(Enable), .Q(Halt_out), .clk(CLK));  // open: clr
  Register #(.width(5), .trigger("rising"), .Select("low")) register_7 (
    .D(multiplexer_7_out), .en(Enable), .Q(W__out), .clk(CLK));  // open: clr
  Multiplexer #(.select(1), .width(1), .disabled("Z"), .enable("false")) multiplexer_8 (
    .in0(MemToReg_in), .in1(1'b0), .out(multiplexer_8_out), .sel(RST));
  Multiplexer #(.select(1), .width(1), .disabled("Z"), .enable("false")) multiplexer_9 (
    .in0(RegWrite_in), .in1(1'b0), .out(multiplexer_9_out), .sel(RST));
  Multiplexer #(.select(1), .width(1), .disabled("Z"), .enable("false")) multiplexer_10 (
    .in0(JAL_in), .in1(1'b0), .out(multiplexer_10_out), .sel(RST));
  Multiplexer #(.select(1), .width(1), .disabled("Z"), .enable("false")) multiplexer_11 (
    .in0(RegDst_in), .in1(1'b0), .out(multiplexer_11_out), .sel(RST));
  Multiplexer #(.select(1), .width(1), .disabled("Z"), .enable("false")) multiplexer_12 (
    .in0(CHANGE_MEM_OR_RAM_in), .in1(1'b0), .out(multiplexer_12_out), .sel(RST));
  Register #(.width(1), .trigger("rising"), .Select("low")) register_8 (
    .D(multiplexer_8_out), .en(Enable), .Q(MemToReg_out), .clk(CLK));  // open: clr
  Register #(.width(1), .trigger("rising"), .Select("low")) register_9 (
    .D(multiplexer_9_out), .en(Enable), .Q(RegWrite_out), .clk(CLK));  // open: clr
  Register #(.width(1), .trigger("rising"), .Select("low")) register_10 (
    .D(multiplexer_10_out), .en(Enable), .Q(JAL_out), .clk(CLK));  // open: clr
  Register #(.width(1), .trigger("rising"), .Select("low")) register_11 (
    .D(multiplexer_11_out), .en(Enable), .Q(RegDst_out), .clk(CLK));  // open: clr
  Register #(.width(1), .trigger("rising"), .Select("low")) register_12 (
    .D(multiplexer_12_out), .en(Enable), .Q(CHANGE_MEM_OR_RAM_out), .clk(CLK));  // open: clr
endmodule
